// Logisim project project.circ as structural Verilog
module main (
  input  clk,
  input  initgame,
  input  [6:0] moving,
  output [31:0] out_4,
  output [31:0] out_5,
  output [31:0] out_6,
  output [31:0] out_7,
  output [31:0] out_8,
  output [31:0] out_9,
  output [31:0] out_10,
  output [31:0] out_11,
  output [31:0] out_12,
  output [31:0] out_13,
  output [31:0] out_14,
  output [31:0] out_15,
  output [31:0] out_16,
  output [31:0] out_17,
  output [31:0] out_18,
  output [31:0] out_19,
  output [31:0] out_20,
  output [31:0] out_21,
  output [31:0] out_22,
  output [31:0] out_23,
  output [31:0] out_24,
  output [31:0] out_25,
  output gameover,
  output [31:0] out_27,
  output win,
  output [31:0] out_29,
  output [31:0] out_30,
  output [31:0] out_31,
  output [31:0] out_32,
  output [31:0] out_33,
  output [31:0] out_34,
  output [31:0] out_35,
  output [31:0] out_36,
  output [31:0] out_37
);

  wire comparator_1_eq, comparator_2_eq, comparator_3_eq, enemies_1_boom;
  wire [4:0] player_move_1_counter, \стрельба_1_номер ;
  wire [31:0] _9_prime, _10_prime, _11_prime, _12_prime, _13_prime, _14_prime, _15_prime, _16_prime,
       _17_prime, _18_prime, _19_prime, _20_prime, _21_prime, _22_prime, _23_prime, _24_prime, _25_prime,
       _26_prime, _27_prime, _28_prime, _29_prime, _30_prime, _31_prime, _32_prime, pull_resistor_1_node,
       wall, \стрельба_1__3 , \стрельба_1__31 , \стрельба_1_out_12 , \стрельба_1_out_13 ,
       \стрельба_1_out_14 , \стрельба_1_out_15 , \стрельба_1_out_16 , \стрельба_1_out_17 ,
       \стрельба_1_out_18 , \стрельба_1_out_19 , \стрельба_1_out_20 , \стрельба_1_out_21 ,
       \стрельба_1_out_22 , \стрельба_1_out_23 , \стрельба_1_out_24 , \стрельба_1_out_25 ,
       \стрельба_1_out_26 , \стрельба_1_out_27 , \стрельба_1_out_28 , \стрельба_1_out_29 ,
       \стрельба_1_out_30 , \стрельба_1_out_31 , \стрельба_1_out_32 , \стрельба_1_out_33 ,
       \стрельба_1_out_34 ;

  oradd32 oradd32_1 (.in(_9_prime), .out(gameover));
  \стенки  \u_стенки_1  (.initwalls(initgame), .bullets(pull_resistor_1_node), .walls(wall), .clock(clk));
  Pull_Resistor pull_resistor_1 (.node(pull_resistor_1_node));
  // Probe on moving
  Player_Move player_move_1 (
    .counter(player_move_1_counter), .in_1(comparator_1_eq), .in_2(comparator_2_eq), ._0(out_4), ._1(out_5));
  Comparator #(.width(7), .mode("unsigned")) comparator_1 (
    .a(moving), .b(7'b1100001), .eq(comparator_1_eq));  // open: gt, lt
  Comparator #(.width(7), .mode("unsigned")) comparator_2 (
    .a(moving), .b(7'b1100100), .eq(comparator_2_eq));  // open: gt, lt
  Comparator #(.width(7), .mode("unsigned")) comparator_3 (
    .a(moving), .b(7'b0100000), .eq(comparator_3_eq));  // open: gt, lt
  \стрельба  \u_стрельба_1  (
    ._2(out_6), ._3(\стрельба_1__3 ), .out_7(out_8), .coord(player_move_1_counter), .out_8(out_9),
    .out_9(out_10), .out_10(out_11), .fire(comparator_3_eq), .out_12(\стрельба_1_out_12 ),
    .out_13(\стрельба_1_out_13 ), .out_14(\стрельба_1_out_14 ), .out_15(\стрельба_1_out_15 ),
    .out_16(\стрельба_1_out_16 ), .out_17(\стрельба_1_out_17 ), .out_18(\стрельба_1_out_18 ),
    .out_19(\стрельба_1_out_19 ), .out_20(\стрельба_1_out_20 ), .out_21(\стрельба_1_out_21 ),
    .out_22(\стрельба_1_out_22 ), .out_23(\стрельба_1_out_23 ), .out_24(\стрельба_1_out_24 ),
    .out_25(\стрельба_1_out_25 ), .out_26(\стрельба_1_out_26 ), .out_27(\стрельба_1_out_27 ),
    .out_28(\стрельба_1_out_28 ), .out_29(\стрельба_1_out_29 ), .out_30(\стрельба_1_out_30 ),
    .out_31(\стрельба_1_out_31 ), .out_32(\стрельба_1_out_32 ), .out_33(\стрельба_1_out_33 ),
    .out_34(\стрельба_1_out_34 ), ._31(\стрельба_1__31 ), .clk(clk), .\Номер (\стрельба_1_номер ),
    .reset(enemies_1_boom));
  Pull_Resistor pull_resistor_2 (.node(\стрельба_1_out_32 ));
  enemies enemies_1 (
    .in_2(\стрельба_1_out_23 ), .in_3(\стрельба_1__31 ), .in_4(\стрельба_1_out_22 ),
    .in_5(\стрельба_1_out_34 ), .initgame(initgame), .in_7(\стрельба_1_out_21 ), .in_8(\стрельба_1_out_33 ),
    .in_9(\стрельба_1_out_20 ), .in_10(\стрельба_1_out_32 ), .in_11(\стрельба_1_out_19 ),
    .in_12(\стрельба_1_out_31 ), .in_13(\стрельба_1_out_18 ), .in_14(\стрельба_1_out_30 ),
    .in_15(\стрельба_1_out_17 ), .in_16(\стрельба_1_out_29 ), .Num(\стрельба_1_номер ),
    .in_18(\стрельба_1_out_16 ), .in_19(\стрельба_1_out_28 ), .in_20(\стрельба_1_out_15 ),
    .in_21(\стрельба_1_out_27 ), .in_22(\стрельба_1_out_14 ), .in_23(\стрельба_1_out_26 ),
    .in_24(\стрельба_1_out_13 ), .in_25(\стрельба_1_out_25 ), .in_26(\стрельба_1_out_12 ), .in_27(out_11),
    .in_28(\стрельба_1_out_24 ), .out_29(_20_prime), .out_30(_32_prime), .out_31(_19_prime),
    .out_32(_31_prime), .out_33(_18_prime), .out_34(_30_prime), .out_35(_17_prime), .out_36(_29_prime),
    .out_37(_16_prime), .out_38(_28_prime), .out_39(_15_prime), .out_40(_27_prime), .out_41(_14_prime),
    .out_42(_26_prime), .out_43(_13_prime), .out_44(_25_prime), .out_45(_12_prime), .out_46(_24_prime),
    .out_47(_11_prime), .out_48(_23_prime), .out_49(_10_prime), .out_50(_22_prime), .out_51(_9_prime),
    .out_52(_21_prime), .boom(enemies_1_boom), .clk(clk), .win(win));  // open: out
  assign out_37 = _32_prime | \стрельба_1__31 ;  // OR_Gate or_1, 32 bits wide
  assign out_36 = _31_prime | \стрельба_1_out_34 ;  // OR_Gate or_2, 32 bits wide
  assign out_35 = _30_prime | \стрельба_1_out_33 ;  // OR_Gate or_3, 32 bits wide
  assign out_34 = _29_prime | \стрельба_1_out_32 ;  // OR_Gate or_4, 32 bits wide
  assign out_33 = _28_prime | \стрельба_1_out_31 ;  // OR_Gate or_5, 32 bits wide
  assign out_32 = _27_prime | \стрельба_1_out_30 ;  // OR_Gate or_6, 32 bits wide
  assign out_31 = _26_prime | \стрельба_1_out_29 ;  // OR_Gate or_7, 32 bits wide
  assign out_30 = _25_prime | \стрельба_1_out_28 ;  // OR_Gate or_8, 32 bits wide
  assign out_29 = _24_prime | \стрельба_1_out_27 ;  // OR_Gate or_9, 32 bits wide
  assign out_27 = _23_prime | \стрельба_1_out_26 ;  // OR_Gate or_10, 32 bits wide
  assign out_25 = _22_prime | \стрельба_1_out_25 ;  // OR_Gate or_11, 32 bits wide
  assign out_24 = _21_prime | \стрельба_1_out_24 ;  // OR_Gate or_12, 32 bits wide
  assign out_23 = _20_prime | \стрельба_1_out_23 ;  // OR_Gate or_13, 32 bits wide
  assign out_22 = _19_prime | \стрельба_1_out_22 ;  // OR_Gate or_14, 32 bits wide
  assign out_21 = _18_prime | \стрельба_1_out_21 ;  // OR_Gate or_15, 32 bits wide
  assign out_20 = _17_prime | \стрельба_1_out_20 ;  // OR_Gate or_16, 32 bits wide
  assign out_19 = _16_prime | \стрельба_1_out_19 ;  // OR_Gate or_17, 32 bits wide
  assign out_18 = _15_prime | \стрельба_1_out_18 ;  // OR_Gate or_18, 32 bits wide
  assign out_17 = _14_prime | \стрельба_1_out_17 ;  // OR_Gate or_19, 32 bits wide
  assign out_16 = _13_prime | \стрельба_1_out_16 ;  // OR_Gate or_20, 32 bits wide
  assign out_15 = _12_prime | \стрельба_1_out_15 ;  // OR_Gate or_21, 32 bits wide
  assign out_14 = _11_prime | \стрельба_1_out_14 ;  // OR_Gate or_22, 32 bits wide
  assign out_13 = _10_prime | \стрельба_1_out_13 ;  // OR_Gate or_23, 32 bits wide
  assign out_12 = _9_prime | \стрельба_1_out_12 ;  // OR_Gate or_24, 32 bits wide
  assign out_7 = wall | \стрельба_1__3 ;  // OR_Gate or_25, 32 bits wide

  // Other names for the same wires on the sheet: _0[31:0] = out_4; _1[31:0] = out_5; _2[31:0] = out_6;
  //   _3[31:0] = out_7; _4[31:0] = out_8; _5[31:0] = out_9; _6[31:0] = out_10; _7[31:0] = out_11; _8[31:0] = out_12;
  //   _9[31:0] = out_13; _10[31:0] = out_14; _11[31:0] = out_15; _12[31:0] = out_16; _13[31:0] = out_17;
  //   _14[31:0] = out_18; _15[31:0] = out_19; _16[31:0] = out_20; _17[31:0] = out_21; _18[31:0] = out_22;
  //   _19[31:0] = out_23; _20[31:0] = out_24; _21[31:0] = out_25; _22[31:0] = out_27; _23[31:0] = out_29;
  //   _24[31:0] = out_30; _25[31:0] = out_31; _26[31:0] = out_32; _27[31:0] = out_33; _28[31:0] = out_34;
  //   _29[31:0] = out_35; _30[31:0] = out_36; _31[31:0] = out_37; init = initgame
endmodule

module inc5 (
  input  [4:0] X,
  output [4:0] R,
  output Cout
);

  wire [4:1] and_1_out;

  assign {Cout, and_1_out} = {and_1_out, 1'b1} & X;  // AND_Gate and_1, 5 bits wide
  assign R = X ^ {and_1_out, 1'b1};  // XOR_Gate xor_1, 5 bits wide
endmodule

module Player_Move (
  input  in_1,
  input  in_2,
  output [4:0] counter,
  output [31:0] _1,
  output [31:0] _0
);

  wire or_1_out;
  wire [31:0] shifter_1_out, shifter_2_out;

  or or_1 (or_1_out, in_1, in_2);
  Counter #(.width(5), .max('h1f)) counter_1 (.load(in_1), .Q(counter), .clk(or_1_out));  // open: D, count, carry, clr
  Decoder #(.select(5), .enable("false")) decoder_1 (
    .out0(_1[31]), .out1(_1[30]), .out2(_1[29]), .out3(_1[28]), .out4(_1[27]), .out5(_1[26]), .out6(_1[25]),
    .out7(_1[24]), .out8(_1[23]), .out9(_1[22]), .out10(_1[21]), .out11(_1[20]), .out12(_1[19]),
    .out13(_1[18]), .out14(_1[17]), .out15(_1[16]), .out16(_1[15]), .out17(_1[14]), .out18(_1[13]),
    .out19(_1[12]), .out20(_1[11]), .out21(_1[10]), .out22(_1[9]), .out23(_1[8]), .out24(_1[7]),
    .out25(_1[6]), .out26(_1[5]), .out27(_1[4]), .out28(_1[3]), .out29(_1[2]), .out30(_1[1]), .out31(_1[0]),
    .sel(counter));
  Shifter #(.width(32), .shift("lr")) shifter_1 (.in(_1), .\dist (5'b00001), .out(shifter_1_out));
  Shifter #(.width(32)) shifter_2 (.in(_1), .\dist (5'b00001), .out(shifter_2_out));
  assign _0 = shifter_2_out | _1 | shifter_1_out;  // OR_Gate or_2, 32 bits wide
endmodule

module transpon (
  input  [31:0] in_1,
  input  [31:0] in_2,
  input  [31:0] in_3,
  input  [31:0] in_4,
  input  [31:0] in_5,
  input  [31:0] in_6,
  input  [31:0] in_7,
  input  [31:0] in_8,
  input  [31:0] in_9,
  input  [31:0] in_10,
  input  [31:0] in_11,
  input  [31:0] in_12,
  input  [31:0] in_13,
  input  [31:0] in_14,
  input  [31:0] in_15,
  input  [31:0] in_16,
  input  [31:0] in_17,
  input  [31:0] in_18,
  input  [31:0] in_19,
  input  [31:0] in_20,
  input  [31:0] in_21,
  input  [31:0] in_22,
  input  [31:0] in_23,
  input  [31:0] in_24,
  input  [31:0] in_25,
  input  [31:0] in_26,
  input  [31:0] in_27,
  input  [31:0] in_28,
  input  [31:0] in_29,
  input  [31:0] in_30,
  input  [31:0] in_31,
  input  [31:0] in_32,
  output [31:0] _0,
  output [31:0] _1,
  output [31:0] _2,
  output [31:0] _3,
  output [31:0] _4,
  output [31:0] _5,
  output [31:0] _6,
  output [31:0] _7,
  output [31:0] _8,
  output [31:0] _9,
  output [31:0] _10,
  output [31:0] _11,
  output [31:0] _12,
  output [31:0] _13,
  output [31:0] _14,
  output [31:0] _15,
  output [31:0] _16,
  output [31:0] _17,
  output [31:0] _18,
  output [31:0] _19,
  output [31:0] _20,
  output [31:0] _21,
  output [31:0] _22,
  output [31:0] _23,
  output [31:0] _24,
  output [31:0] _25,
  output [31:0] _26,
  output [31:0] _27,
  output [31:0] _28,
  output [31:0] _29,
  output [31:0] _30,
  output [31:0] _31
);


  assign _0 = {in_1[0], in_2[0], in_3[0], in_4[0], in_5[0], in_6[0], in_7[0], in_8[0], in_9[0], in_10[0], in_11[0], in_12[0], in_13[0], in_14[0], in_15[0], in_16[0], in_17[0], in_18[0], in_19[0], in_20[0], in_21[0], in_22[0], in_23[0], in_24[0], in_25[0], in_26[0], in_27[0], in_28[0], in_29[0], in_30[0], in_31[0], in_32[0]};
  assign _1 = {in_1[1], in_2[1], in_3[1], in_4[1], in_5[1], in_6[1], in_7[1], in_8[1], in_9[1], in_10[1], in_11[1], in_12[1], in_13[1], in_14[1], in_15[1], in_16[1], in_17[1], in_18[1], in_19[1], in_20[1], in_21[1], in_22[1], in_23[1], in_24[1], in_25[1], in_26[1], in_27[1], in_28[1], in_29[1], in_30[1], in_31[1], in_32[1]};
  assign _2 = {in_1[2], in_2[2], in_3[2], in_4[2], in_5[2], in_6[2], in_7[2], in_8[2], in_9[2], in_10[2], in_11[2], in_12[2], in_13[2], in_14[2], in_15[2], in_16[2], in_17[2], in_18[2], in_19[2], in_20[2], in_21[2], in_22[2], in_23[2], in_24[2], in_25[2], in_26[2], in_27[2], in_28[2], in_29[2], in_30[2], in_31[2], in_32[2]};
  assign _3 = {in_1[3], in_2[3], in_3[3], in_4[3], in_5[3], in_6[3], in_7[3], in_8[3], in_9[3], in_10[3], in_11[3], in_12[3], in_13[3], in_14[3], in_15[3], in_16[3], in_17[3], in_18[3], in_19[3], in_20[3], in_21[3], in_22[3], in_23[3], in_24[3], in_25[3], in_26[3], in_27[3], in_28[3], in_29[3], in_30[3], in_31[3], in_32[3]};
  assign _4 = {in_1[4], in_2[4], in_3[4], in_4[4], in_5[4], in_6[4], in_7[4], in_8[4], in_9[4], in_10[4], in_11[4], in_12[4], in_13[4], in_14[4], in_15[4], in_16[4], in_17[4], in_18[4], in_19[4], in_20[4], in_21[4], in_22[4], in_23[4], in_24[4], in_25[4], in_26[4], in_27[4], in_28[4], in_29[4], in_30[4], in_31[4], in_32[4]};
  assign _5 = {in_1[5], in_2[5], in_3[5], in_4[5], in_5[5], in_6[5], in_7[5], in_8[5], in_9[5], in_10[5], in_11[5], in_12[5], in_13[5], in_14[5], in_15[5], in_16[5], in_17[5], in_18[5], in_19[5], in_20[5], in_21[5], in_22[5], in_23[5], in_24[5], in_25[5], in_26[5], in_27[5], in_28[5], in_29[5], in_30[5], in_31[5], in_32[5]};
  assign _6 = {in_1[6], in_2[6], in_3[6], in_4[6], in_5[6], in_6[6], in_7[6], in_8[6], in_9[6], in_10[6], in_11[6], in_12[6], in_13[6], in_14[6], in_15[6], in_16[6], in_17[6], in_18[6], in_19[6], in_20[6], in_21[6], in_22[6], in_23[6], in_24[6], in_25[6], in_26[6], in_27[6], in_28[6], in_29[6], in_30[6], in_31[6], in_32[6]};
  assign _7 = {in_1[7], in_2[7], in_3[7], in_4[7], in_5[7], in_6[7], in_7[7], in_8[7], in_9[7], in_10[7], in_11[7], in_12[7], in_13[7], in_14[7], in_15[7], in_16[7], in_17[7], in_18[7], in_19[7], in_20[7], in_21[7], in_22[7], in_23[7], in_24[7], in_25[7], in_26[7], in_27[7], in_28[7], in_29[7], in_30[7], in_31[7], in_32[7]};
  assign _8 = {in_1[8], in_2[8], in_3[8], in_4[8], in_5[8], in_6[8], in_7[8], in_8[8], in_9[8], in_10[8], in_11[8], in_12[8], in_13[8], in_14[8], in_15[8], in_16[8], in_17[8], in_18[8], in_19[8], in_20[8], in_21[8], in_22[8], in_23[8], in_24[8], in_25[8], in_26[8], in_27[8], in_28[8], in_29[8], in_30[8], in_31[8], in_32[8]};
  assign _9 = {in_1[9], in_2[9], in_3[9], in_4[9], in_5[9], in_6[9], in_7[9], in_8[9], in_9[9], in_10[9], in_11[9], in_12[9], in_13[9], in_14[9], in_15[9], in_16[9], in_17[9], in_18[9], in_19[9], in_20[9], in_21[9], in_22[9], in_23[9], in_24[9], in_25[9], in_26[9], in_27[9], in_28[9], in_29[9], in_30[9], in_31[9], in_32[9]};
  assign _10 = {in_1[10], in_2[10], in_3[10], in_4[10], in_5[10], in_6[10], in_7[10], in_8[10], in_9[10], in_10[10], in_11[10], in_12[10], in_13[10], in_14[10], in_15[10], in_16[10], in_17[10], in_18[10], in_19[10], in_20[10], in_21[10], in_22[10], in_23[10], in_24[10], in_25[10], in_26[10], in_27[10], in_28[10], in_29[10], in_30[10], in_31[10], in_32[10]};
  assign _11 = {in_1[11], in_2[11], in_3[11], in_4[11], in_5[11], in_6[11], in_7[11], in_8[11], in_9[11], in_10[11], in_11[11], in_12[11], in_13[11], in_14[11], in_15[11], in_16[11], in_17[11], in_18[11], in_19[11], in_20[11], in_21[11], in_22[11], in_23[11], in_24[11], in_25[11], in_26[11], in_27[11], in_28[11], in_29[11], in_30[11], in_31[11], in_32[11]};
  assign _12 = {in_1[12], in_2[12], in_3[12], in_4[12], in_5[12], in_6[12], in_7[12], in_8[12], in_9[12], in_10[12], in_11[12], in_12[12], in_13[12], in_14[12], in_15[12], in_16[12], in_17[12], in_18[12], in_19[12], in_20[12], in_21[12], in_22[12], in_23[12], in_24[12], in_25[12], in_26[12], in_27[12], in_28[12], in_29[12], in_30[12], in_31[12], in_32[12]};
  assign _13 = {in_1[13], in_2[13], in_3[13], in_4[13], in_5[13], in_6[13], in_7[13], in_8[13], in_9[13], in_10[13], in_11[13], in_12[13], in_13[13], in_14[13], in_15[13], in_16[13], in_17[13], in_18[13], in_19[13], in_20[13], in_21[13], in_22[13], in_23[13], in_24[13], in_25[13], in_26[13], in_27[13], in_28[13], in_29[13], in_30[13], in_31[13], in_32[13]};
  assign _14 = {in_1[14], in_2[14], in_3[14], in_4[14], in_5[14], in_6[14], in_7[14], in_8[14], in_9[14], in_10[14], in_11[14], in_12[14], in_13[14], in_14[14], in_15[14], in_16[14], in_17[14], in_18[14], in_19[14], in_20[14], in_21[14], in_22[14], in_23[14], in_24[14], in_25[14], in_26[14], in_27[14], in_28[14], in_29[14], in_30[14], in_31[14], in_32[14]};
  assign _15 = {in_1[15], in_2[15], in_3[15], in_4[15], in_5[15], in_6[15], in_7[15], in_8[15], in_9[15], in_10[15], in_11[15], in_12[15], in_13[15], in_14[15], in_15[15], in_16[15], in_17[15], in_18[15], in_19[15], in_20[15], in_21[15], in_22[15], in_23[15], in_24[15], in_25[15], in_26[15], in_27[15], in_28[15], in_29[15], in_30[15], in_31[15], in_32[15]};
  assign _16 = {in_1[16], in_2[16], in_3[16], in_4[16], in_5[16], in_6[16], in_7[16], in_8[16], in_9[16], in_10[16], in_11[16], in_12[16], in_13[16], in_14[16], in_15[16], in_16[16], in_17[16], in_18[16], in_19[16], in_20[16], in_21[16], in_22[16], in_23[16], in_24[16], in_25[16], in_26[16], in_27[16], in_28[16], in_29[16], in_30[16], in_31[16], in_32[16]};
  assign _17 = {in_1[17], in_2[17], in_3[17], in_4[17], in_5[17], in_6[17], in_7[17], in_8[17], in_9[17], in_10[17], in_11[17], in_12[17], in_13[17], in_14[17], in_15[17], in_16[17], in_17[17], in_18[17], in_19[17], in_20[17], in_21[17], in_22[17], in_23[17], in_24[17], in_25[17], in_26[17], in_27[17], in_28[17], in_29[17], in_30[17], in_31[17], in_32[17]};
  assign _18 = {in_1[18], in_2[18], in_3[18], in_4[18], in_5[18], in_6[18], in_7[18], in_8[18], in_9[18], in_10[18], in_11[18], in_12[18], in_13[18], in_14[18], in_15[18], in_16[18], in_17[18], in_18[18], in_19[18], in_20[18], in_21[18], in_22[18], in_23[18], in_24[18], in_25[18], in_26[18], in_27[18], in_28[18], in_29[18], in_30[18], in_31[18], in_32[18]};
  assign _19 = {in_1[19], in_2[19], in_3[19], in_4[19], in_5[19], in_6[19], in_7[19], in_8[19], in_9[19], in_10[19], in_11[19], in_12[19], in_13[19], in_14[19], in_15[19], in_16[19], in_17[19], in_18[19], in_19[19], in_20[19], in_21[19], in_22[19], in_23[19], in_24[19], in_25[19], in_26[19], in_27[19], in_28[19], in_29[19], in_30[19], in_31[19], in_32[19]};
  assign _20 = {in_1[20], in_2[20], in_3[20], in_4[20], in_5[20], in_6[20], in_7[20], in_8[20], in_9[20], in_10[20], in_11[20], in_12[20], in_13[20], in_14[20], in_15[20], in_16[20], in_17[20], in_18[20], in_19[20], in_20[20], in_21[20], in_22[20], in_23[20], in_24[20], in_25[20], in_26[20], in_27[20], in_28[20], in_29[20], in_30[20], in_31[20], in_32[20]};
  assign _21 = {in_1[21], in_2[21], in_3[21], in_4[21], in_5[21], in_6[21], in_7[21], in_8[21], in_9[21], in_10[21], in_11[21], in_12[21], in_13[21], in_14[21], in_15[21], in_16[21], in_17[21], in_18[21], in_19[21], in_20[21], in_21[21], in_22[21], in_23[21], in_24[21], in_25[21], in_26[21], in_27[21], in_28[21], in_29[21], in_30[21], in_31[21], in_32[21]};
  assign _22 = {in_1[22], in_2[22], in_3[22], in_4[22], in_5[22], in_6[22], in_7[22], in_8[22], in_9[22], in_10[22], in_11[22], in_12[22], in_13[22], in_14[22], in_15[22], in_16[22], in_17[22], in_18[22], in_19[22], in_20[22], in_21[22], in_22[22], in_23[22], in_24[22], in_25[22], in_26[22], in_27[22], in_28[22], in_29[22], in_30[22], in_31[22], in_32[22]};
  assign _23 = {in_1[23], in_2[23], in_3[23], in_4[23], in_5[23], in_6[23], in_7[23], in_8[23], in_9[23], in_10[23], in_11[23], in_12[23], in_13[23], in_14[23], in_15[23], in_16[23], in_17[23], in_18[23], in_19[23], in_20[23], in_21[23], in_22[23], in_23[23], in_24[23], in_25[23], in_26[23], in_27[23], in_28[23], in_29[23], in_30[23], in_31[23], in_32[23]};
  assign _24 = {in_1[24], in_2[24], in_3[24], in_4[24], in_5[24], in_6[24], in_7[24], in_8[24], in_9[24], in_10[24], in_11[24], in_12[24], in_13[24], in_14[24], in_15[24], in_16[24], in_17[24], in_18[24], in_19[24], in_20[24], in_21[24], in_22[24], in_23[24], in_24[24], in_25[24], in_26[24], in_27[24], in_28[24], in_29[24], in_30[24], in_31[24], in_32[24]};
  assign _25 = {in_1[25], in_2[25], in_3[25], in_4[25], in_5[25], in_6[25], in_7[25], in_8[25], in_9[25], in_10[25], in_11[25], in_12[25], in_13[25], in_14[25], in_15[25], in_16[25], in_17[25], in_18[25], in_19[25], in_20[25], in_21[25], in_22[25], in_23[25], in_24[25], in_25[25], in_26[25], in_27[25], in_28[25], in_29[25], in_30[25], in_31[25], in_32[25]};
  assign _26 = {in_1[26], in_2[26], in_3[26], in_4[26], in_5[26], in_6[26], in_7[26], in_8[26], in_9[26], in_10[26], in_11[26], in_12[26], in_13[26], in_14[26], in_15[26], in_16[26], in_17[26], in_18[26], in_19[26], in_20[26], in_21[26], in_22[26], in_23[26], in_24[26], in_25[26], in_26[26], in_27[26], in_28[26], in_29[26], in_30[26], in_31[26], in_32[26]};
  assign _27 = {in_1[27], in_2[27], in_3[27], in_4[27], in_5[27], in_6[27], in_7[27], in_8[27], in_9[27], in_10[27], in_11[27], in_12[27], in_13[27], in_14[27], in_15[27], in_16[27], in_17[27], in_18[27], in_19[27], in_20[27], in_21[27], in_22[27], in_23[27], in_24[27], in_25[27], in_26[27], in_27[27], in_28[27], in_29[27], in_30[27], in_31[27], in_32[27]};
  assign _28 = {in_1[28], in_2[28], in_3[28], in_4[28], in_5[28], in_6[28], in_7[28], in_8[28], in_9[28], in_10[28], in_11[28], in_12[28], in_13[28], in_14[28], in_15[28], in_16[28], in_17[28], in_18[28], in_19[28], in_20[28], in_21[28], in_22[28], in_23[28], in_24[28], in_25[28], in_26[28], in_27[28], in_28[28], in_29[28], in_30[28], in_31[28], in_32[28]};
  assign _29 = {in_1[29], in_2[29], in_3[29], in_4[29], in_5[29], in_6[29], in_7[29], in_8[29], in_9[29], in_10[29], in_11[29], in_12[29], in_13[29], in_14[29], in_15[29], in_16[29], in_17[29], in_18[29], in_19[29], in_20[29], in_21[29], in_22[29], in_23[29], in_24[29], in_25[29], in_26[29], in_27[29], in_28[29], in_29[29], in_30[29], in_31[29], in_32[29]};
  assign _30 = {in_1[30], in_2[30], in_3[30], in_4[30], in_5[30], in_6[30], in_7[30], in_8[30], in_9[30], in_10[30], in_11[30], in_12[30], in_13[30], in_14[30], in_15[30], in_16[30], in_17[30], in_18[30], in_19[30], in_20[30], in_21[30], in_22[30], in_23[30], in_24[30], in_25[30], in_26[30], in_27[30], in_28[30], in_29[30], in_30[30], in_31[30], in_32[30]};
  assign _31 = {in_1[31], in_2[31], in_3[31], in_4[31], in_5[31], in_6[31], in_7[31], in_8[31], in_9[31], in_10[31], in_11[31], in_12[31], in_13[31], in_14[31], in_15[31], in_16[31], in_17[31], in_18[31], in_19[31], in_20[31], in_21[31], in_22[31], in_23[31], in_24[31], in_25[31], in_26[31], in_27[31], in_28[31], in_29[31], in_30[31], in_31[31], in_32[31]};

  // Other names for the same wires on the sheet: _16_t[31:0] = in_17; _15_t[31:0] = in_16; _14_t[31:0] = in_15;
  //   _13_t[31:0] = in_14; _12_t[31:0] = in_13; _11_t[31:0] = in_12; _10_t[31:0] = in_11; _9_t[31:0] = in_10;
  //   _8_t[31:0] = in_9; _7_t[31:0] = in_8; _6_t[31:0] = in_7; _5_t[31:0] = in_6; _4_t[31:0] = in_5;
  //   _3_t[31:0] = in_4; _2_t[31:0] = in_3; _1_t[31:0] = in_2; _0_t[31:0] = in_1; _31_t[31:0] = in_32;
  //   _30_t[31:0] = in_31; _29_t[31:0] = in_30; _28_t[31:0] = in_29; _27_t[31:0] = in_28; _26_t[31:0] = in_27;
  //   _25_t[31:0] = in_26; _24_t[31:0] = in_25; _23_t[31:0] = in_24; _22_t[31:0] = in_23; _21_t[31:0] = in_22;
  //   _20_t[31:0] = in_21; _19_t[31:0] = in_20; _18_t[31:0] = in_19; _17_t[31:0] = in_18
endmodule

module \стенки  (
  input  [31:0] bullets,
  input  initwalls,
  input  clock,
  output [31:0] walls
);

  wire _0, _1, _2, _3, and_3_out, cdm_8_mark5_1_data_inst, cdm_8_mark5_1_mem_cycle, clk1, clk2, clk3,
       comparator_1_gt, comparator_2_lt, d_ff_1_q, d_ff_2_q, d_ff_3_q, d_ff_4_q, decoder_1_out0,
       decoder_1_out1, IAck, IOsel, IRQ, multiplexer_8_out, not_1_out, not_2_out, of1, of2, or_1_out,
       or_2_out, or_3_out, or_4_out, or_5_out, or_6_out, READwrite, reset, resreg, writenow;
  wire [1:0] ctr, index;
  wire [2:0] vec;
  wire [7:0] adress, bulladr, bulldat, cdm_8_mark5_1_data_out, cdm_8_mark5_1_r3, controlled_buffer_2_out,
       demultiplexer_1_out0, demultiplexer_1_out1, demultiplexer_1_out2, demultiplexer_1_out3, IOdat,
       multiplexer_1_out, multiplexer_2_out, multiplexer_3_out, multiplexer_4_out, multiplexer_6_out,
       multiplexer_7_out, walladr, walldat, walls_t;
  wire [7:2] subtractor_1_out;
  wire [31:0] \попадание_1_out ;

  Demultiplexer #(.select(2), .width(8)) demultiplexer_1 (
    .out0(demultiplexer_1_out0), .out1(demultiplexer_1_out1), .out2(demultiplexer_1_out2),
    .out3(demultiplexer_1_out3), .in(walls_t), .sel(index));  // open: en
  \попадание  \u_попадание_1  (.OUT(\попадание_1_out ), .A(walls), .B(bullets));  // open: Trigger
  \передача_данных  bull (
    .data(\попадание_1_out ), .slowenclock(clk1), .adress(8'h2f), .dataout(bulldat), .adressout(bulladr),
    .of(of1), .res(reset));
  D_Flip_Flop d_ff_1 (.D(of2), .Q(d_ff_1_q), .preset(of2), .reset(reset));  // open: clk, Qn, en
  // Probe on bulldat
  // Probe on bulladr
  Multiplexer #(.width(8)) multiplexer_1 (
    .in0(8'h3c), .in1(demultiplexer_1_out0), .out(multiplexer_1_out), .sel(d_ff_1_q));  // open: en
  Multiplexer #(.width(8)) multiplexer_2 (
    .in0(8'h3c), .in1(demultiplexer_1_out1), .out(multiplexer_2_out), .sel(d_ff_1_q));  // open: en
  Multiplexer #(.width(8)) multiplexer_3 (
    .in0(8'h3c), .in1(demultiplexer_1_out2), .out(multiplexer_3_out), .sel(d_ff_1_q));  // open: en
  Multiplexer #(.width(8)) multiplexer_4 (
    .in0(8'h3c), .in1(demultiplexer_1_out3), .out(multiplexer_4_out), .sel(d_ff_1_q));  // open: en
  or or_1 (or_1_out, \попадание_1_out [0], \попадание_1_out [1], \попадание_1_out [2], \попадание_1_out [3], \попадание_1_out [4], \попадание_1_out [5], \попадание_1_out [6], \попадание_1_out [7], \попадание_1_out [8], \попадание_1_out [9], \попадание_1_out [10], \попадание_1_out [11], \попадание_1_out [12], \попадание_1_out [13], \попадание_1_out [14], \попадание_1_out [15], \попадание_1_out [16], \попадание_1_out [17], \попадание_1_out [18], \попадание_1_out [19], \попадание_1_out [20], \попадание_1_out [21], \попадание_1_out [22], \попадание_1_out [23], \попадание_1_out [24], \попадание_1_out [25], \попадание_1_out [26], \попадание_1_out [27], \попадание_1_out [28], \попадание_1_out [29], \попадание_1_out [30], \попадание_1_out [31]);
  Register #(.trigger("high")) register_1 (
    .D(multiplexer_1_out), .en(or_2_out), .Q(walls[7:0]), .clk(clock));  // open: clr
  or or_2 (or_2_out, initwalls, _0);
  Register #(.trigger("high")) register_2 (
    .D(multiplexer_2_out), .en(or_3_out), .Q(walls[15:8]), .clk(clock));  // open: clr
  or or_3 (or_3_out, initwalls, _1);
  Register #(.trigger("high")) register_3 (
    .D(multiplexer_3_out), .en(or_4_out), .Q(walls[23:16]), .clk(clock));  // open: clr
  or or_4 (or_4_out, initwalls, _2);
  Register #(.trigger("high")) register_4 (
    .D(multiplexer_4_out), .en(or_5_out), .Q(walls[31:24]), .clk(clock));  // open: clr
  or or_5 (or_5_out, initwalls, _3);
  D_Flip_Flop d_ff_2 (.Q(d_ff_2_q), .preset(of1), .reset(reset));  // open: clk, D, Qn, en
  D_Flip_Flop d_ff_3 (.D(of2), .Q(d_ff_3_q), .preset(of2), .reset(reset));  // open: clk, Qn, en
  D_Flip_Flop d_ff_4 (.D(or_1_out), .Q(d_ff_4_q), .preset(or_1_out), .reset(reset));  // open: clk, Qn, en
  Multiplexer multiplexer_5 (.in0(1'b0), .in1(1'b1), .out(reset), .sel(resreg));  // open: en
  Priority_Encoder #(.select(2)) priority_encoder_1 (
    .in0(d_ff_4_q), .in1(d_ff_2_q), .in2(d_ff_3_q), .out(ctr));  // open: in3, gs, en_out, en_in
  Demultiplexer #(.select(2)) demultiplexer_2 (
    .out0(clk1), .out1(clk2), .out2(clk3), .in(clock), .sel(ctr));  // open: out3, en
  \передача_данных  \u_передача_данных_1  (
    .data(walls), .slowenclock(clk2), .adress(8'h2b), .dataout(walldat), .adressout(walladr), .of(of2),
    .res(reset));
  // Probe on adress
  Comparator #(.mode("unsigned")) comparator_1 (.a(adress), .b(8'h33), .gt(comparator_1_gt));  // open: eq, lt
  Comparator #(.mode("unsigned")) comparator_2 (.a(adress), .b(8'h38), .lt(comparator_2_lt));  // open: gt, eq
  Comparator comparator_3 (.a(cdm_8_mark5_1_r3), .b({8{1'b1}}), .eq(resreg));  // open: gt, lt
  Comparator comparator_4 (.a(adress), .b({8{1'b0}}));  // open: gt, eq, lt
  Subtractor subtractor_1 (.a(adress), .b(8'h34), .out({subtractor_1_out, index}));  // open: bin, bout
  and and_1 (writenow, comparator_1_gt, comparator_2_lt);
  CdM_8_mark5 cdm_8_mark5_1 (
    .clock(clk3), .addr(adress), .mem_read(READwrite), .mem_cycle(cdm_8_mark5_1_mem_cycle),
    .data_inst(cdm_8_mark5_1_data_inst), .data_out(cdm_8_mark5_1_data_out),
    .data_in(controlled_buffer_2_out), .r3(cdm_8_mark5_1_r3), .IAck(IAck), .IRQ(IRQ), .vec(vec));  // open: r0, r1, r2, PC, SP, PS, reset
  Multiplexer #(.select(2), .width(8)) multiplexer_6 (
    .in0(bulldat), .in1(walldat), .in2(IOdat), .out(multiplexer_6_out), .sel(ctr));  // open: in3, en
  and and_2 (IOsel, adress[4], adress[5], adress[6], adress[7], decoder_1_out1);
  Decoder #(.disabled(0)) decoder_1 (
    .out0(decoder_1_out0), .out1(decoder_1_out1), .sel(cdm_8_mark5_1_data_inst), .en(cdm_8_mark5_1_mem_cycle));
  not not_1 (not_1_out, READwrite);
  assign IOdat = not_1_out ? cdm_8_mark5_1_data_out : 8'bz;  // Controlled_Buffer controlled_buffer_1
  assign controlled_buffer_2_out = READwrite ? IOdat : 8'bz;  // Controlled_Buffer controlled_buffer_2
  Register register_5 (.D(IOdat), .en(writenow), .Q(walls_t), .clk(clk3));  // open: clr
  // Probe on adress
  and and_3 (and_3_out, decoder_1_out1, ~IOsel);  // AND_Gate
  // Probe on multiplexer_7_out
  Multiplexer #(.select(2), .width(8)) multiplexer_7 (
    .in0(bulladr), .in1(walladr), .in2(adress), .out(multiplexer_7_out), .sel(ctr));  // open: in3, en
  Comparator comparator_5 (.a({subtractor_1_out, index}), .b({8{1'b0}}), .eq(_0));  // open: gt, lt
  Comparator comparator_6 (.a({subtractor_1_out, index}), .b(8'h1), .eq(_1));  // open: gt, lt
  Comparator comparator_7 (.a({subtractor_1_out, index}), .b(8'h2), .eq(_2));  // open: gt, lt
  Comparator comparator_8 (.a({subtractor_1_out, index}), .b(8'h3), .eq(_3));  // open: gt, lt
  or or_6 (or_6_out, and_3_out, ~of2);  // OR_Gate
  Multiplexer multiplexer_8 (.in0(1'b0), .in1(READwrite), .out(multiplexer_8_out), .sel(of2));  // open: en
  not not_2 (not_2_out, clock);
  // Probe on IOdat
  RAM #(.bus("separate")) ram_1 (
    .addr(multiplexer_7_out), .din(multiplexer_6_out), .data(IOdat), .sel(or_6_out), .clk(not_2_out),
    .ld(multiplexer_8_out));  // open: str, clr
  ROM rom_1 (.addr(adress), .data(IOdat), .sel(decoder_1_out0));

  // Other names for the same wires on the sheet: IOaddr[3:0] = adress[3:0]; clk = clock

  // Notes on the sheet:
  //   contents of rom_1 (hex, n*v repeats v):
  //   d0 2c d1 30 d2 0 c1 19 b5 5 e0 19 c0 18 b0 1 25 41 d0 34 18 a1 c4 ee 21 c0 18 b0 d1 34 19 a4 c4 c5
  //   d0 2d d1 31 c1 19 b5 5 e0 39 c0 18 b0 1 25 41 d0 35 18 a1 c4 ee 41 c0 18 b0 d1 35 19 a4 c4 c5 d0 2e
  //   d1 32 c1 19 b5 5 e0 59 c0 18 b0 1 25 41 d0 36 18 a1 c4 ee 61 c0 18 b0 d1 36 19 a4 c4 c5 d0 2f d1 33
  //   c1 19 b5 5 e0 79 c0 18 b0 1 25 41 d0 37 18 a1 c4 ee 81 c0 18 b0 d1 37 19 a4 c4 c5 d4
endmodule

module \попадание  (
  input  [31:0] A,
  input  [31:0] B,
  output [31:0] OUT,
  output Trigger
);

  wire [31:0] xnor_1_out;

  assign xnor_1_out = ~(A ^ B);  // XNOR_Gate xnor_1, 32 bits wide
  and and_1 (OUT[0], xnor_1_out[0], B[0]);
  and and_2 (OUT[1], xnor_1_out[1], B[1]);
  and and_3 (OUT[2], xnor_1_out[2], B[2]);
  and and_4 (OUT[3], xnor_1_out[3], B[3]);
  and and_5 (OUT[4], xnor_1_out[4], B[4]);
  and and_6 (OUT[5], xnor_1_out[5], B[5]);
  and and_7 (OUT[6], xnor_1_out[6], B[6]);
  and and_8 (OUT[7], xnor_1_out[7], B[7]);
  and and_9 (OUT[8], xnor_1_out[8], B[8]);
  and and_10 (OUT[9], xnor_1_out[9], B[9]);
  and and_11 (OUT[10], xnor_1_out[10], B[10]);
  and and_12 (OUT[11], xnor_1_out[11], B[11]);
  and and_13 (OUT[12], xnor_1_out[12], B[12]);
  and and_14 (OUT[13], xnor_1_out[13], B[13]);
  and and_15 (OUT[14], xnor_1_out[14], B[14]);
  and and_16 (OUT[15], xnor_1_out[15], B[15]);
  and and_17 (OUT[16], xnor_1_out[16], B[16]);
  and and_18 (OUT[17], xnor_1_out[17], B[17]);
  and and_19 (OUT[18], xnor_1_out[18], B[18]);
  and and_20 (OUT[19], xnor_1_out[19], B[19]);
  and and_21 (OUT[20], xnor_1_out[20], B[20]);
  and and_22 (OUT[21], xnor_1_out[21], B[21]);
  and and_23 (OUT[22], xnor_1_out[22], B[22]);
  and and_24 (OUT[23], xnor_1_out[23], B[23]);
  and and_25 (OUT[24], xnor_1_out[24], B[24]);
  and and_26 (OUT[25], xnor_1_out[25], B[25]);
  and and_27 (OUT[26], xnor_1_out[26], B[26]);
  and and_28 (OUT[27], xnor_1_out[27], B[27]);
  and and_29 (OUT[28], xnor_1_out[28], B[28]);
  and and_30 (OUT[29], xnor_1_out[29], B[29]);
  and and_31 (OUT[30], xnor_1_out[30], B[30]);
  and and_32 (OUT[31], xnor_1_out[31], B[31]);
  oradd32 oradd32_1 (.in(OUT), .out(Trigger));

  // Other names for the same wires on the sheet: _0 = OUT[0]; _1 = OUT[1]; _2 = OUT[2]; _3 = OUT[3]; _4 = OUT[4];
  //   _5 = OUT[5]; _6 = OUT[6]; _7 = OUT[7]; _8 = OUT[8]; _9 = OUT[9]; _10 = OUT[10]; _11 = OUT[11]; _12 = OUT[12];
  //   _13 = OUT[13]; _14 = OUT[14]; _15 = OUT[15]; _16 = OUT[16]; _17 = OUT[17]; _18 = OUT[18]; _19 = OUT[19];
  //   _20 = OUT[20]; _21 = OUT[21]; _22 = OUT[22]; _23 = OUT[23]; _24 = OUT[24]; _25 = OUT[25]; _26 = OUT[26];
  //   _27 = OUT[27]; _28 = OUT[28]; _29 = OUT[29]; _30 = OUT[30]; _31 = OUT[31]
endmodule

module \стрельба  (
  input  [4:0] coord,
  input  clk,
  input  fire,
  input  reset,
  output [31:0] _2,
  output [31:0] _3,
  output [31:0] out_7,
  output [31:0] out_8,
  output [31:0] out_9,
  output [31:0] out_10,
  output [4:0] \Номер ,
  output [31:0] out_12,
  output [31:0] out_13,
  output [31:0] out_14,
  output [31:0] out_15,
  output [31:0] out_16,
  output [31:0] out_17,
  output [31:0] out_18,
  output [31:0] out_19,
  output [31:0] out_20,
  output [31:0] out_21,
  output [31:0] out_22,
  output [31:0] out_23,
  output [31:0] out_24,
  output [31:0] out_25,
  output [31:0] out_26,
  output [31:0] out_27,
  output [31:0] out_28,
  output [31:0] out_29,
  output [31:0] out_30,
  output [31:0] out_31,
  output [31:0] out_32,
  output [31:0] out_33,
  output [31:0] out_34,
  output [31:0] _31
);

  wire A0, controlled_buffer_1_out, controlled_buffer_3_out, counter_1_carry, fire_t, not_1_out, or_1_out,
       or_2_out, started;
  wire [4:0] counter_1_q, register_1_q;
  wire [31:0] demultiplexer_1_out0, demultiplexer_1_out1, demultiplexer_1_out2, demultiplexer_1_out3,
       demultiplexer_1_out4, demultiplexer_1_out5, demultiplexer_1_out6, demultiplexer_1_out7,
       demultiplexer_1_out8, demultiplexer_1_out9, demultiplexer_1_out10, demultiplexer_1_out11,
       demultiplexer_1_out12, demultiplexer_1_out13, demultiplexer_1_out14, demultiplexer_1_out15,
       demultiplexer_1_out16, demultiplexer_1_out17, demultiplexer_1_out18, demultiplexer_1_out19,
       demultiplexer_1_out20, demultiplexer_1_out21, demultiplexer_1_out22, demultiplexer_1_out23,
       demultiplexer_1_out24, demultiplexer_1_out25, demultiplexer_1_out26, demultiplexer_1_out27,
       demultiplexer_1_out28, demultiplexer_1_out29, demultiplexer_1_out30, demultiplexer_1_out31, st;

  not not_1 (not_1_out, started);
  assign controlled_buffer_1_out = not_1_out ? fire : 1'bz;  // Controlled_Buffer controlled_buffer_1
  Pull_Resistor pull_resistor_1 (.node(controlled_buffer_1_out));
  got1 got1_1 (.in_1(controlled_buffer_1_out), .out_2(fire_t));
  // Probe on coord
  Demultiplexer #(.select(5), .width(32)) demultiplexer_1 (
    .out0(demultiplexer_1_out0), .out1(demultiplexer_1_out1), .out2(demultiplexer_1_out2),
    .out3(demultiplexer_1_out3), .out4(demultiplexer_1_out4), .out5(demultiplexer_1_out5),
    .out6(demultiplexer_1_out6), .out7(demultiplexer_1_out7), .out8(demultiplexer_1_out8),
    .out9(demultiplexer_1_out9), .out10(demultiplexer_1_out10), .out11(demultiplexer_1_out11),
    .out12(demultiplexer_1_out12), .out13(demultiplexer_1_out13), .out14(demultiplexer_1_out14),
    .out15(demultiplexer_1_out15), .out16(demultiplexer_1_out16), .out17(demultiplexer_1_out17),
    .out18(demultiplexer_1_out18), .out19(demultiplexer_1_out19), .out20(demultiplexer_1_out20),
    .out21(demultiplexer_1_out21), .out22(demultiplexer_1_out22), .out23(demultiplexer_1_out23),
    .out24(demultiplexer_1_out24), .out25(demultiplexer_1_out25), .out26(demultiplexer_1_out26),
    .out27(demultiplexer_1_out27), .out28(demultiplexer_1_out28), .out29(demultiplexer_1_out29),
    .out30(demultiplexer_1_out30), .out31(demultiplexer_1_out31), .in(st), .sel(register_1_q));  // open: en
  Register #(.width(5)) register_1 (.D(coord), .en(fire_t), .Q(register_1_q), .clk(fire_t));  // open: clr
  // transpon transpon_1: pin names not known; wires that end beside it: demultiplexer_1_out0, demultiplexer_1_out1, demultiplexer_1_out2, demultiplexer_1_out3, demultiplexer_1_out4, demultiplexer_1_out5, demultiplexer_1_out6, demultiplexer_1_out7, demultiplexer_1_out8, demultiplexer_1_out9, demultiplexer_1_out10, demultiplexer_1_out11, demultiplexer_1_out12, demultiplexer_1_out13, demultiplexer_1_out14, demultiplexer_1_out15, demultiplexer_1_out16, demultiplexer_1_out17, demultiplexer_1_out18, demultiplexer_1_out19, demultiplexer_1_out20, demultiplexer_1_out21, demultiplexer_1_out22, demultiplexer_1_out23, demultiplexer_1_out24, demultiplexer_1_out25, demultiplexer_1_out26, demultiplexer_1_out27, demultiplexer_1_out28, demultiplexer_1_out29, demultiplexer_1_out30, demultiplexer_1_out31, _31, out_34, out_33, out_32, out_31, out_30, out_29, out_28, out_27, out_26, out_25, out_24, out_23, out_22, out_21, out_20, out_19, out_18, out_17, out_16, out_15, out_14, out_13, out_12, out_10, out_9, out_8, out_7, _3, _2
  assign A0 = fire_t ? fire_t : 1'bz;  // Controlled_Buffer controlled_buffer_2
  D_Flip_Flop d_ff_1 (.Q(started), .preset(fire_t), .reset(or_1_out));  // open: clk, D, Qn, en
  or or_1 (or_1_out, reset, counter_1_carry);
  assign controlled_buffer_3_out = started ? clk : 1'bz;  // Controlled_Buffer controlled_buffer_3
  Counter #(.width(5), .max('h1e)) counter_1 (
    .Q(counter_1_q), .carry(counter_1_carry), .clk(controlled_buffer_3_out), .clr(or_2_out));  // open: load, D, count
  or or_2 (or_2_out, reset, ~started);  // OR_Gate
  Decoder #(.select(5), .enable("false")) decoder_1 (
    .out0(st[0]), .out1(st[1]), .out2(st[2]), .out3(st[3]), .out4(st[4]), .out5(st[5]), .out6(st[6]),
    .out7(st[7]), .out8(st[8]), .out9(st[9]), .out10(st[10]), .out11(st[11]), .out12(st[12]), .out13(st[13]),
    .out14(st[14]), .out15(st[15]), .out16(st[16]), .out17(st[17]), .out18(st[18]), .out19(st[19]),
    .out20(st[20]), .out21(st[21]), .out22(st[22]), .out23(st[23]), .out24(st[24]), .out25(st[25]),
    .out26(st[26]), .out27(st[27]), .out28(st[28]), .out29(st[29]), .out30(st[30]), .out31(st[31]),
    .sel(\Номер ));
  inc5 inc5_1 (.X(counter_1_q), .R(\Номер ));  // open: Cout

  // Other names for the same wires on the sheet: _4[31:0] = out_7; _5[31:0] = out_8; _6[31:0] = out_9;
  //   _7[31:0] = out_10; _8[31:0] = out_12; _9[31:0] = out_13; _10[31:0] = out_14; _11[31:0] = out_15;
  //   _12[31:0] = out_16; _13[31:0] = out_17; _14[31:0] = out_18; _15[31:0] = out_19; _16[31:0] = out_20;
  //   _17[31:0] = out_21; _18[31:0] = out_22; _19[31:0] = out_23; _20[31:0] = out_24; _21[31:0] = out_25;
  //   _22[31:0] = out_26; _23[31:0] = out_27; _24[31:0] = out_28; _25[31:0] = out_29; _26[31:0] = out_30;
  //   _27[31:0] = out_31; _28[31:0] = out_32; _29[31:0] = out_33; _30[31:0] = out_34; A1 = A0; A2 = A0; A3 = A0

  // Notes on the sheet:
  //   Столбец из пуль
endmodule

// 0x7
module \передача_данных  (
  input  [31:0] data,
  input  slowenclock,
  input  res,
  input  [7:0] adress,
  output [7:0] dataout,
  output [7:0] adressout,
  output of
);

  wire [1:0] counter_1_q;
  wire [2:2] counter_1_q_2;
  wire [7:0] bit_extender_1_out;

  Multiplexer #(.select(2), .width(8)) multiplexer_1 (
    .in0(data[7:0]), .in1(data[15:8]), .in2(data[23:16]), .in3(data[31:24]), .out(dataout), .sel(counter_1_q));  // open: en
  Counter #(.width(3), .max('h5)) counter_1 (
    .Q({counter_1_q_2[2], counter_1_q}), .carry(of), .clk(slowenclock), .clr(res));  // open: load, D, count
  assign bit_extender_1_out = {{5{1'b0}}, {counter_1_q_2[2], counter_1_q}};  // Bit_Extender bit_extender_1
  Adder adder_1 (.a(bit_extender_1_out), .b(adress), .out(adressout));  // open: cin, cout
endmodule

module menu (
  input  [4:0] in,
  output [31:0] out
);

  wire decoder_1_out0, decoder_1_out1, decoder_1_out2, decoder_1_out3, decoder_1_out4, decoder_1_out5,
       decoder_1_out6, decoder_1_out7, decoder_1_out8, decoder_1_out9, decoder_1_out10, decoder_1_out11,
       decoder_1_out12, decoder_1_out13, decoder_1_out14, decoder_1_out15, decoder_1_out16, decoder_1_out17,
       decoder_1_out18, decoder_1_out19, decoder_1_out20, decoder_1_out21, decoder_1_out22, decoder_1_out23,
       decoder_1_out24, decoder_1_out25, decoder_1_out26, decoder_1_out27, decoder_1_out28, decoder_1_out29,
       decoder_1_out30, decoder_1_out31;
  wire [31:0] pull_resistor_1_node, pull_resistor_2_node, pull_resistor_3_node;

  Pull_Resistor pull_resistor_1 (.node(pull_resistor_1_node));
  Pull_Resistor pull_resistor_2 (.node(pull_resistor_2_node));
  Pull_Resistor pull_resistor_3 (.node(pull_resistor_3_node));
  Decoder #(.select(5), .disabled(0), .enable("false")) decoder_1 (
    .out0(decoder_1_out0), .out1(decoder_1_out1), .out2(decoder_1_out2), .out3(decoder_1_out3),
    .out4(decoder_1_out4), .out5(decoder_1_out5), .out6(decoder_1_out6), .out7(decoder_1_out7),
    .out8(decoder_1_out8), .out9(decoder_1_out9), .out10(decoder_1_out10), .out11(decoder_1_out11),
    .out12(decoder_1_out12), .out13(decoder_1_out13), .out14(decoder_1_out14), .out15(decoder_1_out15),
    .out16(decoder_1_out16), .out17(decoder_1_out17), .out18(decoder_1_out18), .out19(decoder_1_out19),
    .out20(decoder_1_out20), .out21(decoder_1_out21), .out22(decoder_1_out22), .out23(decoder_1_out23),
    .out24(decoder_1_out24), .out25(decoder_1_out25), .out26(decoder_1_out26), .out27(decoder_1_out27),
    .out28(decoder_1_out28), .out29(decoder_1_out29), .out30(decoder_1_out30), .out31(decoder_1_out31),
    .sel(in));
  assign out = decoder_1_out28 ? pull_resistor_3_node : 32'bz;  // Controlled_Buffer controlled_buffer_1
  assign out = decoder_1_out29 ? pull_resistor_3_node : 32'bz;  // Controlled_Buffer controlled_buffer_2
  assign out = decoder_1_out30 ? pull_resistor_3_node : 32'bz;  // Controlled_Buffer controlled_buffer_3
  assign out = decoder_1_out31 ? pull_resistor_3_node : 32'bz;  // Controlled_Buffer controlled_buffer_4
  assign out = decoder_1_out25 ? 32'h45141040 : 32'bz;  // Controlled_Buffer controlled_buffer_5
  assign out = decoder_1_out26 ? 32'h45141040 : 32'bz;  // Controlled_Buffer controlled_buffer_6
  assign out = decoder_1_out27 ? 32'h7df7df7c : 32'bz;  // Controlled_Buffer controlled_buffer_7
  assign out = decoder_1_out22 ? 32'h41840104 : 32'bz;  // Controlled_Buffer controlled_buffer_8
  assign out = decoder_1_out23 ? 32'h7df7df7c : 32'bz;  // Controlled_Buffer controlled_buffer_9
  assign out = decoder_1_out24 ? 32'h45141040 : 32'bz;  // Controlled_Buffer controlled_buffer_10
  assign out = decoder_1_out19 ? pull_resistor_2_node : 32'bz;  // Controlled_Buffer controlled_buffer_11
  assign out = decoder_1_out20 ? 32'h4117df7c : 32'bz;  // Controlled_Buffer controlled_buffer_12
  assign out = decoder_1_out21 ? 32'h41240104 : 32'bz;  // Controlled_Buffer controlled_buffer_13
  assign out = decoder_1_out15 ? pull_resistor_2_node : 32'bz;  // Controlled_Buffer controlled_buffer_14
  assign out = decoder_1_out16 ? pull_resistor_2_node : 32'bz;  // Controlled_Buffer controlled_buffer_15
  assign out = decoder_1_out17 ? pull_resistor_2_node : 32'bz;  // Controlled_Buffer controlled_buffer_16
  assign out = decoder_1_out18 ? pull_resistor_2_node : 32'bz;  // Controlled_Buffer controlled_buffer_17
  assign out = decoder_1_out12 ? 32'h7df7dfbe : 32'bz;  // Controlled_Buffer controlled_buffer_18
  assign out = decoder_1_out13 ? pull_resistor_2_node : 32'bz;  // Controlled_Buffer controlled_buffer_19
  assign out = decoder_1_out14 ? pull_resistor_2_node : 32'bz;  // Controlled_Buffer controlled_buffer_20
  assign out = decoder_1_out9 ? 32'h40445088 : 32'bz;  // Controlled_Buffer controlled_buffer_21
  assign out = decoder_1_out10 ? 32'h40445088 : 32'bz;  // Controlled_Buffer controlled_buffer_22
  assign out = decoder_1_out11 ? 32'h40445088 : 32'bz;  // Controlled_Buffer controlled_buffer_23
  assign out = decoder_1_out5 ? 32'h7c445108 : 32'bz;  // Controlled_Buffer controlled_buffer_24
  assign out = decoder_1_out6 ? 32'h4445208 : 32'bz;  // Controlled_Buffer controlled_buffer_25
  assign out = decoder_1_out7 ? 32'h4445808 : 32'bz;  // Controlled_Buffer controlled_buffer_26
  assign out = decoder_1_out8 ? 32'h7c47df88 : 32'bz;  // Controlled_Buffer controlled_buffer_27
  assign out = decoder_1_out1 ? pull_resistor_1_node : 32'bz;  // Controlled_Buffer controlled_buffer_28
  assign out = decoder_1_out2 ? pull_resistor_1_node : 32'bz;  // Controlled_Buffer controlled_buffer_29
  assign out = decoder_1_out3 ? pull_resistor_1_node : 32'bz;  // Controlled_Buffer controlled_buffer_30
  assign out = decoder_1_out4 ? pull_resistor_1_node : 32'bz;  // Controlled_Buffer controlled_buffer_31
  assign out = decoder_1_out0 ? pull_resistor_1_node : 32'bz;  // Controlled_Buffer controlled_buffer_32
endmodule

module circ (
  input  on,
  input  isgameover,
  input  start,
  input  [4:0] counter,
  input  [31:0] game,
  input  endgame,
  output [31:0] out_7
);

  wire and_1_out, and_2_out, not_1_out;
  wire [31:0] gameover_1_out, menu_1_out;

  not not_1 (not_1_out, on);
  and and_1 (and_1_out, on, ~start);  // AND_Gate
  menu menu_1 (.in(counter), .out(menu_1_out));
  and and_2 (and_2_out, on, ~endgame, start);  // AND_Gate
  assign out_7 = not_1_out ? {32{1'b0}} : 32'bz;  // Controlled_Buffer controlled_buffer_1
  assign out_7 = and_1_out ? menu_1_out : 32'bz;  // Controlled_Buffer controlled_buffer_2
  assign out_7 = and_2_out ? game : 32'bz;  // Controlled_Buffer controlled_buffer_3
  gameover gameover_1 (.in(counter), .isGameOver(isgameover), .out(gameover_1_out));
  assign out_7 = endgame ? gameover_1_out : 32'bz;  // Controlled_Buffer controlled_buffer_4
endmodule

module menumega (
  input  gameover,
  input  endgame,
  input  on,
  input  [4:0] beg,
  input  start,
  input  [31:0] in_6,
  input  [31:0] in_7,
  input  [31:0] in_8,
  input  [31:0] in_9,
  input  [31:0] in_10,
  input  [31:0] in_11,
  input  [31:0] in_12,
  input  [31:0] in_13,
  output [31:0] out_14,
  output [31:0] out_15,
  output [31:0] out_16,
  output [31:0] out_17,
  output [31:0] out_18,
  output [31:0] out_19,
  output [31:0] out_20,
  output [31:0] out_21,
  output [4:0] \end 
);

  wire [4:0] inc5_1_r, inc5_2_r, inc5_3_r, inc5_4_r, inc5_5_r, inc5_7_r;

  circ circ_1 (
    .on(on), .start(start), .counter(beg), .game(in_6), .out_7(out_14), .isgameover(gameover),
    .endgame(endgame));
  circ circ_2 (
    .on(on), .start(start), .counter(inc5_1_r), .game(in_7), .out_7(out_15), .isgameover(gameover),
    .endgame(endgame));
  circ circ_3 (
    .on(on), .start(start), .counter(inc5_2_r), .game(in_10), .out_7(out_18), .isgameover(gameover),
    .endgame(endgame));
  inc5 inc5_1 (.X(inc5_2_r), .R(inc5_1_r));  // open: Cout
  inc5 inc5_2 (.X(beg), .R(inc5_2_r));  // open: Cout
  circ circ_4 (
    .on(on), .start(start), .counter(inc5_3_r), .game(in_11), .out_7(out_19), .isgameover(gameover),
    .endgame(endgame));
  inc5 inc5_3 (.X(inc5_1_r), .R(inc5_3_r));  // open: Cout
  inc5 inc5_4 (.X(inc5_3_r), .R(inc5_4_r));  // open: Cout
  circ circ_5 (
    .on(on), .start(start), .counter(inc5_4_r), .game(in_8), .out_7(out_16), .isgameover(gameover),
    .endgame(endgame));
  circ circ_6 (
    .on(on), .start(start), .counter(inc5_5_r), .game(in_12), .out_7(out_20), .isgameover(gameover),
    .endgame(endgame));
  inc5 inc5_5 (.X(inc5_4_r), .R(inc5_5_r));  // open: Cout
  circ circ_7 (
    .on(on), .start(start), .counter(inc5_7_r), .game(in_9), .out_7(out_17), .isgameover(gameover),
    .endgame(endgame));
  inc5 inc5_6 (.X(inc5_7_r), .R(\end ));  // open: Cout
  inc5 inc5_7 (.X(inc5_5_r), .R(inc5_7_r));  // open: Cout
  circ circ_8 (
    .on(on), .start(start), .counter(\end ), .game(in_13), .out_7(out_21), .isgameover(gameover),
    .endgame(endgame));
endmodule

module pentamenu (
  input  start,
  input  on,
  input  [6:0] control,
  output [31:0] out_4,
  output [31:0] out_5,
  output [31:0] out_6,
  output [31:0] out_7,
  output [31:0] out_8,
  output [31:0] out_9,
  output clk,
  output [31:0] out_11,
  output [31:0] out_12,
  output [31:0] out_13,
  output [31:0] out_14,
  output [31:0] out_15,
  output [31:0] out_16,
  output [31:0] out_17,
  output [31:0] out_18,
  output [31:0] out_19,
  output [31:0] out_20,
  output [31:0] out_21,
  output [31:0] out_22,
  output [31:0] out_23,
  output [31:0] out_24,
  output [31:0] out_25,
  output [31:0] out_26,
  output [31:0] out_27,
  output [31:0] out_28,
  output [31:0] out_29,
  output [31:0] out_30,
  output [31:0] out_31,
  output [31:0] out_32,
  output [31:0] out_33,
  output [31:0] out_34,
  output [31:0] out_35,
  output [31:0] out_36
);

  wire d_ff_1_q, d_ff_2_q, eg, go, main_1_gameover, main_1_win, multiplexer_1_out, not_1_out, on_t, start_t;
  wire [4:0] menumega_1_end, menumega_2_end, menumega_3_end;
  wire [31:0] main_1_out_4, main_1_out_5, main_1_out_6, main_1_out_7, main_1_out_8, main_1_out_9,
       main_1_out_10, main_1_out_11, main_1_out_12, main_1_out_13, main_1_out_14, main_1_out_15,
       main_1_out_16, main_1_out_17, main_1_out_18, main_1_out_19, main_1_out_20, main_1_out_21,
       main_1_out_22, main_1_out_23, main_1_out_24, main_1_out_25, main_1_out_27, main_1_out_29,
       main_1_out_30, main_1_out_31, main_1_out_32, main_1_out_33, main_1_out_34, main_1_out_35,
       main_1_out_36, main_1_out_37;

  Counter #(.width(1), .max('h1)) counter_1 (.count(start), .Q(start_t), .clk(start));  // open: load, D, carry, clr
  Counter #(.width(1), .max('h1)) counter_2 (.count(on), .Q(on_t), .clk(on));  // open: load, D, carry, clr
  main main_1 (
    .out_4(main_1_out_4), .out_5(main_1_out_5), .out_6(main_1_out_6), .out_7(main_1_out_7),
    .out_8(main_1_out_8), .out_9(main_1_out_9), .out_10(main_1_out_10), .out_11(main_1_out_11),
    .out_12(main_1_out_12), .out_13(main_1_out_13), .out_14(main_1_out_14), .out_15(main_1_out_15),
    .out_16(main_1_out_16), .out_17(main_1_out_17), .out_18(main_1_out_18), .out_19(main_1_out_19),
    .out_20(main_1_out_20), .out_21(main_1_out_21), .out_22(main_1_out_22), .out_23(main_1_out_23),
    .out_24(main_1_out_24), .out_25(main_1_out_25), .out_27(main_1_out_27), .out_29(main_1_out_29),
    .out_30(main_1_out_30), .out_31(main_1_out_31), .out_32(main_1_out_32), .out_33(main_1_out_33),
    .out_34(main_1_out_34), .out_35(main_1_out_35), .out_36(main_1_out_36), .out_37(main_1_out_37),
    .initgame(start_t), .moving(control), .clk(clk), .gameover(main_1_gameover), .win(main_1_win));
  D_Flip_Flop d_ff_1 (.clk(main_1_win), .D(main_1_win), .Q(d_ff_1_q));  // open: Qn, preset, en, reset
  menumega menumega_1 (
    .beg({5{1'b0}}), .on(on_t), .start(start_t), .out_14(out_4), .out_18(out_5), .out_15(out_6),
    .out_19(out_7), .out_16(out_8), .out_20(out_9), .out_17(out_11), .out_21(out_12), .\end (menumega_1_end),
    .in_6(main_1_out_4), .in_7(main_1_out_6), .in_8(main_1_out_8), .in_9(main_1_out_10),
    .in_10(main_1_out_5), .in_11(main_1_out_7), .in_12(main_1_out_9), .in_13(main_1_out_11), .endgame(eg),
    .gameover(go));
  Pull_Resistor pull_resistor_1 (.node(eg));
  assign eg = not_1_out ? d_ff_1_q : 1'bz;  // Controlled_Buffer controlled_buffer_1
  menumega menumega_2 (
    .beg(menumega_1_end), .on(on_t), .start(start_t), .out_14(out_13), .out_18(out_14), .out_15(out_15),
    .out_19(out_16), .out_16(out_17), .out_20(out_18), .out_17(out_19), .out_21(out_20),
    .\end (menumega_2_end), .in_6(main_1_out_12), .in_7(main_1_out_14), .in_8(main_1_out_16),
    .in_9(main_1_out_18), .in_10(main_1_out_13), .in_11(main_1_out_15), .in_12(main_1_out_17),
    .in_13(main_1_out_19), .endgame(eg), .gameover(go));
  menumega menumega_3 (
    .beg(menumega_2_end), .on(on_t), .start(start_t), .out_14(out_21), .out_18(out_22), .out_15(out_23),
    .out_19(out_24), .out_16(out_25), .out_20(out_26), .out_17(out_27), .out_21(out_28),
    .\end (menumega_3_end), .in_6(main_1_out_20), .in_7(main_1_out_22), .in_8(main_1_out_24),
    .in_9(main_1_out_27), .in_10(main_1_out_21), .in_11(main_1_out_23), .in_12(main_1_out_25),
    .in_13(main_1_out_29), .endgame(eg), .gameover(go));
  menumega menumega_4 (
    .beg(menumega_3_end), .on(on_t), .start(start_t), .out_14(out_29), .out_18(out_30), .out_15(out_31),
    .out_19(out_32), .out_16(out_33), .out_20(out_34), .out_17(out_35), .out_21(out_36),
    .in_6(main_1_out_30), .in_7(main_1_out_32), .in_8(main_1_out_34), .in_9(main_1_out_36),
    .in_10(main_1_out_31), .in_11(main_1_out_33), .in_12(main_1_out_35), .in_13(main_1_out_37), .endgame(eg),
    .gameover(go));  // open: end
  Clock clock_1 (.out(clk));
  Pull_Resistor pull_resistor_2 (.node(eg));
  assign eg = d_ff_2_q ? d_ff_2_q : 1'bz;  // Controlled_Buffer controlled_buffer_2
  D_Flip_Flop d_ff_2 (.clk(main_1_gameover), .D(main_1_gameover), .Q(d_ff_2_q));  // open: Qn, preset, en, reset
  assign go = multiplexer_1_out ? d_ff_2_q : 1'bz;  // Controlled_Buffer controlled_buffer_3
  Multiplexer multiplexer_1 (.in0(d_ff_2_q), .in1(1'b0), .out(multiplexer_1_out), .sel(d_ff_1_q));  // open: en
  not not_1 (not_1_out, d_ff_2_q);
  Pull_Resistor pull_resistor_3 (.node(go));

  // Other names for the same wires on the sheet: _0[31:0] = out_4; _1[31:0] = out_5; _2[31:0] = out_6;
  //   _3[31:0] = out_7; _4[31:0] = out_8; _5[31:0] = out_9; _6[31:0] = out_11; _7[31:0] = out_12; _8[31:0] = out_13;
  //   _9[31:0] = out_14; _10[31:0] = out_15; _11[31:0] = out_16; _12[31:0] = out_17; _13[31:0] = out_18;
  //   _14[31:0] = out_19; _15[31:0] = out_20; _16[31:0] = out_21; _17[31:0] = out_22; _18[31:0] = out_23;
  //   _19[31:0] = out_24; _20[31:0] = out_25; _21[31:0] = out_26; _22[31:0] = out_27; _23[31:0] = out_28;
  //   _24[31:0] = out_29; _25[31:0] = out_30; _26[31:0] = out_31; _27[31:0] = out_32; _28[31:0] = out_33;
  //   _29[31:0] = out_34; _30[31:0] = out_35; _31[31:0] = out_36
endmodule

module MAIN (
);

  wire keyboard_1_avail, ON_OFF_out, pentamenu_1_clk, START_out;
  wire [6:0] keyboard_1_data;
  wire [31:0] pentamenu_1_out_4, pentamenu_1_out_5, pentamenu_1_out_6, pentamenu_1_out_7, pentamenu_1_out_8,
       pentamenu_1_out_9, pentamenu_1_out_11, pentamenu_1_out_12, pentamenu_1_out_13, pentamenu_1_out_14,
       pentamenu_1_out_15, pentamenu_1_out_16, pentamenu_1_out_17, pentamenu_1_out_18, pentamenu_1_out_19,
       pentamenu_1_out_20, pentamenu_1_out_21, pentamenu_1_out_22, pentamenu_1_out_23, pentamenu_1_out_24,
       pentamenu_1_out_25, pentamenu_1_out_26, pentamenu_1_out_27, pentamenu_1_out_28, pentamenu_1_out_29,
       pentamenu_1_out_30, pentamenu_1_out_31, pentamenu_1_out_32, pentamenu_1_out_33, pentamenu_1_out_34,
       pentamenu_1_out_35, pentamenu_1_out_36;

  DotMatrix #(.inputtype("row"), .matrixcols(32), .matrixrows(32)) dotmatrix_1 (
    .row0(pentamenu_1_out_36), .row1(pentamenu_1_out_35), .row2(pentamenu_1_out_34),
    .row3(pentamenu_1_out_33), .row4(pentamenu_1_out_32), .row5(pentamenu_1_out_31),
    .row6(pentamenu_1_out_30), .row7(pentamenu_1_out_29), .row8(pentamenu_1_out_28),
    .row9(pentamenu_1_out_27), .row10(pentamenu_1_out_26), .row11(pentamenu_1_out_25),
    .row12(pentamenu_1_out_24), .row13(pentamenu_1_out_23), .row14(pentamenu_1_out_22),
    .row15(pentamenu_1_out_21), .row16(pentamenu_1_out_20), .row17(pentamenu_1_out_19),
    .row18(pentamenu_1_out_18), .row19(pentamenu_1_out_17), .row20(pentamenu_1_out_16),
    .row21(pentamenu_1_out_15), .row22(pentamenu_1_out_14), .row23(pentamenu_1_out_13),
    .row24(pentamenu_1_out_12), .row25(pentamenu_1_out_11), .row26(pentamenu_1_out_9),
    .row27(pentamenu_1_out_8), .row28(pentamenu_1_out_7), .row29(pentamenu_1_out_6),
    .row30(pentamenu_1_out_5), .row31(pentamenu_1_out_4));
  pentamenu pentamenu_1 (
    .out_4(pentamenu_1_out_4), .out_5(pentamenu_1_out_5), .start(START_out), .out_6(pentamenu_1_out_6),
    .on(ON_OFF_out), .out_7(pentamenu_1_out_7), .out_8(pentamenu_1_out_8), .out_9(pentamenu_1_out_9),
    .out_11(pentamenu_1_out_11), .control(keyboard_1_data), .out_12(pentamenu_1_out_12),
    .out_13(pentamenu_1_out_13), .out_14(pentamenu_1_out_14), .out_15(pentamenu_1_out_15),
    .out_16(pentamenu_1_out_16), .out_17(pentamenu_1_out_17), .out_18(pentamenu_1_out_18),
    .out_19(pentamenu_1_out_19), .out_20(pentamenu_1_out_20), .out_21(pentamenu_1_out_21),
    .out_22(pentamenu_1_out_22), .out_23(pentamenu_1_out_23), .out_24(pentamenu_1_out_24),
    .out_25(pentamenu_1_out_25), .out_26(pentamenu_1_out_26), .out_27(pentamenu_1_out_27),
    .out_28(pentamenu_1_out_28), .out_29(pentamenu_1_out_29), .out_30(pentamenu_1_out_30),
    .out_31(pentamenu_1_out_31), .out_32(pentamenu_1_out_32), .out_33(pentamenu_1_out_33),
    .out_34(pentamenu_1_out_34), .out_35(pentamenu_1_out_35), .out_36(pentamenu_1_out_36),
    .clk(pentamenu_1_clk));
  Keyboard keyboard_1 (
    .clk(pentamenu_1_clk), .clr(keyboard_1_avail), .avail(keyboard_1_avail), .data(keyboard_1_data));  // open: re
  cosmsirc_nonuse cosmsirc_nonuse_1 ();
  Button ON_OFF (.out(ON_OFF_out));
  Button START (.out(START_out));
endmodule

module gameover (
  input  [4:0] in,
  input  isGameOver,
  output [31:0] out
);

  wire decoder_1_out0, decoder_1_out1, decoder_1_out2, decoder_1_out3, decoder_1_out4, decoder_1_out5,
       decoder_1_out6, decoder_1_out7, decoder_1_out8, decoder_1_out9, decoder_1_out10, decoder_1_out11,
       decoder_1_out12, decoder_1_out13, decoder_1_out14, decoder_1_out15, decoder_1_out16, decoder_1_out17,
       decoder_1_out18, decoder_1_out19, decoder_1_out20, decoder_1_out21, decoder_1_out22, decoder_1_out23,
       decoder_1_out24, decoder_1_out25, decoder_1_out26, decoder_1_out27, decoder_1_out28, decoder_1_out29,
       decoder_1_out30, decoder_1_out31;
  wire [31:0] multiplexer_1_out, multiplexer_2_out, multiplexer_3_out, multiplexer_4_out, multiplexer_5_out,
       multiplexer_6_out, multiplexer_7_out, multiplexer_8_out, multiplexer_9_out, multiplexer_10_out,
       multiplexer_11_out, multiplexer_12_out, multiplexer_13_out, multiplexer_14_out, multiplexer_15_out,
       pull_resistor_1_node, pull_resistor_2_node, pull_resistor_3_node;

  Pull_Resistor pull_resistor_1 (.node(pull_resistor_1_node));
  Multiplexer #(.width(32)) multiplexer_1 (
    .in0(32'h1c3e840), .in1(32'h7e187e44), .out(multiplexer_1_out), .sel(isGameOver));  // open: en
  Multiplexer #(.width(32)) multiplexer_2 (
    .in0(32'h2a088c0), .in1(32'h42184048), .out(multiplexer_2_out), .sel(isGameOver));  // open: en
  Multiplexer #(.width(32)) multiplexer_3 (
    .in0(32'h2a089c0), .in1(32'h42247c60), .out(multiplexer_3_out), .sel(isGameOver));  // open: en
  Multiplexer #(.width(32)) multiplexer_4 (
    .in0(32'h6b08940), .in1(32'h2466407c), .out(multiplexer_4_out), .sel(isGameOver));  // open: en
  Multiplexer #(.width(32)) multiplexer_5 (
    .in0(32'h6b08b40), .in1(32'h42424042), .out(multiplexer_5_out), .sel(isGameOver));  // open: en
  Multiplexer #(.width(32)) multiplexer_6 (
    .in0(32'hc988e40), .in1(32'h42c34042), .out(multiplexer_6_out), .sel(isGameOver));  // open: en
  Multiplexer #(.width(32)) multiplexer_7 (
    .in0(32'hc988c40), .in1(32'h7e817e7c), .out(multiplexer_7_out), .sel(isGameOver));  // open: en
  Multiplexer #(.width(32)) multiplexer_8 (
    .in0(32'h80be840), .in1(pull_resistor_2_node), .out(multiplexer_8_out), .sel(isGameOver));  // open: en
  Pull_Resistor pull_resistor_2 (.node(pull_resistor_2_node));
  Multiplexer #(.width(32)) multiplexer_9 (
    .in0(32'h1f7df00), .in1(32'h7e42817e), .out(multiplexer_9_out), .sel(isGameOver));  // open: en
  Multiplexer #(.width(32)) multiplexer_10 (
    .in0(32'h145100), .in1(32'h42428140), .out(multiplexer_10_out), .sel(isGameOver));  // open: en
  Multiplexer #(.width(32)) multiplexer_11 (
    .in0(32'h145100), .in1(32'h407e817c), .out(multiplexer_11_out), .sel(isGameOver));  // open: en
  Multiplexer #(.width(32)) multiplexer_12 (
    .in0(32'h1f45100), .in1(32'h40429940), .out(multiplexer_12_out), .sel(isGameOver));  // open: en
  Multiplexer #(.width(32)) multiplexer_13 (
    .in0(32'h1145100), .in1(32'h4242bd40), .out(multiplexer_13_out), .sel(isGameOver));  // open: en
  Multiplexer #(.width(32)) multiplexer_14 (
    .in0(32'h1145100), .in1(32'h4242e740), .out(multiplexer_14_out), .sel(isGameOver));  // open: en
  Multiplexer #(.width(32)) multiplexer_15 (
    .in0(32'h117d100), .in1(32'h7e7ec37e), .out(multiplexer_15_out), .sel(isGameOver));  // open: en
  Pull_Resistor pull_resistor_3 (.node(pull_resistor_3_node));
  Decoder #(.select(5), .disabled(0), .enable("false")) decoder_1 (
    .out0(decoder_1_out0), .out1(decoder_1_out1), .out2(decoder_1_out2), .out3(decoder_1_out3),
    .out4(decoder_1_out4), .out5(decoder_1_out5), .out6(decoder_1_out6), .out7(decoder_1_out7),
    .out8(decoder_1_out8), .out9(decoder_1_out9), .out10(decoder_1_out10), .out11(decoder_1_out11),
    .out12(decoder_1_out12), .out13(decoder_1_out13), .out14(decoder_1_out14), .out15(decoder_1_out15),
    .out16(decoder_1_out16), .out17(decoder_1_out17), .out18(decoder_1_out18), .out19(decoder_1_out19),
    .out20(decoder_1_out20), .out21(decoder_1_out21), .out22(decoder_1_out22), .out23(decoder_1_out23),
    .out24(decoder_1_out24), .out25(decoder_1_out25), .out26(decoder_1_out26), .out27(decoder_1_out27),
    .out28(decoder_1_out28), .out29(decoder_1_out29), .out30(decoder_1_out30), .out31(decoder_1_out31),
    .sel(in));
  assign out = decoder_1_out28 ? pull_resistor_3_node : 32'bz;  // Controlled_Buffer controlled_buffer_1
  assign out = decoder_1_out29 ? pull_resistor_3_node : 32'bz;  // Controlled_Buffer controlled_buffer_2
  assign out = decoder_1_out30 ? pull_resistor_3_node : 32'bz;  // Controlled_Buffer controlled_buffer_3
  assign out = decoder_1_out31 ? pull_resistor_3_node : 32'bz;  // Controlled_Buffer controlled_buffer_4
  assign out = decoder_1_out26 ? multiplexer_14_out : 32'bz;  // Controlled_Buffer controlled_buffer_5
  assign out = decoder_1_out27 ? multiplexer_15_out : 32'bz;  // Controlled_Buffer controlled_buffer_6
  assign out = decoder_1_out23 ? multiplexer_11_out : 32'bz;  // Controlled_Buffer controlled_buffer_7
  assign out = decoder_1_out24 ? multiplexer_12_out : 32'bz;  // Controlled_Buffer controlled_buffer_8
  assign out = decoder_1_out25 ? multiplexer_13_out : 32'bz;  // Controlled_Buffer controlled_buffer_9
  assign out = decoder_1_out19 ? pull_resistor_2_node : 32'bz;  // Controlled_Buffer controlled_buffer_10
  assign out = decoder_1_out20 ? pull_resistor_2_node : 32'bz;  // Controlled_Buffer controlled_buffer_11
  assign out = decoder_1_out21 ? multiplexer_9_out : 32'bz;  // Controlled_Buffer controlled_buffer_12
  assign out = decoder_1_out22 ? multiplexer_10_out : 32'bz;  // Controlled_Buffer controlled_buffer_13
  assign out = decoder_1_out15 ? pull_resistor_2_node : 32'bz;  // Controlled_Buffer controlled_buffer_14
  assign out = decoder_1_out16 ? pull_resistor_2_node : 32'bz;  // Controlled_Buffer controlled_buffer_15
  assign out = decoder_1_out17 ? pull_resistor_2_node : 32'bz;  // Controlled_Buffer controlled_buffer_16
  assign out = decoder_1_out18 ? pull_resistor_2_node : 32'bz;  // Controlled_Buffer controlled_buffer_17
  assign out = decoder_1_out12 ? multiplexer_8_out : 32'bz;  // Controlled_Buffer controlled_buffer_18
  assign out = decoder_1_out13 ? pull_resistor_2_node : 32'bz;  // Controlled_Buffer controlled_buffer_19
  assign out = decoder_1_out14 ? pull_resistor_2_node : 32'bz;  // Controlled_Buffer controlled_buffer_20
  assign out = decoder_1_out9 ? multiplexer_5_out : 32'bz;  // Controlled_Buffer controlled_buffer_21
  assign out = decoder_1_out10 ? multiplexer_6_out : 32'bz;  // Controlled_Buffer controlled_buffer_22
  assign out = decoder_1_out11 ? multiplexer_7_out : 32'bz;  // Controlled_Buffer controlled_buffer_23
  assign out = decoder_1_out5 ? multiplexer_1_out : 32'bz;  // Controlled_Buffer controlled_buffer_24
  assign out = decoder_1_out6 ? multiplexer_2_out : 32'bz;  // Controlled_Buffer controlled_buffer_25
  assign out = decoder_1_out7 ? multiplexer_3_out : 32'bz;  // Controlled_Buffer controlled_buffer_26
  assign out = decoder_1_out8 ? multiplexer_4_out : 32'bz;  // Controlled_Buffer controlled_buffer_27
  assign out = decoder_1_out2 ? pull_resistor_1_node : 32'bz;  // Controlled_Buffer controlled_buffer_28
  assign out = decoder_1_out3 ? pull_resistor_1_node : 32'bz;  // Controlled_Buffer controlled_buffer_29
  assign out = decoder_1_out4 ? pull_resistor_1_node : 32'bz;  // Controlled_Buffer controlled_buffer_30
  assign out = decoder_1_out0 ? pull_resistor_1_node : 32'bz;  // Controlled_Buffer controlled_buffer_31
  assign out = decoder_1_out1 ? pull_resistor_1_node : 32'bz;  // Controlled_Buffer controlled_buffer_32
  DotMatrix #(.inputtype("row"), .matrixcols(32), .matrixrows(32)) dotmatrix_1 (
    .row19(32'h7e42817e), .row28(32'h42247c60), .row29(32'h42184048), .row30(32'h7e187e44));  // open: row0, row1, row2, row3, row4, row5, row6, row7, row8, row9, row10, row11, row12, row13, row14, row15, row16, row17, row18, row20, row21, row22, row23, row24, row25, row26, row27, row31
endmodule

module oradd32 (
  input  [31:0] in,
  output out
);

  or or_1 (out, in[0], in[1], in[2], in[3], in[4], in[5], in[6], in[7], in[8], in[9], in[10], in[11], in[12], in[13], in[14], in[15], in[16], in[17], in[18], in[19], in[20], in[21], in[22], in[23], in[24], in[25], in[26], in[27], in[28], in[29], in[30], in[31]);
endmodule

module got1 (
  input  in_1,
  output out_2
);

  wire clock_1_out;

  D_Flip_Flop d_ff_1 (.Q(out_2), .preset(in_1), .reset(clock_1_out));  // open: clk, D, Qn, en
  Clock #(.highDuration(2), .lowDuration(2)) clock_1 (.out(clock_1_out));

  // Notes on the sheet:
  //   У этойсхемы частота в 2 раза меньше, для того чтобы поймать мгновенную единичку
endmodule

module enemies (
  input  clk,
  input  [31:0] in_2,
  input  [31:0] in_3,
  input  [31:0] in_4,
  input  [31:0] in_5,
  input  initgame,
  input  [31:0] in_7,
  input  [31:0] in_8,
  input  [31:0] in_9,
  input  [31:0] in_10,
  input  [31:0] in_11,
  input  [31:0] in_12,
  input  [31:0] in_13,
  input  [31:0] in_14,
  input  [31:0] in_15,
  input  [31:0] in_16,
  input  [4:0] Num,
  input  [31:0] in_18,
  input  [31:0] in_19,
  input  [31:0] in_20,
  input  [31:0] in_21,
  input  [31:0] in_22,
  input  [31:0] in_23,
  input  [31:0] in_24,
  input  [31:0] in_25,
  input  [31:0] in_26,
  input  [31:0] in_27,
  input  [31:0] in_28,
  output [31:0] out_29,
  output [31:0] out_30,
  output [31:0] out_31,
  output [31:0] out_32,
  output [31:0] out_33,
  output [31:0] out_34,
  output [31:0] out_35,
  output [31:0] out_36,
  output [31:0] out_37,
  output [31:0] out_38,
  output [31:0] out_39,
  output [31:0] out_40,
  output [31:0] out_41,
  output [31:0] out_42,
  output [31:0] out_43,
  output [31:0] out_44,
  output [31:0] out_45,
  output [31:0] out_46,
  output [31:0] out_47,
  output [31:0] out_48,
  output [31:0] out_49,
  output [31:0] out_50,
  output [31:0] out_51,
  output [31:0] out_52,
  output boom,
  output [7:0] out,
  output win
);

  wire _1_prime_prime_prime, _2_prime_prime_prime, _3_prime_prime_prime, _4_prime_prime_prime,
       _11_prime_prime_prime, _12_prime_prime_prime, _13_prime_prime_prime, _14_prime_prime_prime, and_2_out,
       and_3_out, and_4_out, cdm_8_mark5_1_data_inst, cdm_8_mark5_1_mem_cycle, clk_t, clock_1_out,
       clock_2_out, clr, comparator_1_eq, comparator_2_lt, comparator_3_eq, controlled_buffer_5_out,
       controlled_buffer_9_out, d_ff_1_q, d_ff_2_q, decoder_1_out0, decoder_1_out1, decoder_3_out0,
       decoder_3_out1, decoder_3_out2, decoder_3_out3, decoder_3_out4, DONE, I_O_sel, init,
       multiplexer_1_out, not_1_out, not_2_out, not_3_out, not_4_out, not_6_out, not_7_out, not_8_out,
       or_1_out, or_2_out, or_3_out, or_4_out, or_5_out, pull_resistor_1_node, r, r_w, register_1_q, w,
       \попадание_1_trigger ;
  wire [2:0] counter_1_q;
  wire [4:0] inc5_1_r;
  wire [7:0] addr, arr0, arr1, arr2, arr3, cdm_8_mark5_1_data_out, cdm_8_mark5_1_ps, cdm_8_mark5_1_r0,
       cdm_8_mark5_1_r1, cdm_8_mark5_1_r2, cdm_8_mark5_1_r3, cdm_8_mark5_1_sp, controlled_buffer_2_out,
       controlled_buffer_6_out, demultiplexer_1_out4, enem, io_data, multiplexer_4_out, Oarr0, Oarr1, Oarr2,
       Oarr3, PC, register_9_q, register_10_q, register_11_q, register_12_q, register_13_q, register_14_q,
       register_15_q, register_16_q, register_17_q, register_18_q, register_19_q, register_20_q,
       register_21_q, register_22_q, register_23_q, register_24_q;
  wire [31:0] _2bul, _3bul, _4bul, _5bul, _6bul, _24bul, multiplexer_2_out, multiplexer_3_out,
       pull_resistor_9_node, register_25_q, register_29_q, register_35_q, register_40_q, \попадание_1_out ;

  and and_1 (I_O_sel, and_3_out, decoder_1_out1);
  and and_2 (and_2_out, boom, ~not_1_out, initgame);  // AND_Gate
  Clock \u_Частота_процессора  (.out(clk_t));
  D_Flip_Flop #(.trigger("falling")) d_ff_1 (
    .Q(d_ff_1_q), .preset(comparator_1_eq), .reset(d_ff_2_q));  // open: clk, D, Qn, en
  Comparator comparator_1 (.a(PC), .b(8'h8), .eq(comparator_1_eq));  // open: gt, lt
  D_Flip_Flop #(.trigger("falling")) d_ff_2 (.clk(clk_t), .D(and_2_out), .Q(d_ff_2_q));  // open: Qn, preset, en, reset
  and and_3 (and_3_out, addr[4], addr[5], addr[6], addr[7], decoder_1_out1);
  // Probe on cdm_8_mark5_1_r1
  // Probe on cdm_8_mark5_1_r3
  // Probe on cdm_8_mark5_1_r0
  // Probe on cdm_8_mark5_1_r2
  Multiplexer #(.enable("false")) multiplexer_1 (.in0(1'b0), .in1(clk_t), .out(multiplexer_1_out), .sel(not_1_out));
  and and_4 (and_4_out, decoder_1_out1, ~and_3_out);  // AND_Gate
  // Probe on cdm_8_mark5_1_sp
  // Probe on cdm_8_mark5_1_ps
  // Probe on PC
  CdM_8_mark5 cdm_8_mark5_1 (
    .clock(multiplexer_1_out), .addr(addr), .mem_read(r_w), .mem_cycle(cdm_8_mark5_1_mem_cycle),
    .data_inst(cdm_8_mark5_1_data_inst), .data_out(cdm_8_mark5_1_data_out),
    .data_in(controlled_buffer_2_out), .r0(cdm_8_mark5_1_r0), .r1(cdm_8_mark5_1_r1), .r2(cdm_8_mark5_1_r2),
    .r3(cdm_8_mark5_1_r3), .PC(PC), .SP(cdm_8_mark5_1_sp), .PS(cdm_8_mark5_1_ps));  // open: IAck, IRQ, vec, reset
  not not_1 (not_1_out, d_ff_1_q);
  Decoder #(.disabled(0)) decoder_1 (
    .out0(decoder_1_out0), .out1(decoder_1_out1), .sel(cdm_8_mark5_1_data_inst), .en(cdm_8_mark5_1_mem_cycle));
  not not_2 (not_2_out, r_w);
  assign io_data = not_2_out ? cdm_8_mark5_1_data_out : 8'bz;  // Controlled_Buffer controlled_buffer_1
  assign controlled_buffer_2_out = r_w ? io_data : 8'bz;  // Controlled_Buffer controlled_buffer_2
  Clock #(.highDuration(10), .lowDuration(10)) clock_1 (.out(clock_1_out));
  // Probe on addr
  Register #(.width(1)) register_1 (.D(pull_resistor_1_node), .Q(register_1_q), .clk(clk));  // open: en, clr
  not not_3 (not_3_out, boom);
  assign init = not_3_out ? clock_1_out : 1'bz;  // Controlled_Buffer controlled_buffer_3
  // Probe on Num
  D_Flip_Flop d_ff_3 (.Q(boom), .preset(register_1_q), .reset(DONE));  // open: clk, D, Qn, en
  Pull_Resistor pull_resistor_1 (.node(pull_resistor_1_node));
  Register #(.width(32)) register_2 (
    .D(\попадание_1_out ), .en(pull_resistor_1_node), .Q({arr3, arr2, arr1, arr0}), .clk(clk));  // open: clr
  RAM ram_1 (.addr(addr), .data(io_data), .sel(and_4_out), .clk(clk_t), .ld(r_w), .clr(clr));
  ROM rom_1 (.addr(addr), .data(io_data), .sel(decoder_1_out0));
  buf buffer_1 (pull_resistor_1_node, controlled_buffer_5_out);
  not not_4 (not_4_out, initgame);
  assign enem = not_4_out ? {8{1'b1}} : 8'bz;  // Controlled_Buffer controlled_buffer_4
  // Probe on io_data
  \попадание  \u_попадание_1  (
    .OUT(\попадание_1_out ), .A(multiplexer_2_out), .B(multiplexer_3_out), .Trigger(\попадание_1_trigger ));
  Comparator #(.width(5), .mode("unsigned")) comparator_2 (
    .a(5'b00011), .b(inc5_1_r), .lt(comparator_2_lt));  // open: gt, eq
  assign controlled_buffer_5_out = comparator_2_lt ? \попадание_1_trigger  : 1'bz;  // Controlled_Buffer controlled_buffer_5
  assign {_1_prime_prime_prime, _2_prime_prime_prime, _3_prime_prime_prime, _4_prime_prime_prime, _11_prime_prime_prime, _12_prime_prime_prime, _13_prime_prime_prime, _14_prime_prime_prime} = ~out;  // NOT_Gate not_5, 8 bits wide
  Decoder decoder_2 (.out0(r), .out1(w), .sel(r_w), .en(I_O_sel));
  Multiplexer #(.select(5), .width(32), .enable("false")) multiplexer_2 (
    .in0({32{1'b0}}), .in1({32{1'b0}}), .in2(_2bul), .in3(_3bul), .in4(_4bul), .in5(_5bul), .in6(_6bul),
    .in7(in_26), .in8(in_27), .in9(in_24), .in10(in_22), .in11(in_20), .in12(in_18), .in13(in_15),
    .in14(in_13), .in15(in_11), .in16(in_9), .in17(in_7), .in18(in_4), .in19(in_2), .in20(in_28),
    .in21(in_25), .in22(in_23), .in23(in_21), .in24(_24bul), .in25(in_16), .in26(in_14), .in27(in_12),
    .in28(in_10), .in29(in_8), .in30(in_5), .in31(in_3), .out(multiplexer_2_out), .sel(Num));
  inc5 inc5_1 (.X(Num), .R(inc5_1_r));  // open: Cout
  Multiplexer #(.select(5), .width(32), .enable("false")) multiplexer_3 (
    .in0({32{1'b0}}), .in1({32{1'b0}}), .in2({32{1'b0}}), .in3({32{1'b0}}), .in4({32{1'b0}}),
    .in5({32{1'b0}}), .in6({32{1'b0}}), .in7({32{1'b0}}), .in8(out_51), .in9(out_49), .in10(out_47),
    .in11(out_45), .in12(out_43), .in13(out_41), .in14(out_39), .in15(out_37), .in16(out_35), .in17(out_33),
    .in18(out_31), .in19(out_29), .in20(out_52), .in21(out_50), .in22(out_48), .in23(out_46), .in24(out_44),
    .in25(out_42), .in26(out_40), .in27(out_38), .in28(out_36), .in29(out_34), .in30(out_32), .in31(out_30),
    .out(multiplexer_3_out), .sel(inc5_1_r));
  Pull_Resistor pull_resistor_2 (.node(r));
  Pull_Resistor pull_resistor_3 (.node(w));
  or or_1 (or_1_out, r, w);
  Decoder #(.select(4)) decoder_3 (
    .out0(decoder_3_out0), .out1(decoder_3_out1), .out2(decoder_3_out2), .out3(decoder_3_out3),
    .out4(decoder_3_out4), .sel(addr[3:0]), .en(or_1_out));  // open: out5, out6, out7, out8, out9, out10, out11, out12, out13, out14, out15
  assign controlled_buffer_6_out = r ? io_data : 8'bz;  // Controlled_Buffer controlled_buffer_6
  Pull_Resistor pull_resistor_4 (.node(decoder_3_out0));
  Pull_Resistor pull_resistor_5 (.node(decoder_3_out1));
  Pull_Resistor pull_resistor_6 (.node(decoder_3_out2));
  Pull_Resistor pull_resistor_7 (.node(decoder_3_out3));
  Demultiplexer #(.select(4), .width(8)) demultiplexer_1 (
    .out4(demultiplexer_1_out4), .in(controlled_buffer_6_out), .sel(addr[3:0]), .en(r));  // open: out0, out1, out2, out3, out5, out6, out7, out8, out9, out10, out11, out12, out13, out14, out15
  Pull_Resistor pull_resistor_8 (.node(decoder_3_out4));
  assign enem = r ? demultiplexer_1_out4 : 8'bz;  // Controlled_Buffer controlled_buffer_7
  assign io_data = w ? multiplexer_4_out : 8'bz;  // Controlled_Buffer controlled_buffer_8
  Multiplexer #(.select(4), .width(8)) multiplexer_4 (
    .in0(Oarr0), .in1(Oarr1), .in2(Oarr2), .in3(Oarr3), .in4(out), .out(multiplexer_4_out), .sel(addr[3:0]),
    .en(w));  // open: in5, in6, in7, in8, in9, in10, in11, in12, in13, in14, in15
  or or_2 (or_2_out, decoder_3_out0, boom);
  or or_3 (or_3_out, decoder_3_out1, boom);
  or or_4 (or_4_out, decoder_3_out2, boom);
  or or_5 (or_5_out, decoder_3_out3, boom);
  Counter #(.width(3), .max('h2)) counter_1 (
    .count(decoder_3_out4), .Q(counter_1_q), .clk(decoder_3_out4), .clr(not_6_out));  // open: load, D, carry
  not not_6 (not_6_out, boom);
  Register register_3 (.D(arr0), .en(or_2_out), .Q(Oarr0), .clk(clk_t));  // open: clr
  Register register_4 (.D(arr1), .en(or_3_out), .Q(Oarr1), .clk(clk_t));  // open: clr
  Register register_5 (.D(arr2), .en(or_4_out), .Q(Oarr2), .clk(clk_t));  // open: clr
  Register register_6 (.D(arr3), .en(or_5_out), .Q(Oarr3), .clk(clk_t));  // open: clr
  Register register_7 (.D(enem), .en(decoder_3_out4), .Q(out), .clk(clk_t));  // open: clr
  Comparator #(.width(3), .mode("unsigned")) comparator_3 (
    .a(counter_1_q), .b(3'b010), .eq(comparator_3_eq));  // open: gt, lt
  Comparator comparator_4 (.a(out), .b({8{1'b0}}), .eq(win));  // open: gt, lt
  Register #(.width(1)) register_8 (.D(comparator_3_eq), .Q(DONE), .clk(comparator_3_eq), .clr(not_7_out));  // open: en
  not not_7 (not_7_out, boom);
  Register register_9 (.D(8'h18), .en(init), .Q(register_9_q), .clk(init), .clr(_1_prime_prime_prime));
  Register register_10 (.D(8'h18), .en(init), .Q(register_10_q), .clk(init), .clr(_11_prime_prime_prime));
  Register register_11 (.D(8'h18), .en(init), .Q(register_11_q), .clk(init), .clr(_2_prime_prime_prime));
  Register register_12 (.D(8'h18), .en(init), .Q(register_12_q), .clk(init), .clr(_3_prime_prime_prime));
  Register register_13 (.D(8'h18), .en(init), .Q(register_13_q), .clk(init), .clr(_12_prime_prime_prime));
  Register register_14 (.D(8'h18), .en(init), .Q(register_14_q), .clk(init), .clr(_13_prime_prime_prime));
  Register register_15 (.D(8'h24), .en(init), .Q(register_15_q), .clk(init), .clr(_4_prime_prime_prime));
  Register register_16 (.D(8'h24), .en(init), .Q(register_16_q), .clk(init), .clr(_3_prime_prime_prime));
  Register register_17 (.D(8'h24), .en(init), .Q(register_17_q), .clk(init), .clr(_2_prime_prime_prime));
  Register register_18 (.D(8'h24), .en(init), .Q(register_18_q), .clk(init), .clr(_1_prime_prime_prime));
  Register register_19 (.D(8'h18), .en(init), .Q(register_19_q), .clk(init), .clr(_4_prime_prime_prime));
  Register register_20 (.D(8'h18), .en(init), .Q(register_20_q), .clk(init), .clr(_14_prime_prime_prime));
  Register register_21 (.D(8'h24), .en(init), .Q(register_21_q), .clk(init), .clr(_14_prime_prime_prime));
  Register register_22 (.D(8'h24), .en(init), .Q(register_22_q), .clk(init), .clr(_13_prime_prime_prime));
  Register register_23 (.D(8'h24), .en(init), .Q(register_23_q), .clk(init), .clr(_12_prime_prime_prime));
  Register register_24 (.D(8'h24), .en(init), .Q(register_24_q), .clk(init), .clr(_11_prime_prime_prime));
  Register register_25 (.D(8'h5a), .en(init), .Q(register_25_q[7:0]), .clk(init), .clr(_14_prime_prime_prime));
  Register register_26 (.D(8'h24), .en(init), .Q(register_25_q[15:8]), .clk(init), .clr(_13_prime_prime_prime));
  Register register_27 (.D(8'h24), .en(init), .Q(register_25_q[23:16]), .clk(init), .clr(_12_prime_prime_prime));
  Register register_28 (.D(8'h5a), .en(init), .Q(register_25_q[31:24]), .clk(init), .clr(_11_prime_prime_prime));
  Register register_29 (.D(8'h5a), .en(init), .Q(register_29_q[7:0]), .clk(init), .clr(_4_prime_prime_prime));
  Register register_30 (.D(8'h24), .en(init), .Q(register_29_q[15:8]), .clk(init), .clr(_3_prime_prime_prime));
  Register register_31 (.D(8'h24), .en(init), .Q(register_29_q[23:16]), .clk(init), .clr(_2_prime_prime_prime));
  Register register_32 (.D(8'h5a), .en(init), .Q(register_29_q[31:24]), .clk(init), .clr(_1_prime_prime_prime));
  Clock #(.highDuration(70), .lowDuration(70)) clock_2 (.out(clock_2_out));
  not not_8 (not_8_out, boom);
  assign controlled_buffer_9_out = not_8_out ? clock_2_out : 1'bz;  // Controlled_Buffer controlled_buffer_9
  Register register_33 (.D(8'h24), .en(init), .Q(register_35_q[7:0]), .clk(init), .clr(_14_prime_prime_prime));
  Register register_34 (.D(8'h18), .en(init), .Q(register_35_q[15:8]), .clk(init), .clr(_13_prime_prime_prime));
  Register register_35 (.D(8'h18), .en(init), .Q(register_35_q[23:16]), .clk(init), .clr(_12_prime_prime_prime));
  Register register_36 (.D(8'h24), .en(init), .Q(register_35_q[31:24]), .clk(init), .clr(_11_prime_prime_prime));
  Register register_37 (.D(8'h24), .en(init), .Q(register_40_q[7:0]), .clk(init), .clr(_4_prime_prime_prime));
  Register register_38 (.D(8'h18), .en(init), .Q(register_40_q[15:8]), .clk(init), .clr(_3_prime_prime_prime));
  Register register_39 (.D(8'h18), .en(init), .Q(register_40_q[23:16]), .clk(init), .clr(_2_prime_prime_prime));
  Register register_40 (.D(8'h24), .en(init), .Q(register_40_q[31:24]), .clk(init), .clr(_1_prime_prime_prime));
  Pull_Resistor pull_resistor_9 (.node(pull_resistor_9_node));
  \сдвиги  \u_сдвиги_1  (
    .\Очистка (initgame), .\Выход_16 (out_35), .out_21(out_33), .out_22(out_31), .out_23(out_29),
    .out_24(out_52), .out_25(out_50), .out_26(out_48), .out_27(out_46), .out_28(out_44), .out_29(out_42),
    .out_30(out_40), .out_31(out_38), .out_32(out_36), .out_33(out_34), .out_34(out_32), .out_35(out_30),
    .\Вход_0 (register_40_q), .in_2(register_29_q),
    .in_3({register_9_q, register_11_q, register_12_q, register_19_q}),
    .in_4({register_18_q, register_17_q, register_16_q, register_15_q}), .in_5(pull_resistor_9_node),
    .in_7(register_35_q), .in_8(register_25_q),
    .in_10({register_10_q, register_13_q, register_14_q, register_20_q}),
    .in_11({register_24_q, register_23_q, register_22_q, register_21_q}), .clock(controlled_buffer_9_out),
    .out_12(out_51), .out_13(out_49), .out_14(out_47), .out_15(out_45), .out_16(out_43), .out_17(out_41),
    .out_18(out_39), .out_19(out_37));

  // Other names for the same wires on the sheet: _7bul[31:0] = in_26; _8bul[31:0] = in_27; _8e[31:0] = out_51;
  //   _9bul[31:0] = in_24; _9e[31:0] = out_49; _10bul[31:0] = in_22; _10e[31:0] = out_47; _11bul[31:0] = in_20;
  //   _11e[31:0] = out_45; _12bul[31:0] = in_18; _12e[31:0] = out_43; _13bul[31:0] = in_15; _13e[31:0] = out_41;
  //   _14bul[31:0] = in_13; _14e[31:0] = out_39; _15bul[31:0] = in_11; _15e[31:0] = out_37; _16bul[31:0] = in_9;
  //   _16e[31:0] = out_35; _17bul[31:0] = in_7; _17e[31:0] = out_33; _18bul[31:0] = in_4; _18e[31:0] = out_31;
  //   _19bul[31:0] = in_2; _19e[31:0] = out_29; _20bul[31:0] = in_28; _20e[31:0] = out_52; _21bul[31:0] = in_25;
  //   _21e[31:0] = out_50; _22bul[31:0] = in_23; _22e[31:0] = out_48; _23bul[31:0] = in_21; _23e[31:0] = out_46;
  //   _24e[31:0] = out_44; _25bul[31:0] = in_16; _25e[31:0] = out_42; _26bul[31:0] = in_14; _26e[31:0] = out_40;
  //   _27bul[31:0] = in_12; _27e[31:0] = out_38; _28bul[31:0] = in_10; _28e[31:0] = out_36; _29bul[31:0] = in_8;
  //   _29e[31:0] = out_34; _30bul[31:0] = in_5; _30e[31:0] = out_32; _31bul[31:0] = in_3; _31e[31:0] = out_30;
  //   IOaddr[3:0] = addr[3:0]; gen = clk; Oenem[7:0] = out; StartGame = initgame

  // Notes on the sheet:
  //   Сохранение строки для кода
  //   contents of rom_1 (hex, n*v repeats v):
  //   c0 c4 c0 d1 ff d2 f4 a9 c4 d1 f0 d0 0 d2 3 7 a eb 1e bd 5 e0 19 ee 1e 8f 8c 8a ee 10 d1 1 d2 f4 ba 0
  //   e0 2a 25 88 ee 23 7 4b f e1 38 d0 4 0 e0 38 25 88 ee 31 66 d0 f4 a2 a e0 41 d6 8 d6 1 173*0 1 0 0 4
  //   ff
  //   buffer_1 drives only 1 and floats otherwise
  //   запись в регитсры (st)
  //   чтение из регитров (ld)
  //   Указывает, завершилась ли обработка попадания
endmodule

module \сдвиги  (
  input  [31:0] \Вход_0 ,
  input  [31:0] in_2,
  input  [31:0] in_3,
  input  [31:0] in_4,
  input  [31:0] in_5,
  input  clock,
  input  [31:0] in_7,
  input  [31:0] in_8,
  input  \Очистка ,
  input  [31:0] in_10,
  input  [31:0] in_11,
  output [31:0] out_12,
  output [31:0] out_13,
  output [31:0] out_14,
  output [31:0] out_15,
  output [31:0] out_16,
  output [31:0] out_17,
  output [31:0] out_18,
  output [31:0] out_19,
  output [31:0] \Выход_16 ,
  output [31:0] out_21,
  output [31:0] out_22,
  output [31:0] out_23,
  output [31:0] out_24,
  output [31:0] out_25,
  output [31:0] out_26,
  output [31:0] out_27,
  output [31:0] out_28,
  output [31:0] out_29,
  output [31:0] out_30,
  output [31:0] out_31,
  output [31:0] out_32,
  output [31:0] out_33,
  output [31:0] out_34,
  output [31:0] out_35
);

  wire and_1_out, comparator_1_eq, comparator_2_eq, comparator_3_eq, comparator_4_eq, comparator_5_eq,
       comparator_6_eq, L, or_1_out, or_2_out, or_3_out, R, START;
  wire [2:0] counter_1_q;
  wire [4:0] Heght;
  wire [31:0] pull_resistor_1_node, shifterdown_1_out_28, shifterdown_1_out_29, shifterdown_1_out_30,
       shifterdown_1_out_31, shifterdown_1_out_32, shifterdown_1_out_33, shifterdown_1_out_34,
       shifterdown_1_out_35, shifterdown_1_out_36, shifterdown_1_out_37, shifterdown_1_out_38,
       shifterdown_1_out_39, shifterdown_1_out_40, shifterdown_1_out_41, shifterdown_1_out_42,
       shifterdown_1_out_43, shifterdown_1_out_44, shifterdown_1_out_45, shifterdown_1_out_46,
       shifterdown_1_out_47, shifterdown_1_out_48, shifterdown_1_out_49, shifterdown_1_out_50,
       \shifterdown_1_выход_0 ;

  Counter #(.width(3), .max('h5)) counter_1 (.Q(counter_1_q), .clk(clock), .clr(START));  // open: load, D, count, carry
  Comparator #(.width(3)) comparator_1 (.a(counter_1_q), .b(3'b010), .eq(comparator_1_eq));  // open: gt, lt
  Comparator #(.width(3)) comparator_2 (.a(counter_1_q), .b(3'b101), .eq(comparator_2_eq));  // open: gt, lt
  Comparator #(.width(3)) comparator_3 (.a(counter_1_q), .b(3'b001), .eq(comparator_3_eq));  // open: gt, lt
  Comparator #(.width(3)) comparator_4 (.a(counter_1_q), .b(3'b011), .eq(comparator_4_eq));  // open: gt, lt
  Comparator #(.width(3)) comparator_5 (.a(counter_1_q), .b(3'b100), .eq(comparator_5_eq));  // open: gt, lt
  Comparator #(.width(3)) comparator_6 (.a(counter_1_q), .b(3'b000), .eq(comparator_6_eq));  // open: gt, lt
  Counter #(.width(5), .max('h17)) counter_2 (.Q(Heght), .clk(or_1_out), .clr(START));  // open: load, D, count, carry
  or or_1 (or_1_out, comparator_1_eq, comparator_2_eq);
  Counter #(.width(1), .max('h1)) counter_3 (.Q(L), .clk(or_2_out), .clr(START));  // open: load, D, count, carry
  or or_2 (or_2_out, comparator_3_eq, comparator_4_eq);
  Counter #(.width(1), .max('h1)) counter_4 (.Q(R), .clk(or_3_out), .clr(START));  // open: load, D, count, carry
  or or_3 (or_3_out, comparator_5_eq, comparator_6_eq);
  not not_1 (START, \Очистка );
  and and_1 (and_1_out, ~L, ~R);  // AND_Gate
  assign out_12 = and_1_out ? shifterdown_1_out_50 : 32'bz;  // Controlled_Buffer controlled_buffer_1
  assign out_13 = and_1_out ? shifterdown_1_out_49 : 32'bz;  // Controlled_Buffer controlled_buffer_2
  assign out_17 = and_1_out ? shifterdown_1_out_45 : 32'bz;  // Controlled_Buffer controlled_buffer_3
  assign out_15 = and_1_out ? shifterdown_1_out_47 : 32'bz;  // Controlled_Buffer controlled_buffer_4
  assign out_16 = and_1_out ? shifterdown_1_out_46 : 32'bz;  // Controlled_Buffer controlled_buffer_5
  assign out_14 = and_1_out ? shifterdown_1_out_48 : 32'bz;  // Controlled_Buffer controlled_buffer_6
  Pull_Resistor pull_resistor_1 (.node(pull_resistor_1_node));
  assign out_19 = and_1_out ? shifterdown_1_out_43 : 32'bz;  // Controlled_Buffer controlled_buffer_7
  assign \Выход_16  = and_1_out ? shifterdown_1_out_42 : 32'bz;  // Controlled_Buffer controlled_buffer_8
  assign out_24 = and_1_out ? shifterdown_1_out_38 : 32'bz;  // Controlled_Buffer controlled_buffer_9
  assign out_21 = and_1_out ? shifterdown_1_out_41 : 32'bz;  // Controlled_Buffer controlled_buffer_10
  assign out_23 = and_1_out ? shifterdown_1_out_39 : 32'bz;  // Controlled_Buffer controlled_buffer_11
  assign out_18 = and_1_out ? shifterdown_1_out_44 : 32'bz;  // Controlled_Buffer controlled_buffer_12
  assign out_22 = and_1_out ? shifterdown_1_out_40 : 32'bz;  // Controlled_Buffer controlled_buffer_13
  assign out_25 = and_1_out ? shifterdown_1_out_37 : 32'bz;  // Controlled_Buffer controlled_buffer_14
  assign out_33 = and_1_out ? shifterdown_1_out_29 : 32'bz;  // Controlled_Buffer controlled_buffer_15
  assign out_27 = and_1_out ? shifterdown_1_out_35 : 32'bz;  // Controlled_Buffer controlled_buffer_16
  assign out_32 = and_1_out ? shifterdown_1_out_30 : 32'bz;  // Controlled_Buffer controlled_buffer_17
  assign out_31 = and_1_out ? shifterdown_1_out_31 : 32'bz;  // Controlled_Buffer controlled_buffer_18
  assign out_26 = and_1_out ? shifterdown_1_out_36 : 32'bz;  // Controlled_Buffer controlled_buffer_19
  assign out_28 = and_1_out ? shifterdown_1_out_34 : 32'bz;  // Controlled_Buffer controlled_buffer_20
  assign out_29 = and_1_out ? shifterdown_1_out_33 : 32'bz;  // Controlled_Buffer controlled_buffer_21
  assign out_30 = and_1_out ? shifterdown_1_out_32 : 32'bz;  // Controlled_Buffer controlled_buffer_22
  shifterDown shifterdown_1 (
    .\Вход_0 (\Вход_0 ), .\Выход_0 (\shifterdown_1_выход_0 ), .in_2(in_2), .out_28(shifterdown_1_out_28),
    .in_3(Heght), .in_4(in_3), .out_29(shifterdown_1_out_29), .in_6(in_4), .out_30(shifterdown_1_out_30),
    .in_7(in_5), .out_31(shifterdown_1_out_31), .in_8(in_7), .out_32(shifterdown_1_out_32), .in_9(in_8),
    .out_33(shifterdown_1_out_33), .in_10(in_10), .out_34(shifterdown_1_out_34), .in_11(in_11),
    .out_35(shifterdown_1_out_35), .in_12(pull_resistor_1_node), .out_36(shifterdown_1_out_36),
    .in_13(pull_resistor_1_node), .out_37(shifterdown_1_out_37), .in_14(pull_resistor_1_node),
    .out_38(shifterdown_1_out_38), .in_15(pull_resistor_1_node), .out_39(shifterdown_1_out_39),
    .in_16(pull_resistor_1_node), .out_40(shifterdown_1_out_40), .in_17(pull_resistor_1_node),
    .out_41(shifterdown_1_out_41), .in_18(pull_resistor_1_node), .out_42(shifterdown_1_out_42),
    .En(\Очистка ), .in_19(pull_resistor_1_node), .out_43(shifterdown_1_out_43),
    .in_20(pull_resistor_1_node), .out_44(shifterdown_1_out_44), .in_21(pull_resistor_1_node),
    .out_45(shifterdown_1_out_45), .in_22(pull_resistor_1_node), .out_46(shifterdown_1_out_46),
    .in_23(pull_resistor_1_node), .out_47(shifterdown_1_out_47), .in_24(pull_resistor_1_node),
    .out_48(shifterdown_1_out_48), .in_25(pull_resistor_1_node), .out_49(shifterdown_1_out_49),
    .in_26(pull_resistor_1_node), .out_50(shifterdown_1_out_50));
  ShifterLeft shifterleft_1 (
    .\Вход_0 (\shifterdown_1_выход_0 ), .out_26(out_35), .in_2(shifterdown_1_out_28), .out_27(out_34),
    .in_3(shifterdown_1_out_29), .out_28(out_33), .in_4(shifterdown_1_out_30), .out_29(out_32),
    .in_5(shifterdown_1_out_31), .out_30(out_31), .in_6(shifterdown_1_out_32), .out_31(out_30),
    .in_7(shifterdown_1_out_33), .out_32(out_29), .in_8(shifterdown_1_out_34), .out_33(out_28),
    .in_9(shifterdown_1_out_35), .out_34(out_27), .in_10(shifterdown_1_out_36), .out_35(out_26),
    .in_11(shifterdown_1_out_37), .out_36(out_25), .in_12(shifterdown_1_out_38), .out_37(out_24),
    .in_13(shifterdown_1_out_39), .out_38(out_23), .in_14(shifterdown_1_out_40), .out_39(out_22),
    .in_15(shifterdown_1_out_41), .out_40(out_21), .in_16(shifterdown_1_out_42), .out_41(\Выход_16 ),
    .in_17(shifterdown_1_out_43), .out_42(out_19), .in_18(shifterdown_1_out_44), .out_43(out_18),
    .in_19(shifterdown_1_out_45), .out_44(out_17), .in_20(shifterdown_1_out_46), .out_45(out_16),
    .in_21(shifterdown_1_out_47), .out_46(out_15), .in_22(shifterdown_1_out_48), .out_47(out_14),
    .in_23(shifterdown_1_out_49), .out_48(out_13), .in_24(shifterdown_1_out_50), .out_49(out_12), .in_25(L));
  ShifterRight shifterright_1 (
    .\Вход_0 (\shifterdown_1_выход_0 ), .out_26(out_35), .in_2(shifterdown_1_out_28), .out_27(out_34),
    .in_3(shifterdown_1_out_29), .out_28(out_33), .in_4(shifterdown_1_out_30), .out_29(out_32),
    .in_5(shifterdown_1_out_31), .out_30(out_31), .in_6(shifterdown_1_out_32), .out_31(out_30),
    .in_7(shifterdown_1_out_33), .out_32(out_29), .in_8(shifterdown_1_out_34), .out_33(out_28),
    .in_9(shifterdown_1_out_35), .out_34(out_27), .in_10(shifterdown_1_out_36), .out_35(out_26),
    .in_11(shifterdown_1_out_37), .out_36(out_25), .in_12(shifterdown_1_out_38), .out_37(out_24),
    .in_13(shifterdown_1_out_39), .out_38(out_23), .in_14(shifterdown_1_out_40), .out_39(out_22),
    .in_15(shifterdown_1_out_41), .out_40(out_21), .in_16(shifterdown_1_out_42), .out_41(\Выход_16 ),
    .in_17(shifterdown_1_out_43), .out_42(out_19), .in_18(shifterdown_1_out_44), .out_43(out_18),
    .in_19(shifterdown_1_out_45), .out_44(out_17), .in_20(shifterdown_1_out_46), .out_45(out_16),
    .in_21(shifterdown_1_out_47), .out_46(out_15), .in_22(shifterdown_1_out_48), .out_47(out_14),
    .in_24(shifterdown_1_out_49), .out_49(out_13), .in_25(R), .in_23(shifterdown_1_out_50), .out_48(out_12));
  assign out_34 = and_1_out ? shifterdown_1_out_28 : 32'bz;  // Controlled_Buffer controlled_buffer_23
  assign out_35 = and_1_out ? \shifterdown_1_выход_0  : 32'bz;  // Controlled_Buffer controlled_buffer_24

  // Other names for the same wires on the sheet: _8e[31:0] = out_12; _9e[31:0] = out_13; _10e[31:0] = out_14;
  //   _11e[31:0] = out_15; _12e[31:0] = out_16; _13e[31:0] = out_17; _14e[31:0] = out_18; _15e[31:0] = out_19;
  //   _16e[31:0] = \Выход_16 ; _17e[31:0] = out_21; _18e[31:0] = out_22; _19e[31:0] = out_23; _20e[31:0] = out_24;
  //   _21e[31:0] = out_25; _22e[31:0] = out_26; _23e[31:0] = out_27; _24e[31:0] = out_28; _25e[31:0] = out_29;
  //   _26e[31:0] = out_30; _27e[31:0] = out_31; _28e[31:0] = out_32; _29e[31:0] = out_33; _30e[31:0] = out_34;
  //   _31e[31:0] = out_35; En = \Очистка 

  // Notes on the sheet:
  //   V
  //   >
  //   <
endmodule
module shifterDown (
  input  [31:0] \Вход_0 ,
  input  [31:0] in_2,
  input  [4:0] in_3,
  input  [31:0] in_4,
  input  En,
  input  [31:0] in_6,
  input  [31:0] in_7,
  input  [31:0] in_8,
  input  [31:0] in_9,
  input  [31:0] in_10,
  input  [31:0] in_11,
  input  [31:0] in_12,
  input  [31:0] in_13,
  input  [31:0] in_14,
  input  [31:0] in_15,
  input  [31:0] in_16,
  input  [31:0] in_17,
  input  [31:0] in_18,
  input  [31:0] in_19,
  input  [31:0] in_20,
  input  [31:0] in_21,
  input  [31:0] in_22,
  input  [31:0] in_23,
  input  [31:0] in_24,
  input  [31:0] in_25,
  input  [31:0] in_26,
  output [31:0] \Выход_0 ,
  output [31:0] out_28,
  output [31:0] out_29,
  output [31:0] out_30,
  output [31:0] out_31,
  output [31:0] out_32,
  output [31:0] out_33,
  output [31:0] out_34,
  output [31:0] out_35,
  output [31:0] out_36,
  output [31:0] out_37,
  output [31:0] out_38,
  output [31:0] out_39,
  output [31:0] out_40,
  output [31:0] out_41,
  output [31:0] out_42,
  output [31:0] out_43,
  output [31:0] out_44,
  output [31:0] out_45,
  output [31:0] out_46,
  output [31:0] out_47,
  output [31:0] out_48,
  output [31:0] out_49,
  output [31:0] out_50
);

  wire not_1_out;
  wire [4:0] controlled_buffer_1_out, inc5_1_r, inc5_2_r, inc5_3_r, inc5_4_r, inc5_5_r, inc5_6_r, inc5_7_r,
       inc5_8_r, inc5_9_r, inc5_10_r, inc5_11_r, inc5_12_r, inc5_13_r, inc5_14_r, inc5_15_r, inc5_16_r,
       inc5_17_r, inc5_18_r, inc5_19_r, inc5_20_r, inc5_21_r, inc5_22_r, inc5_23_r;
  wire [31:0] demultiplexer_1_out0, demultiplexer_1_out1, demultiplexer_1_out2, demultiplexer_1_out3,
       demultiplexer_1_out4, demultiplexer_1_out5, demultiplexer_1_out6, demultiplexer_1_out7,
       demultiplexer_1_out8, demultiplexer_1_out9, demultiplexer_1_out10, demultiplexer_1_out11,
       demultiplexer_1_out12, demultiplexer_1_out13, demultiplexer_1_out14, demultiplexer_1_out15,
       demultiplexer_1_out16, demultiplexer_1_out17, demultiplexer_1_out18, demultiplexer_1_out19,
       demultiplexer_1_out20, demultiplexer_1_out21, demultiplexer_1_out22, demultiplexer_1_out23,
       demultiplexer_2_out4, demultiplexer_2_out5, demultiplexer_2_out6, demultiplexer_2_out7,
       demultiplexer_2_out8, demultiplexer_2_out9, demultiplexer_2_out10, demultiplexer_2_out11,
       demultiplexer_2_out12, demultiplexer_2_out13, demultiplexer_2_out14, demultiplexer_2_out15,
       demultiplexer_2_out16, demultiplexer_2_out17, demultiplexer_2_out18, demultiplexer_2_out19,
       demultiplexer_2_out20, demultiplexer_2_out21, demultiplexer_2_out22, demultiplexer_2_out23,
       demultiplexer_3_out8, demultiplexer_3_out9, demultiplexer_3_out10, demultiplexer_3_out11,
       demultiplexer_3_out12, demultiplexer_3_out13, demultiplexer_3_out14, demultiplexer_3_out15,
       demultiplexer_3_out16, demultiplexer_3_out17, demultiplexer_3_out18, demultiplexer_3_out19,
       demultiplexer_3_out20, demultiplexer_3_out21, demultiplexer_3_out22, demultiplexer_3_out23,
       demultiplexer_4_out12, demultiplexer_4_out13, demultiplexer_4_out14, demultiplexer_4_out15,
       demultiplexer_4_out16, demultiplexer_4_out17, demultiplexer_4_out18, demultiplexer_4_out19,
       demultiplexer_4_out20, demultiplexer_4_out21, demultiplexer_4_out22, demultiplexer_4_out23,
       demultiplexer_5_out16, demultiplexer_5_out17, demultiplexer_5_out18, demultiplexer_5_out19,
       demultiplexer_5_out20, demultiplexer_5_out21, demultiplexer_5_out22, demultiplexer_5_out23,
       demultiplexer_6_out20, demultiplexer_6_out21, demultiplexer_6_out22, demultiplexer_6_out23,
       demultiplexer_7_out1, demultiplexer_7_out2, demultiplexer_7_out3, demultiplexer_7_out4,
       demultiplexer_7_out5, demultiplexer_7_out6, demultiplexer_7_out7, demultiplexer_7_out8,
       demultiplexer_7_out9, demultiplexer_7_out10, demultiplexer_7_out11, demultiplexer_7_out12,
       demultiplexer_7_out13, demultiplexer_7_out14, demultiplexer_7_out15, demultiplexer_7_out16,
       demultiplexer_7_out17, demultiplexer_7_out18, demultiplexer_7_out19, demultiplexer_7_out20,
       demultiplexer_7_out21, demultiplexer_7_out22, demultiplexer_7_out23, demultiplexer_8_out5,
       demultiplexer_8_out6, demultiplexer_8_out7, demultiplexer_8_out8, demultiplexer_8_out9,
       demultiplexer_8_out10, demultiplexer_8_out11, demultiplexer_8_out12, demultiplexer_8_out13,
       demultiplexer_8_out14, demultiplexer_8_out15, demultiplexer_8_out16, demultiplexer_8_out17,
       demultiplexer_8_out18, demultiplexer_8_out19, demultiplexer_8_out20, demultiplexer_8_out21,
       demultiplexer_8_out22, demultiplexer_8_out23, demultiplexer_9_out9, demultiplexer_9_out10,
       demultiplexer_9_out11, demultiplexer_9_out12, demultiplexer_9_out13, demultiplexer_9_out14,
       demultiplexer_9_out15, demultiplexer_9_out16, demultiplexer_9_out17, demultiplexer_9_out18,
       demultiplexer_9_out19, demultiplexer_9_out20, demultiplexer_9_out21, demultiplexer_9_out22,
       demultiplexer_9_out23, demultiplexer_10_out13, demultiplexer_10_out14, demultiplexer_10_out15,
       demultiplexer_10_out16, demultiplexer_10_out17, demultiplexer_10_out18, demultiplexer_10_out19,
       demultiplexer_10_out20, demultiplexer_10_out21, demultiplexer_10_out22, demultiplexer_10_out23,
       demultiplexer_11_out17, demultiplexer_11_out18, demultiplexer_11_out19, demultiplexer_11_out20,
       demultiplexer_11_out21, demultiplexer_11_out22, demultiplexer_11_out23, demultiplexer_12_out21,
       demultiplexer_12_out22, demultiplexer_12_out23, demultiplexer_13_out2, demultiplexer_13_out3,
       demultiplexer_13_out4, demultiplexer_13_out5, demultiplexer_13_out6, demultiplexer_13_out7,
       demultiplexer_13_out8, demultiplexer_13_out9, demultiplexer_13_out10, demultiplexer_13_out11,
       demultiplexer_13_out12, demultiplexer_13_out13, demultiplexer_13_out14, demultiplexer_13_out15,
       demultiplexer_13_out16, demultiplexer_13_out17, demultiplexer_13_out18, demultiplexer_13_out19,
       demultiplexer_13_out20, demultiplexer_13_out21, demultiplexer_13_out22, demultiplexer_13_out23,
       demultiplexer_14_out6, demultiplexer_14_out7, demultiplexer_14_out8, demultiplexer_14_out9,
       demultiplexer_14_out10, demultiplexer_14_out11, demultiplexer_14_out12, demultiplexer_14_out13,
       demultiplexer_14_out14, demultiplexer_14_out15, demultiplexer_14_out16, demultiplexer_14_out17,
       demultiplexer_14_out18, demultiplexer_14_out19, demultiplexer_14_out20, demultiplexer_14_out21,
       demultiplexer_14_out22, demultiplexer_14_out23, demultiplexer_15_out14, demultiplexer_15_out15,
       demultiplexer_15_out16, demultiplexer_15_out17, demultiplexer_15_out18, demultiplexer_15_out19,
       demultiplexer_15_out20, demultiplexer_15_out21, demultiplexer_15_out22, demultiplexer_15_out23,
       demultiplexer_16_out18, demultiplexer_16_out19, demultiplexer_16_out20, demultiplexer_16_out21,
       demultiplexer_16_out22, demultiplexer_16_out23, demultiplexer_17_out22, demultiplexer_17_out23,
       demultiplexer_18_out10, demultiplexer_18_out11, demultiplexer_18_out12, demultiplexer_18_out13,
       demultiplexer_18_out14, demultiplexer_18_out15, demultiplexer_18_out16, demultiplexer_18_out17,
       demultiplexer_18_out18, demultiplexer_18_out19, demultiplexer_18_out20, demultiplexer_18_out21,
       demultiplexer_18_out22, demultiplexer_18_out23, demultiplexer_19_out3, demultiplexer_19_out4,
       demultiplexer_19_out5, demultiplexer_19_out6, demultiplexer_19_out7, demultiplexer_19_out8,
       demultiplexer_19_out9, demultiplexer_19_out10, demultiplexer_19_out11, demultiplexer_19_out12,
       demultiplexer_19_out13, demultiplexer_19_out14, demultiplexer_19_out15, demultiplexer_19_out16,
       demultiplexer_19_out17, demultiplexer_19_out18, demultiplexer_19_out19, demultiplexer_19_out20,
       demultiplexer_19_out21, demultiplexer_19_out22, demultiplexer_19_out23, demultiplexer_20_out7,
       demultiplexer_20_out8, demultiplexer_20_out9, demultiplexer_20_out10, demultiplexer_20_out11,
       demultiplexer_20_out12, demultiplexer_20_out13, demultiplexer_20_out14, demultiplexer_20_out15,
       demultiplexer_20_out16, demultiplexer_20_out17, demultiplexer_20_out18, demultiplexer_20_out19,
       demultiplexer_20_out20, demultiplexer_20_out21, demultiplexer_20_out22, demultiplexer_20_out23,
       demultiplexer_21_out11, demultiplexer_21_out12, demultiplexer_21_out13, demultiplexer_21_out14,
       demultiplexer_21_out15, demultiplexer_21_out16, demultiplexer_21_out17, demultiplexer_21_out18,
       demultiplexer_21_out19, demultiplexer_21_out20, demultiplexer_21_out21, demultiplexer_21_out22,
       demultiplexer_21_out23, demultiplexer_22_out15, demultiplexer_22_out16, demultiplexer_22_out17,
       demultiplexer_22_out18, demultiplexer_22_out19, demultiplexer_22_out20, demultiplexer_22_out21,
       demultiplexer_22_out22, demultiplexer_22_out23, demultiplexer_23_out19, demultiplexer_23_out20,
       demultiplexer_23_out21, demultiplexer_23_out22, demultiplexer_23_out23, demultiplexer_24_out22;

  Pull_Resistor pull_resistor_1 (.node(\Выход_0 ));
  Pull_Resistor pull_resistor_2 (.node(out_28));
  Pull_Resistor pull_resistor_3 (.node(out_29));
  Pull_Resistor pull_resistor_4 (.node(out_30));
  Pull_Resistor pull_resistor_5 (.node(out_31));
  Pull_Resistor pull_resistor_6 (.node(out_32));
  Pull_Resistor pull_resistor_7 (.node(out_33));
  Pull_Resistor pull_resistor_8 (.node(out_34));
  Pull_Resistor pull_resistor_9 (.node(out_35));
  Pull_Resistor pull_resistor_10 (.node(out_36));
  Pull_Resistor pull_resistor_11 (.node(out_37));
  Pull_Resistor pull_resistor_12 (.node(out_38));
  Pull_Resistor pull_resistor_13 (.node(out_39));
  Pull_Resistor pull_resistor_14 (.node(out_40));
  Pull_Resistor pull_resistor_15 (.node(out_41));
  Pull_Resistor pull_resistor_16 (.node(out_42));
  Pull_Resistor pull_resistor_17 (.node(out_43));
  Pull_Resistor pull_resistor_18 (.node(out_44));
  Pull_Resistor pull_resistor_19 (.node(out_45));
  Pull_Resistor pull_resistor_20 (.node(out_46));
  Pull_Resistor pull_resistor_21 (.node(out_47));
  Pull_Resistor pull_resistor_22 (.node(out_48));
  Pull_Resistor pull_resistor_23 (.node(out_49));
  Pull_Resistor pull_resistor_24 (.node(out_50));
  assign controlled_buffer_1_out = En ? in_3 : 5'bz;  // Controlled_Buffer controlled_buffer_1
  not not_1 (not_1_out, En);
  assign controlled_buffer_1_out = not_1_out ? {5{1'b0}} : 5'bz;  // Controlled_Buffer controlled_buffer_2
  Demultiplexer #(.select(5), .width(32)) demultiplexer_1 (
    .out0(demultiplexer_1_out0), .out1(demultiplexer_1_out1), .out2(demultiplexer_1_out2),
    .out3(demultiplexer_1_out3), .out4(demultiplexer_1_out4), .out5(demultiplexer_1_out5),
    .out6(demultiplexer_1_out6), .out7(demultiplexer_1_out7), .out8(demultiplexer_1_out8),
    .out9(demultiplexer_1_out9), .out10(demultiplexer_1_out10), .out11(demultiplexer_1_out11),
    .out12(demultiplexer_1_out12), .out13(demultiplexer_1_out13), .out14(demultiplexer_1_out14),
    .out15(demultiplexer_1_out15), .out16(demultiplexer_1_out16), .out17(demultiplexer_1_out17),
    .out18(demultiplexer_1_out18), .out19(demultiplexer_1_out19), .out20(demultiplexer_1_out20),
    .out21(demultiplexer_1_out21), .out22(demultiplexer_1_out22), .out23(demultiplexer_1_out23),
    .in(\Вход_0 ), .sel(controlled_buffer_1_out));  // open: out24, out25, out26, out27, out28, out29, out30, out31, en
  Demultiplexer #(.select(5), .width(32)) demultiplexer_2 (
    .out4(demultiplexer_2_out4), .out5(demultiplexer_2_out5), .out6(demultiplexer_2_out6),
    .out7(demultiplexer_2_out7), .out8(demultiplexer_2_out8), .out9(demultiplexer_2_out9),
    .out10(demultiplexer_2_out10), .out11(demultiplexer_2_out11), .out12(demultiplexer_2_out12),
    .out13(demultiplexer_2_out13), .out14(demultiplexer_2_out14), .out15(demultiplexer_2_out15),
    .out16(demultiplexer_2_out16), .out17(demultiplexer_2_out17), .out18(demultiplexer_2_out18),
    .out19(demultiplexer_2_out19), .out20(demultiplexer_2_out20), .out21(demultiplexer_2_out21),
    .out22(demultiplexer_2_out22), .out23(demultiplexer_2_out23), .in(in_7), .sel(inc5_1_r));  // open: out0, out1, out2, out3, out24, out25, out26, out27, out28, out29, out30, out31, en
  inc5 inc5_1 (.X(inc5_18_r), .R(inc5_1_r));  // open: Cout
  Demultiplexer #(.select(5), .width(32)) demultiplexer_3 (
    .out8(demultiplexer_3_out8), .out9(demultiplexer_3_out9), .out10(demultiplexer_3_out10),
    .out11(demultiplexer_3_out11), .out12(demultiplexer_3_out12), .out13(demultiplexer_3_out13),
    .out14(demultiplexer_3_out14), .out15(demultiplexer_3_out15), .out16(demultiplexer_3_out16),
    .out17(demultiplexer_3_out17), .out18(demultiplexer_3_out18), .out19(demultiplexer_3_out19),
    .out20(demultiplexer_3_out20), .out21(demultiplexer_3_out21), .out22(demultiplexer_3_out22),
    .out23(demultiplexer_3_out23), .in(in_11), .sel(inc5_2_r));  // open: out0, out1, out2, out3, out4, out5, out6, out7, out24, out25, out26, out27, out28, out29, out30, out31, en
  inc5 inc5_2 (.X(inc5_19_r), .R(inc5_2_r));  // open: Cout
  Demultiplexer #(.select(5), .width(32)) demultiplexer_4 (
    .out12(demultiplexer_4_out12), .out13(demultiplexer_4_out13), .out14(demultiplexer_4_out14),
    .out15(demultiplexer_4_out15), .out16(demultiplexer_4_out16), .out17(demultiplexer_4_out17),
    .out18(demultiplexer_4_out18), .out19(demultiplexer_4_out19), .out20(demultiplexer_4_out20),
    .out21(demultiplexer_4_out21), .out22(demultiplexer_4_out22), .out23(demultiplexer_4_out23), .in(in_15),
    .sel(inc5_3_r));  // open: out0, out1, out2, out3, out4, out5, out6, out7, out8, out9, out10, out11, out24, out25, out26, out27, out28, out29, out30, out31, en
  inc5 inc5_3 (.X(inc5_20_r), .R(inc5_3_r));  // open: Cout
  Demultiplexer #(.select(5), .width(32)) demultiplexer_5 (
    .out16(demultiplexer_5_out16), .out17(demultiplexer_5_out17), .out18(demultiplexer_5_out18),
    .out19(demultiplexer_5_out19), .out20(demultiplexer_5_out20), .out21(demultiplexer_5_out21),
    .out22(demultiplexer_5_out22), .out23(demultiplexer_5_out23), .in(in_19), .sel(inc5_4_r));  // open: out0, out1, out2, out3, out4, out5, out6, out7, out8, out9, out10, out11, out12, out13, out14, out15, out24, out25, out26, out27, out28, out29, out30, out31, en
  inc5 inc5_4 (.X(inc5_21_r), .R(inc5_4_r));  // open: Cout
  Demultiplexer #(.select(5), .width(32)) demultiplexer_6 (
    .out20(demultiplexer_6_out20), .out21(demultiplexer_6_out21), .out22(demultiplexer_6_out22),
    .out23(demultiplexer_6_out23), .in(in_23), .sel(inc5_5_r));  // open: out0, out1, out2, out3, out4, out5, out6, out7, out8, out9, out10, out11, out12, out13, out14, out15, out16, out17, out18, out19, out24, out25, out26, out27, out28, out29, out30, out31, en
  inc5 inc5_5 (.X(inc5_22_r), .R(inc5_5_r));  // open: Cout
  decodBufer decodbufer_1 (.in_1(demultiplexer_1_out0), .out_2(\Выход_0 ));
  decodBufer decodbufer_2 (.in_1(demultiplexer_1_out1), .out_2(out_28));
  decodBufer decodbufer_3 (.in_1(demultiplexer_1_out2), .out_2(out_29));
  decodBufer decodbufer_4 (.in_1(demultiplexer_1_out3), .out_2(out_30));
  decodBufer decodbufer_5 (.in_1(demultiplexer_1_out4), .out_2(out_31));
  decodBufer decodbufer_6 (.in_1(demultiplexer_1_out5), .out_2(out_32));
  decodBufer decodbufer_7 (.in_1(demultiplexer_1_out6), .out_2(out_33));
  decodBufer decodbufer_8 (.in_1(demultiplexer_1_out7), .out_2(out_34));
  decodBufer decodbufer_9 (.in_1(demultiplexer_1_out8), .out_2(out_35));
  decodBufer decodbufer_10 (.in_1(demultiplexer_1_out9), .out_2(out_36));
  decodBufer decodbufer_11 (.in_1(demultiplexer_1_out10), .out_2(out_37));
  decodBufer decodbufer_12 (.in_1(demultiplexer_1_out11), .out_2(out_38));
  decodBufer decodbufer_13 (.in_1(demultiplexer_1_out12), .out_2(out_39));
  decodBufer decodbufer_14 (.in_1(demultiplexer_1_out13), .out_2(out_40));
  decodBufer decodbufer_15 (.in_1(demultiplexer_1_out14), .out_2(out_41));
  decodBufer decodbufer_16 (.in_1(demultiplexer_1_out15), .out_2(out_42));
  decodBufer decodbufer_17 (.in_1(demultiplexer_1_out16), .out_2(out_43));
  decodBufer decodbufer_18 (.in_1(demultiplexer_1_out17), .out_2(out_44));
  decodBufer decodbufer_19 (.in_1(demultiplexer_1_out18), .out_2(out_45));
  decodBufer decodbufer_20 (.in_1(demultiplexer_1_out19), .out_2(out_46));
  decodBufer decodbufer_21 (.in_1(demultiplexer_1_out20), .out_2(out_47));
  decodBufer decodbufer_22 (.in_1(demultiplexer_1_out21), .out_2(out_48));
  decodBufer decodbufer_23 (.in_1(demultiplexer_1_out22), .out_2(out_49));
  decodBufer decodbufer_24 (.in_1(demultiplexer_1_out23), .out_2(out_50));
  inc5 inc5_6 (.X(controlled_buffer_1_out), .R(inc5_6_r));  // open: Cout
  decodBufer decodbufer_25 (.in_1(demultiplexer_2_out4), .out_2(out_31));
  decodBufer decodbufer_26 (.in_1(demultiplexer_2_out5), .out_2(out_32));
  decodBufer decodbufer_27 (.in_1(demultiplexer_2_out6), .out_2(out_33));
  decodBufer decodbufer_28 (.in_1(demultiplexer_2_out7), .out_2(out_34));
  decodBufer decodbufer_29 (.in_1(demultiplexer_2_out8), .out_2(out_35));
  decodBufer decodbufer_30 (.in_1(demultiplexer_2_out9), .out_2(out_36));
  decodBufer decodbufer_31 (.in_1(demultiplexer_2_out10), .out_2(out_37));
  decodBufer decodbufer_32 (.in_1(demultiplexer_2_out11), .out_2(out_38));
  decodBufer decodbufer_33 (.in_1(demultiplexer_2_out12), .out_2(out_39));
  decodBufer decodbufer_34 (.in_1(demultiplexer_2_out13), .out_2(out_40));
  decodBufer decodbufer_35 (.in_1(demultiplexer_2_out14), .out_2(out_41));
  decodBufer decodbufer_36 (.in_1(demultiplexer_2_out15), .out_2(out_42));
  decodBufer decodbufer_37 (.in_1(demultiplexer_2_out16), .out_2(out_43));
  decodBufer decodbufer_38 (.in_1(demultiplexer_2_out17), .out_2(out_44));
  decodBufer decodbufer_39 (.in_1(demultiplexer_2_out18), .out_2(out_45));
  decodBufer decodbufer_40 (.in_1(demultiplexer_2_out19), .out_2(out_46));
  decodBufer decodbufer_41 (.in_1(demultiplexer_2_out20), .out_2(out_47));
  decodBufer decodbufer_42 (.in_1(demultiplexer_2_out21), .out_2(out_48));
  decodBufer decodbufer_43 (.in_1(demultiplexer_2_out22), .out_2(out_49));
  decodBufer decodbufer_44 (.in_1(demultiplexer_2_out23), .out_2(out_50));
  inc5 inc5_7 (.X(inc5_1_r), .R(inc5_7_r));  // open: Cout
  decodBufer decodbufer_45 (.in_1(demultiplexer_3_out8), .out_2(out_35));
  decodBufer decodbufer_46 (.in_1(demultiplexer_3_out9), .out_2(out_36));
  decodBufer decodbufer_47 (.in_1(demultiplexer_3_out10), .out_2(out_37));
  decodBufer decodbufer_48 (.in_1(demultiplexer_3_out11), .out_2(out_38));
  decodBufer decodbufer_49 (.in_1(demultiplexer_3_out12), .out_2(out_39));
  decodBufer decodbufer_50 (.in_1(demultiplexer_3_out13), .out_2(out_40));
  decodBufer decodbufer_51 (.in_1(demultiplexer_3_out14), .out_2(out_41));
  decodBufer decodbufer_52 (.in_1(demultiplexer_3_out15), .out_2(out_42));
  decodBufer decodbufer_53 (.in_1(demultiplexer_3_out16), .out_2(out_43));
  decodBufer decodbufer_54 (.in_1(demultiplexer_3_out17), .out_2(out_44));
  decodBufer decodbufer_55 (.in_1(demultiplexer_3_out18), .out_2(out_45));
  decodBufer decodbufer_56 (.in_1(demultiplexer_3_out19), .out_2(out_46));
  decodBufer decodbufer_57 (.in_1(demultiplexer_3_out20), .out_2(out_47));
  decodBufer decodbufer_58 (.in_1(demultiplexer_3_out21), .out_2(out_48));
  decodBufer decodbufer_59 (.in_1(demultiplexer_3_out22), .out_2(out_49));
  decodBufer decodbufer_60 (.in_1(demultiplexer_3_out23), .out_2(out_50));
  inc5 inc5_8 (.X(inc5_2_r), .R(inc5_8_r));  // open: Cout
  decodBufer decodbufer_61 (.in_1(demultiplexer_4_out12), .out_2(out_39));
  decodBufer decodbufer_62 (.in_1(demultiplexer_4_out13), .out_2(out_40));
  decodBufer decodbufer_63 (.in_1(demultiplexer_4_out14), .out_2(out_41));
  decodBufer decodbufer_64 (.in_1(demultiplexer_4_out15), .out_2(out_42));
  decodBufer decodbufer_65 (.in_1(demultiplexer_4_out16), .out_2(out_43));
  decodBufer decodbufer_66 (.in_1(demultiplexer_4_out17), .out_2(out_44));
  decodBufer decodbufer_67 (.in_1(demultiplexer_4_out18), .out_2(out_45));
  decodBufer decodbufer_68 (.in_1(demultiplexer_4_out19), .out_2(out_46));
  decodBufer decodbufer_69 (.in_1(demultiplexer_4_out20), .out_2(out_47));
  decodBufer decodbufer_70 (.in_1(demultiplexer_4_out21), .out_2(out_48));
  decodBufer decodbufer_71 (.in_1(demultiplexer_4_out22), .out_2(out_49));
  decodBufer decodbufer_72 (.in_1(demultiplexer_4_out23), .out_2(out_50));
  inc5 inc5_9 (.X(inc5_3_r), .R(inc5_9_r));  // open: Cout
  decodBufer decodbufer_73 (.in_1(demultiplexer_5_out16), .out_2(out_43));
  decodBufer decodbufer_74 (.in_1(demultiplexer_5_out17), .out_2(out_44));
  decodBufer decodbufer_75 (.in_1(demultiplexer_5_out18), .out_2(out_45));
  decodBufer decodbufer_76 (.in_1(demultiplexer_5_out19), .out_2(out_46));
  decodBufer decodbufer_77 (.in_1(demultiplexer_5_out20), .out_2(out_47));
  decodBufer decodbufer_78 (.in_1(demultiplexer_5_out21), .out_2(out_48));
  decodBufer decodbufer_79 (.in_1(demultiplexer_5_out22), .out_2(out_49));
  decodBufer decodbufer_80 (.in_1(demultiplexer_5_out23), .out_2(out_50));
  inc5 inc5_10 (.X(inc5_4_r), .R(inc5_10_r));  // open: Cout
  decodBufer decodbufer_81 (.in_1(demultiplexer_6_out20), .out_2(out_47));
  decodBufer decodbufer_82 (.in_1(demultiplexer_6_out21), .out_2(out_48));
  decodBufer decodbufer_83 (.in_1(demultiplexer_6_out22), .out_2(out_49));
  decodBufer decodbufer_84 (.in_1(demultiplexer_6_out23), .out_2(out_50));
  inc5 inc5_11 (.X(inc5_5_r), .R(inc5_11_r));  // open: Cout
  Demultiplexer #(.select(5), .width(32)) demultiplexer_7 (
    .out1(demultiplexer_7_out1), .out2(demultiplexer_7_out2), .out3(demultiplexer_7_out3),
    .out4(demultiplexer_7_out4), .out5(demultiplexer_7_out5), .out6(demultiplexer_7_out6),
    .out7(demultiplexer_7_out7), .out8(demultiplexer_7_out8), .out9(demultiplexer_7_out9),
    .out10(demultiplexer_7_out10), .out11(demultiplexer_7_out11), .out12(demultiplexer_7_out12),
    .out13(demultiplexer_7_out13), .out14(demultiplexer_7_out14), .out15(demultiplexer_7_out15),
    .out16(demultiplexer_7_out16), .out17(demultiplexer_7_out17), .out18(demultiplexer_7_out18),
    .out19(demultiplexer_7_out19), .out20(demultiplexer_7_out20), .out21(demultiplexer_7_out21),
    .out22(demultiplexer_7_out22), .out23(demultiplexer_7_out23), .in(in_2), .sel(inc5_6_r));  // open: out0, out24, out25, out26, out27, out28, out29, out30, out31, en
  Demultiplexer #(.select(5), .width(32)) demultiplexer_8 (
    .out5(demultiplexer_8_out5), .out6(demultiplexer_8_out6), .out7(demultiplexer_8_out7),
    .out8(demultiplexer_8_out8), .out9(demultiplexer_8_out9), .out10(demultiplexer_8_out10),
    .out11(demultiplexer_8_out11), .out12(demultiplexer_8_out12), .out13(demultiplexer_8_out13),
    .out14(demultiplexer_8_out14), .out15(demultiplexer_8_out15), .out16(demultiplexer_8_out16),
    .out17(demultiplexer_8_out17), .out18(demultiplexer_8_out18), .out19(demultiplexer_8_out19),
    .out20(demultiplexer_8_out20), .out21(demultiplexer_8_out21), .out22(demultiplexer_8_out22),
    .out23(demultiplexer_8_out23), .in(in_8), .sel(inc5_7_r));  // open: out0, out1, out2, out3, out4, out24, out25, out26, out27, out28, out29, out30, out31, en
  Demultiplexer #(.select(5), .width(32)) demultiplexer_9 (
    .out9(demultiplexer_9_out9), .out10(demultiplexer_9_out10), .out11(demultiplexer_9_out11),
    .out12(demultiplexer_9_out12), .out13(demultiplexer_9_out13), .out14(demultiplexer_9_out14),
    .out15(demultiplexer_9_out15), .out16(demultiplexer_9_out16), .out17(demultiplexer_9_out17),
    .out18(demultiplexer_9_out18), .out19(demultiplexer_9_out19), .out20(demultiplexer_9_out20),
    .out21(demultiplexer_9_out21), .out22(demultiplexer_9_out22), .out23(demultiplexer_9_out23), .in(in_12),
    .sel(inc5_8_r));  // open: out0, out1, out2, out3, out4, out5, out6, out7, out8, out24, out25, out26, out27, out28, out29, out30, out31, en
  Demultiplexer #(.select(5), .width(32)) demultiplexer_10 (
    .out13(demultiplexer_10_out13), .out14(demultiplexer_10_out14), .out15(demultiplexer_10_out15),
    .out16(demultiplexer_10_out16), .out17(demultiplexer_10_out17), .out18(demultiplexer_10_out18),
    .out19(demultiplexer_10_out19), .out20(demultiplexer_10_out20), .out21(demultiplexer_10_out21),
    .out22(demultiplexer_10_out22), .out23(demultiplexer_10_out23), .in(in_16), .sel(inc5_9_r));  // open: out0, out1, out2, out3, out4, out5, out6, out7, out8, out9, out10, out11, out12, out24, out25, out26, out27, out28, out29, out30, out31, en
  Demultiplexer #(.select(5), .width(32)) demultiplexer_11 (
    .out17(demultiplexer_11_out17), .out18(demultiplexer_11_out18), .out19(demultiplexer_11_out19),
    .out20(demultiplexer_11_out20), .out21(demultiplexer_11_out21), .out22(demultiplexer_11_out22),
    .out23(demultiplexer_11_out23), .in(in_20), .sel(inc5_10_r));  // open: out0, out1, out2, out3, out4, out5, out6, out7, out8, out9, out10, out11, out12, out13, out14, out15, out16, out24, out25, out26, out27, out28, out29, out30, out31, en
  Demultiplexer #(.select(5), .width(32)) demultiplexer_12 (
    .out21(demultiplexer_12_out21), .out22(demultiplexer_12_out22), .out23(demultiplexer_12_out23),
    .in(in_24), .sel(inc5_11_r));  // open: out0, out1, out2, out3, out4, out5, out6, out7, out8, out9, out10, out11, out12, out13, out14, out15, out16, out17, out18, out19, out20, out24, out25, out26, out27, out28, out29, out30, out31, en
  decodBufer decodbufer_85 (.in_1(demultiplexer_7_out1), .out_2(out_28));
  decodBufer decodbufer_86 (.in_1(demultiplexer_7_out2), .out_2(out_29));
  decodBufer decodbufer_87 (.in_1(demultiplexer_7_out3), .out_2(out_30));
  decodBufer decodbufer_88 (.in_1(demultiplexer_7_out4), .out_2(out_31));
  decodBufer decodbufer_89 (.in_1(demultiplexer_7_out5), .out_2(out_32));
  decodBufer decodbufer_90 (.in_1(demultiplexer_7_out6), .out_2(out_33));
  decodBufer decodbufer_91 (.in_1(demultiplexer_7_out7), .out_2(out_34));
  decodBufer decodbufer_92 (.in_1(demultiplexer_7_out8), .out_2(out_35));
  decodBufer decodbufer_93 (.in_1(demultiplexer_7_out9), .out_2(out_36));
  decodBufer decodbufer_94 (.in_1(demultiplexer_7_out10), .out_2(out_37));
  decodBufer decodbufer_95 (.in_1(demultiplexer_7_out11), .out_2(out_38));
  decodBufer decodbufer_96 (.in_1(demultiplexer_7_out12), .out_2(out_39));
  decodBufer decodbufer_97 (.in_1(demultiplexer_7_out13), .out_2(out_40));
  decodBufer decodbufer_98 (.in_1(demultiplexer_7_out14), .out_2(out_41));
  Demultiplexer #(.select(5), .width(32)) demultiplexer_13 (
    .out2(demultiplexer_13_out2), .out3(demultiplexer_13_out3), .out4(demultiplexer_13_out4),
    .out5(demultiplexer_13_out5), .out6(demultiplexer_13_out6), .out7(demultiplexer_13_out7),
    .out8(demultiplexer_13_out8), .out9(demultiplexer_13_out9), .out10(demultiplexer_13_out10),
    .out11(demultiplexer_13_out11), .out12(demultiplexer_13_out12), .out13(demultiplexer_13_out13),
    .out14(demultiplexer_13_out14), .out15(demultiplexer_13_out15), .out16(demultiplexer_13_out16),
    .out17(demultiplexer_13_out17), .out18(demultiplexer_13_out18), .out19(demultiplexer_13_out19),
    .out20(demultiplexer_13_out20), .out21(demultiplexer_13_out21), .out22(demultiplexer_13_out22),
    .out23(demultiplexer_13_out23), .in(in_4), .sel(inc5_12_r));  // open: out0, out1, out24, out25, out26, out27, out28, out29, out30, out31, en
  decodBufer decodbufer_99 (.in_1(demultiplexer_7_out15), .out_2(out_42));
  decodBufer decodbufer_100 (.in_1(demultiplexer_7_out16), .out_2(out_43));
  decodBufer decodbufer_101 (.in_1(demultiplexer_7_out17), .out_2(out_44));
  decodBufer decodbufer_102 (.in_1(demultiplexer_7_out18), .out_2(out_45));
  decodBufer decodbufer_103 (.in_1(demultiplexer_7_out19), .out_2(out_46));
  decodBufer decodbufer_104 (.in_1(demultiplexer_7_out20), .out_2(out_47));
  decodBufer decodbufer_105 (.in_1(demultiplexer_7_out21), .out_2(out_48));
  decodBufer decodbufer_106 (.in_1(demultiplexer_7_out22), .out_2(out_49));
  decodBufer decodbufer_107 (.in_1(demultiplexer_7_out23), .out_2(out_50));
  inc5 inc5_12 (.X(inc5_6_r), .R(inc5_12_r));  // open: Cout
  decodBufer decodbufer_108 (.in_1(demultiplexer_8_out5), .out_2(out_32));
  decodBufer decodbufer_109 (.in_1(demultiplexer_8_out6), .out_2(out_33));
  decodBufer decodbufer_110 (.in_1(demultiplexer_8_out7), .out_2(out_34));
  decodBufer decodbufer_111 (.in_1(demultiplexer_8_out8), .out_2(out_35));
  decodBufer decodbufer_112 (.in_1(demultiplexer_8_out9), .out_2(out_36));
  decodBufer decodbufer_113 (.in_1(demultiplexer_8_out10), .out_2(out_37));
  decodBufer decodbufer_114 (.in_1(demultiplexer_8_out11), .out_2(out_38));
  decodBufer decodbufer_115 (.in_1(demultiplexer_8_out12), .out_2(out_39));
  decodBufer decodbufer_116 (.in_1(demultiplexer_8_out13), .out_2(out_40));
  decodBufer decodbufer_117 (.in_1(demultiplexer_8_out14), .out_2(out_41));
  decodBufer decodbufer_118 (.in_1(demultiplexer_8_out15), .out_2(out_42));
  Demultiplexer #(.select(5), .width(32)) demultiplexer_14 (
    .out6(demultiplexer_14_out6), .out7(demultiplexer_14_out7), .out8(demultiplexer_14_out8),
    .out9(demultiplexer_14_out9), .out10(demultiplexer_14_out10), .out11(demultiplexer_14_out11),
    .out12(demultiplexer_14_out12), .out13(demultiplexer_14_out13), .out14(demultiplexer_14_out14),
    .out15(demultiplexer_14_out15), .out16(demultiplexer_14_out16), .out17(demultiplexer_14_out17),
    .out18(demultiplexer_14_out18), .out19(demultiplexer_14_out19), .out20(demultiplexer_14_out20),
    .out21(demultiplexer_14_out21), .out22(demultiplexer_14_out22), .out23(demultiplexer_14_out23),
    .in(in_9), .sel(inc5_13_r));  // open: out0, out1, out2, out3, out4, out5, out24, out25, out26, out27, out28, out29, out30, out31, en
  decodBufer decodbufer_119 (.in_1(demultiplexer_8_out16), .out_2(out_43));
  decodBufer decodbufer_120 (.in_1(demultiplexer_8_out17), .out_2(out_44));
  decodBufer decodbufer_121 (.in_1(demultiplexer_8_out18), .out_2(out_45));
  decodBufer decodbufer_122 (.in_1(demultiplexer_8_out19), .out_2(out_46));
  decodBufer decodbufer_123 (.in_1(demultiplexer_8_out20), .out_2(out_47));
  decodBufer decodbufer_124 (.in_1(demultiplexer_8_out21), .out_2(out_48));
  decodBufer decodbufer_125 (.in_1(demultiplexer_8_out22), .out_2(out_49));
  decodBufer decodbufer_126 (.in_1(demultiplexer_8_out23), .out_2(out_50));
  inc5 inc5_13 (.X(inc5_7_r), .R(inc5_13_r));  // open: Cout
  decodBufer decodbufer_127 (.in_1(demultiplexer_9_out9), .out_2(out_36));
  decodBufer decodbufer_128 (.in_1(demultiplexer_9_out10), .out_2(out_37));
  decodBufer decodbufer_129 (.in_1(demultiplexer_9_out11), .out_2(out_38));
  decodBufer decodbufer_130 (.in_1(demultiplexer_9_out12), .out_2(out_39));
  decodBufer decodbufer_131 (.in_1(demultiplexer_9_out13), .out_2(out_40));
  decodBufer decodbufer_132 (.in_1(demultiplexer_9_out14), .out_2(out_41));
  decodBufer decodbufer_133 (.in_1(demultiplexer_9_out15), .out_2(out_42));
  decodBufer decodbufer_134 (.in_1(demultiplexer_9_out16), .out_2(out_43));
  decodBufer decodbufer_135 (.in_1(demultiplexer_9_out17), .out_2(out_44));
  decodBufer decodbufer_136 (.in_1(demultiplexer_9_out18), .out_2(out_45));
  decodBufer decodbufer_137 (.in_1(demultiplexer_9_out19), .out_2(out_46));
  decodBufer decodbufer_138 (.in_1(demultiplexer_9_out20), .out_2(out_47));
  decodBufer decodbufer_139 (.in_1(demultiplexer_9_out21), .out_2(out_48));
  decodBufer decodbufer_140 (.in_1(demultiplexer_9_out22), .out_2(out_49));
  decodBufer decodbufer_141 (.in_1(demultiplexer_9_out23), .out_2(out_50));
  inc5 inc5_14 (.X(inc5_8_r), .R(inc5_14_r));  // open: Cout
  decodBufer decodbufer_142 (.in_1(demultiplexer_10_out13), .out_2(out_40));
  decodBufer decodbufer_143 (.in_1(demultiplexer_10_out14), .out_2(out_41));
  decodBufer decodbufer_144 (.in_1(demultiplexer_10_out15), .out_2(out_42));
  Demultiplexer #(.select(5), .width(32)) demultiplexer_15 (
    .out14(demultiplexer_15_out14), .out15(demultiplexer_15_out15), .out16(demultiplexer_15_out16),
    .out17(demultiplexer_15_out17), .out18(demultiplexer_15_out18), .out19(demultiplexer_15_out19),
    .out20(demultiplexer_15_out20), .out21(demultiplexer_15_out21), .out22(demultiplexer_15_out22),
    .out23(demultiplexer_15_out23), .in(in_17), .sel(inc5_15_r));  // open: out0, out1, out2, out3, out4, out5, out6, out7, out8, out9, out10, out11, out12, out13, out24, out25, out26, out27, out28, out29, out30, out31, en
  decodBufer decodbufer_145 (.in_1(demultiplexer_10_out16), .out_2(out_43));
  decodBufer decodbufer_146 (.in_1(demultiplexer_10_out17), .out_2(out_44));
  decodBufer decodbufer_147 (.in_1(demultiplexer_10_out18), .out_2(out_45));
  decodBufer decodbufer_148 (.in_1(demultiplexer_10_out19), .out_2(out_46));
  decodBufer decodbufer_149 (.in_1(demultiplexer_10_out20), .out_2(out_47));
  decodBufer decodbufer_150 (.in_1(demultiplexer_10_out21), .out_2(out_48));
  decodBufer decodbufer_151 (.in_1(demultiplexer_10_out22), .out_2(out_49));
  decodBufer decodbufer_152 (.in_1(demultiplexer_10_out23), .out_2(out_50));
  inc5 inc5_15 (.X(inc5_9_r), .R(inc5_15_r));  // open: Cout
  Demultiplexer #(.select(5), .width(32)) demultiplexer_16 (
    .out18(demultiplexer_16_out18), .out19(demultiplexer_16_out19), .out20(demultiplexer_16_out20),
    .out21(demultiplexer_16_out21), .out22(demultiplexer_16_out22), .out23(demultiplexer_16_out23),
    .in(in_21), .sel(inc5_16_r));  // open: out0, out1, out2, out3, out4, out5, out6, out7, out8, out9, out10, out11, out12, out13, out14, out15, out16, out17, out24, out25, out26, out27, out28, out29, out30, out31, en
  decodBufer decodbufer_153 (.in_1(demultiplexer_11_out17), .out_2(out_44));
  decodBufer decodbufer_154 (.in_1(demultiplexer_11_out18), .out_2(out_45));
  decodBufer decodbufer_155 (.in_1(demultiplexer_11_out19), .out_2(out_46));
  decodBufer decodbufer_156 (.in_1(demultiplexer_11_out20), .out_2(out_47));
  decodBufer decodbufer_157 (.in_1(demultiplexer_11_out21), .out_2(out_48));
  decodBufer decodbufer_158 (.in_1(demultiplexer_11_out22), .out_2(out_49));
  decodBufer decodbufer_159 (.in_1(demultiplexer_11_out23), .out_2(out_50));
  inc5 inc5_16 (.X(inc5_10_r), .R(inc5_16_r));  // open: Cout
  Demultiplexer #(.select(5), .width(32)) demultiplexer_17 (
    .out22(demultiplexer_17_out22), .out23(demultiplexer_17_out23), .in(in_25), .sel(inc5_17_r));  // open: out0, out1, out2, out3, out4, out5, out6, out7, out8, out9, out10, out11, out12, out13, out14, out15, out16, out17, out18, out19, out20, out21, out24, out25, out26, out27, out28, out29, out30, out31, en
  decodBufer decodbufer_160 (.in_1(demultiplexer_12_out21), .out_2(out_48));
  decodBufer decodbufer_161 (.in_1(demultiplexer_12_out22), .out_2(out_49));
  decodBufer decodbufer_162 (.in_1(demultiplexer_12_out23), .out_2(out_50));
  inc5 inc5_17 (.X(inc5_11_r), .R(inc5_17_r));  // open: Cout
  decodBufer decodbufer_163 (.in_1(demultiplexer_13_out2), .out_2(out_29));
  decodBufer decodbufer_164 (.in_1(demultiplexer_13_out3), .out_2(out_30));
  decodBufer decodbufer_165 (.in_1(demultiplexer_13_out4), .out_2(out_31));
  decodBufer decodbufer_166 (.in_1(demultiplexer_13_out5), .out_2(out_32));
  decodBufer decodbufer_167 (.in_1(demultiplexer_13_out6), .out_2(out_33));
  decodBufer decodbufer_168 (.in_1(demultiplexer_13_out7), .out_2(out_34));
  decodBufer decodbufer_169 (.in_1(demultiplexer_13_out8), .out_2(out_35));
  decodBufer decodbufer_170 (.in_1(demultiplexer_13_out9), .out_2(out_36));
  decodBufer decodbufer_171 (.in_1(demultiplexer_13_out10), .out_2(out_37));
  decodBufer decodbufer_172 (.in_1(demultiplexer_13_out11), .out_2(out_38));
  decodBufer decodbufer_173 (.in_1(demultiplexer_13_out12), .out_2(out_39));
  decodBufer decodbufer_174 (.in_1(demultiplexer_13_out13), .out_2(out_40));
  decodBufer decodbufer_175 (.in_1(demultiplexer_13_out14), .out_2(out_41));
  decodBufer decodbufer_176 (.in_1(demultiplexer_13_out15), .out_2(out_42));
  decodBufer decodbufer_177 (.in_1(demultiplexer_13_out16), .out_2(out_43));
  decodBufer decodbufer_178 (.in_1(demultiplexer_13_out17), .out_2(out_44));
  decodBufer decodbufer_179 (.in_1(demultiplexer_13_out18), .out_2(out_45));
  decodBufer decodbufer_180 (.in_1(demultiplexer_13_out19), .out_2(out_46));
  decodBufer decodbufer_181 (.in_1(demultiplexer_13_out20), .out_2(out_47));
  decodBufer decodbufer_182 (.in_1(demultiplexer_13_out21), .out_2(out_48));
  decodBufer decodbufer_183 (.in_1(demultiplexer_13_out22), .out_2(out_49));
  decodBufer decodbufer_184 (.in_1(demultiplexer_13_out23), .out_2(out_50));
  decodBufer decodbufer_185 (.in_1(demultiplexer_14_out6), .out_2(out_33));
  decodBufer decodbufer_186 (.in_1(demultiplexer_14_out7), .out_2(out_34));
  decodBufer decodbufer_187 (.in_1(demultiplexer_14_out8), .out_2(out_35));
  decodBufer decodbufer_188 (.in_1(demultiplexer_14_out9), .out_2(out_36));
  decodBufer decodbufer_189 (.in_1(demultiplexer_14_out10), .out_2(out_37));
  decodBufer decodbufer_190 (.in_1(demultiplexer_14_out11), .out_2(out_38));
  decodBufer decodbufer_191 (.in_1(demultiplexer_14_out12), .out_2(out_39));
  decodBufer decodbufer_192 (.in_1(demultiplexer_14_out13), .out_2(out_40));
  decodBufer decodbufer_193 (.in_1(demultiplexer_14_out14), .out_2(out_41));
  decodBufer decodbufer_194 (.in_1(demultiplexer_14_out15), .out_2(out_42));
  decodBufer decodbufer_195 (.in_1(demultiplexer_14_out16), .out_2(out_43));
  decodBufer decodbufer_196 (.in_1(demultiplexer_14_out17), .out_2(out_44));
  decodBufer decodbufer_197 (.in_1(demultiplexer_14_out18), .out_2(out_45));
  decodBufer decodbufer_198 (.in_1(demultiplexer_14_out19), .out_2(out_46));
  decodBufer decodbufer_199 (.in_1(demultiplexer_14_out20), .out_2(out_47));
  decodBufer decodbufer_200 (.in_1(demultiplexer_14_out21), .out_2(out_48));
  decodBufer decodbufer_201 (.in_1(demultiplexer_14_out22), .out_2(out_49));
  decodBufer decodbufer_202 (.in_1(demultiplexer_14_out23), .out_2(out_50));
  Demultiplexer #(.select(5), .width(32)) demultiplexer_18 (
    .out10(demultiplexer_18_out10), .out11(demultiplexer_18_out11), .out12(demultiplexer_18_out12),
    .out13(demultiplexer_18_out13), .out14(demultiplexer_18_out14), .out15(demultiplexer_18_out15),
    .out16(demultiplexer_18_out16), .out17(demultiplexer_18_out17), .out18(demultiplexer_18_out18),
    .out19(demultiplexer_18_out19), .out20(demultiplexer_18_out20), .out21(demultiplexer_18_out21),
    .out22(demultiplexer_18_out22), .out23(demultiplexer_18_out23), .in(in_13), .sel(inc5_14_r));  // open: out0, out1, out2, out3, out4, out5, out6, out7, out8, out9, out24, out25, out26, out27, out28, out29, out30, out31, en
  decodBufer decodbufer_203 (.in_1(demultiplexer_15_out14), .out_2(out_41));
  decodBufer decodbufer_204 (.in_1(demultiplexer_15_out15), .out_2(out_42));
  decodBufer decodbufer_205 (.in_1(demultiplexer_15_out16), .out_2(out_43));
  decodBufer decodbufer_206 (.in_1(demultiplexer_15_out17), .out_2(out_44));
  decodBufer decodbufer_207 (.in_1(demultiplexer_15_out18), .out_2(out_45));
  decodBufer decodbufer_208 (.in_1(demultiplexer_15_out19), .out_2(out_46));
  decodBufer decodbufer_209 (.in_1(demultiplexer_15_out20), .out_2(out_47));
  decodBufer decodbufer_210 (.in_1(demultiplexer_15_out21), .out_2(out_48));
  decodBufer decodbufer_211 (.in_1(demultiplexer_15_out22), .out_2(out_49));
  decodBufer decodbufer_212 (.in_1(demultiplexer_15_out23), .out_2(out_50));
  decodBufer decodbufer_213 (.in_1(demultiplexer_16_out18), .out_2(out_45));
  decodBufer decodbufer_214 (.in_1(demultiplexer_16_out19), .out_2(out_46));
  decodBufer decodbufer_215 (.in_1(demultiplexer_16_out20), .out_2(out_47));
  decodBufer decodbufer_216 (.in_1(demultiplexer_16_out21), .out_2(out_48));
  decodBufer decodbufer_217 (.in_1(demultiplexer_16_out22), .out_2(out_49));
  decodBufer decodbufer_218 (.in_1(demultiplexer_16_out23), .out_2(out_50));
  decodBufer decodbufer_219 (.in_1(demultiplexer_17_out22), .out_2(out_49));
  decodBufer decodbufer_220 (.in_1(demultiplexer_17_out23), .out_2(out_50));
  Demultiplexer #(.select(5), .width(32)) demultiplexer_19 (
    .out3(demultiplexer_19_out3), .out4(demultiplexer_19_out4), .out5(demultiplexer_19_out5),
    .out6(demultiplexer_19_out6), .out7(demultiplexer_19_out7), .out8(demultiplexer_19_out8),
    .out9(demultiplexer_19_out9), .out10(demultiplexer_19_out10), .out11(demultiplexer_19_out11),
    .out12(demultiplexer_19_out12), .out13(demultiplexer_19_out13), .out14(demultiplexer_19_out14),
    .out15(demultiplexer_19_out15), .out16(demultiplexer_19_out16), .out17(demultiplexer_19_out17),
    .out18(demultiplexer_19_out18), .out19(demultiplexer_19_out19), .out20(demultiplexer_19_out20),
    .out21(demultiplexer_19_out21), .out22(demultiplexer_19_out22), .out23(demultiplexer_19_out23),
    .in(in_6), .sel(inc5_18_r));  // open: out0, out1, out2, out24, out25, out26, out27, out28, out29, out30, out31, en
  inc5 inc5_18 (.X(inc5_12_r), .R(inc5_18_r));  // open: Cout
  Demultiplexer #(.select(5), .width(32)) demultiplexer_20 (
    .out7(demultiplexer_20_out7), .out8(demultiplexer_20_out8), .out9(demultiplexer_20_out9),
    .out10(demultiplexer_20_out10), .out11(demultiplexer_20_out11), .out12(demultiplexer_20_out12),
    .out13(demultiplexer_20_out13), .out14(demultiplexer_20_out14), .out15(demultiplexer_20_out15),
    .out16(demultiplexer_20_out16), .out17(demultiplexer_20_out17), .out18(demultiplexer_20_out18),
    .out19(demultiplexer_20_out19), .out20(demultiplexer_20_out20), .out21(demultiplexer_20_out21),
    .out22(demultiplexer_20_out22), .out23(demultiplexer_20_out23), .in(in_10), .sel(inc5_19_r));  // open: out0, out1, out2, out3, out4, out5, out6, out24, out25, out26, out27, out28, out29, out30, out31, en
  inc5 inc5_19 (.X(inc5_13_r), .R(inc5_19_r));  // open: Cout
  decodBufer decodbufer_221 (.in_1(demultiplexer_18_out10), .out_2(out_37));
  decodBufer decodbufer_222 (.in_1(demultiplexer_18_out11), .out_2(out_38));
  decodBufer decodbufer_223 (.in_1(demultiplexer_18_out12), .out_2(out_39));
  decodBufer decodbufer_224 (.in_1(demultiplexer_18_out13), .out_2(out_40));
  decodBufer decodbufer_225 (.in_1(demultiplexer_18_out14), .out_2(out_41));
  decodBufer decodbufer_226 (.in_1(demultiplexer_18_out15), .out_2(out_42));
  decodBufer decodbufer_227 (.in_1(demultiplexer_18_out16), .out_2(out_43));
  Demultiplexer #(.select(5), .width(32)) demultiplexer_21 (
    .out11(demultiplexer_21_out11), .out12(demultiplexer_21_out12), .out13(demultiplexer_21_out13),
    .out14(demultiplexer_21_out14), .out15(demultiplexer_21_out15), .out16(demultiplexer_21_out16),
    .out17(demultiplexer_21_out17), .out18(demultiplexer_21_out18), .out19(demultiplexer_21_out19),
    .out20(demultiplexer_21_out20), .out21(demultiplexer_21_out21), .out22(demultiplexer_21_out22),
    .out23(demultiplexer_21_out23), .in(in_14), .sel(inc5_20_r));  // open: out0, out1, out2, out3, out4, out5, out6, out7, out8, out9, out10, out24, out25, out26, out27, out28, out29, out30, out31, en
  decodBufer decodbufer_228 (.in_1(demultiplexer_18_out17), .out_2(out_44));
  decodBufer decodbufer_229 (.in_1(demultiplexer_18_out18), .out_2(out_45));
  decodBufer decodbufer_230 (.in_1(demultiplexer_18_out19), .out_2(out_46));
  decodBufer decodbufer_231 (.in_1(demultiplexer_18_out20), .out_2(out_47));
  decodBufer decodbufer_232 (.in_1(demultiplexer_18_out21), .out_2(out_48));
  decodBufer decodbufer_233 (.in_1(demultiplexer_18_out22), .out_2(out_49));
  decodBufer decodbufer_234 (.in_1(demultiplexer_18_out23), .out_2(out_50));
  inc5 inc5_20 (.X(inc5_14_r), .R(inc5_20_r));  // open: Cout
  Demultiplexer #(.select(5), .width(32)) demultiplexer_22 (
    .out15(demultiplexer_22_out15), .out16(demultiplexer_22_out16), .out17(demultiplexer_22_out17),
    .out18(demultiplexer_22_out18), .out19(demultiplexer_22_out19), .out20(demultiplexer_22_out20),
    .out21(demultiplexer_22_out21), .out22(demultiplexer_22_out22), .out23(demultiplexer_22_out23),
    .in(in_18), .sel(inc5_21_r));  // open: out0, out1, out2, out3, out4, out5, out6, out7, out8, out9, out10, out11, out12, out13, out14, out24, out25, out26, out27, out28, out29, out30, out31, en
  inc5 inc5_21 (.X(inc5_15_r), .R(inc5_21_r));  // open: Cout
  Demultiplexer #(.select(5), .width(32)) demultiplexer_23 (
    .out19(demultiplexer_23_out19), .out20(demultiplexer_23_out20), .out21(demultiplexer_23_out21),
    .out22(demultiplexer_23_out22), .out23(demultiplexer_23_out23), .in(in_22), .sel(inc5_22_r));  // open: out0, out1, out2, out3, out4, out5, out6, out7, out8, out9, out10, out11, out12, out13, out14, out15, out16, out17, out18, out24, out25, out26, out27, out28, out29, out30, out31, en
  inc5 inc5_22 (.X(inc5_16_r), .R(inc5_22_r));  // open: Cout
  Demultiplexer #(.select(5), .width(32)) demultiplexer_24 (
    .out22(demultiplexer_24_out22), .in(in_26), .sel(inc5_23_r));  // open: out0, out1, out2, out3, out4, out5, out6, out7, out8, out9, out10, out11, out12, out13, out14, out15, out16, out17, out18, out19, out20, out21, out23, out24, out25, out26, out27, out28, out29, out30, out31, en
  inc5 inc5_23 (.X(inc5_17_r), .R(inc5_23_r));  // open: Cout
  decodBufer decodbufer_235 (.in_1(demultiplexer_19_out3), .out_2(out_30));
  decodBufer decodbufer_236 (.in_1(demultiplexer_19_out4), .out_2(out_31));
  decodBufer decodbufer_237 (.in_1(demultiplexer_19_out5), .out_2(out_32));
  decodBufer decodbufer_238 (.in_1(demultiplexer_19_out6), .out_2(out_33));
  decodBufer decodbufer_239 (.in_1(demultiplexer_19_out7), .out_2(out_34));
  decodBufer decodbufer_240 (.in_1(demultiplexer_19_out8), .out_2(out_35));
  decodBufer decodbufer_241 (.in_1(demultiplexer_19_out9), .out_2(out_36));
  decodBufer decodbufer_242 (.in_1(demultiplexer_19_out10), .out_2(out_37));
  decodBufer decodbufer_243 (.in_1(demultiplexer_19_out11), .out_2(out_38));
  decodBufer decodbufer_244 (.in_1(demultiplexer_19_out12), .out_2(out_39));
  decodBufer decodbufer_245 (.in_1(demultiplexer_19_out13), .out_2(out_40));
  decodBufer decodbufer_246 (.in_1(demultiplexer_19_out14), .out_2(out_41));
  decodBufer decodbufer_247 (.in_1(demultiplexer_19_out15), .out_2(out_42));
  decodBufer decodbufer_248 (.in_1(demultiplexer_19_out16), .out_2(out_43));
  decodBufer decodbufer_249 (.in_1(demultiplexer_19_out17), .out_2(out_44));
  decodBufer decodbufer_250 (.in_1(demultiplexer_19_out18), .out_2(out_45));
  decodBufer decodbufer_251 (.in_1(demultiplexer_19_out19), .out_2(out_46));
  decodBufer decodbufer_252 (.in_1(demultiplexer_19_out20), .out_2(out_47));
  decodBufer decodbufer_253 (.in_1(demultiplexer_19_out21), .out_2(out_48));
  decodBufer decodbufer_254 (.in_1(demultiplexer_19_out22), .out_2(out_49));
  decodBufer decodbufer_255 (.in_1(demultiplexer_19_out23), .out_2(out_50));
  decodBufer decodbufer_256 (.in_1(demultiplexer_20_out7), .out_2(out_34));
  decodBufer decodbufer_257 (.in_1(demultiplexer_20_out8), .out_2(out_35));
  decodBufer decodbufer_258 (.in_1(demultiplexer_20_out9), .out_2(out_36));
  decodBufer decodbufer_259 (.in_1(demultiplexer_20_out10), .out_2(out_37));
  decodBufer decodbufer_260 (.in_1(demultiplexer_20_out11), .out_2(out_38));
  decodBufer decodbufer_261 (.in_1(demultiplexer_20_out12), .out_2(out_39));
  decodBufer decodbufer_262 (.in_1(demultiplexer_20_out13), .out_2(out_40));
  decodBufer decodbufer_263 (.in_1(demultiplexer_20_out14), .out_2(out_41));
  decodBufer decodbufer_264 (.in_1(demultiplexer_20_out15), .out_2(out_42));
  decodBufer decodbufer_265 (.in_1(demultiplexer_20_out16), .out_2(out_43));
  decodBufer decodbufer_266 (.in_1(demultiplexer_20_out17), .out_2(out_44));
  decodBufer decodbufer_267 (.in_1(demultiplexer_20_out18), .out_2(out_45));
  decodBufer decodbufer_268 (.in_1(demultiplexer_20_out19), .out_2(out_46));
  decodBufer decodbufer_269 (.in_1(demultiplexer_20_out20), .out_2(out_47));
  decodBufer decodbufer_270 (.in_1(demultiplexer_20_out21), .out_2(out_48));
  decodBufer decodbufer_271 (.in_1(demultiplexer_20_out22), .out_2(out_49));
  decodBufer decodbufer_272 (.in_1(demultiplexer_20_out23), .out_2(out_50));
  decodBufer decodbufer_273 (.in_1(demultiplexer_21_out11), .out_2(out_38));
  decodBufer decodbufer_274 (.in_1(demultiplexer_21_out12), .out_2(out_39));
  decodBufer decodbufer_275 (.in_1(demultiplexer_21_out13), .out_2(out_40));
  decodBufer decodbufer_276 (.in_1(demultiplexer_21_out14), .out_2(out_41));
  decodBufer decodbufer_277 (.in_1(demultiplexer_21_out15), .out_2(out_42));
  decodBufer decodbufer_278 (.in_1(demultiplexer_21_out16), .out_2(out_43));
  decodBufer decodbufer_279 (.in_1(demultiplexer_21_out17), .out_2(out_44));
  decodBufer decodbufer_280 (.in_1(demultiplexer_21_out18), .out_2(out_45));
  decodBufer decodbufer_281 (.in_1(demultiplexer_21_out19), .out_2(out_46));
  decodBufer decodbufer_282 (.in_1(demultiplexer_21_out20), .out_2(out_47));
  decodBufer decodbufer_283 (.in_1(demultiplexer_21_out21), .out_2(out_48));
  decodBufer decodbufer_284 (.in_1(demultiplexer_21_out22), .out_2(out_49));
  decodBufer decodbufer_285 (.in_1(demultiplexer_21_out23), .out_2(out_50));
  decodBufer decodbufer_286 (.in_1(demultiplexer_22_out15), .out_2(out_42));
  decodBufer decodbufer_287 (.in_1(demultiplexer_22_out16), .out_2(out_43));
  decodBufer decodbufer_288 (.in_1(demultiplexer_22_out17), .out_2(out_44));
  decodBufer decodbufer_289 (.in_1(demultiplexer_22_out18), .out_2(out_45));
  decodBufer decodbufer_290 (.in_1(demultiplexer_22_out19), .out_2(out_46));
  decodBufer decodbufer_291 (.in_1(demultiplexer_22_out20), .out_2(out_47));
  decodBufer decodbufer_292 (.in_1(demultiplexer_22_out21), .out_2(out_48));
  decodBufer decodbufer_293 (.in_1(demultiplexer_22_out22), .out_2(out_49));
  decodBufer decodbufer_294 (.in_1(demultiplexer_22_out23), .out_2(out_50));
  decodBufer decodbufer_295 (.in_1(demultiplexer_23_out19), .out_2(out_46));
  decodBufer decodbufer_296 (.in_1(demultiplexer_23_out20), .out_2(out_47));
  decodBufer decodbufer_297 (.in_1(demultiplexer_23_out21), .out_2(out_48));
  decodBufer decodbufer_298 (.in_1(demultiplexer_23_out22), .out_2(out_49));
  decodBufer decodbufer_299 (.in_1(demultiplexer_23_out23), .out_2(out_50));
  decodBufer decodbufer_300 (.in_1(demultiplexer_24_out22), .out_2(out_50));

  // Other names for the same wires on the sheet: _0[31:0] = \Вход_0 ; _0_prime[31:0] = \Выход_0 ; _1[31:0] = in_2;
  //   _1_prime[31:0] = out_28; _2[31:0] = in_4; _2_prime[31:0] = out_29; _3[31:0] = in_6; _3_prime[31:0] = out_30;
  //   _4[31:0] = in_7; _4_prime[31:0] = out_31; _5[31:0] = in_8; _5_prime[31:0] = out_32; _6[31:0] = in_9;
  //   _6_prime[31:0] = out_33; _7[31:0] = in_10; _7_prime[31:0] = out_34; _8[31:0] = in_11; _8_prime[31:0] = out_35;
  //   _9[31:0] = in_12; _9_prime[31:0] = out_36; _10[31:0] = in_13; _10_prime[31:0] = out_37; _11[31:0] = in_14;
  //   _11_prime[31:0] = out_38; _12[31:0] = in_15; _12_prime[31:0] = out_39; _13[31:0] = in_16;
  //   _13_prime[31:0] = out_40; _14[31:0] = in_17; _14_prime[31:0] = out_41; _15[31:0] = in_18;
  //   _15_prime[31:0] = out_42; _16[31:0] = in_19; _16_prime[31:0] = out_43; _17[31:0] = in_20;
  //   _17_prime[31:0] = out_44; _18[31:0] = in_21; _18_prime[31:0] = out_45; _19[31:0] = in_22;
  //   _19_prime[31:0] = out_46; _20[31:0] = in_23; _20_prime[31:0] = out_47; _21[31:0] = in_24;
  //   _21_prime[31:0] = out_48; _22[31:0] = in_25; _22_prime[31:0] = out_49; _23[31:0] = in_26;
  //   _23_prime[31:0] = out_50
endmodule

module decodBufer (
  input  [31:0] in_1,
  output [31:0] out_2
);

  wire oradd32_1_out;

  oradd32 oradd32_1 (.in(in_1), .out(oradd32_1_out));
  assign out_2 = oradd32_1_out ? in_1 : 32'bz;  // Controlled_Buffer controlled_buffer_1

  // Notes on the sheet:
  //   out_2: pull=down
endmodule

module ShifterLeft (
  input  [31:0] \Вход_0 ,
  input  [31:0] in_2,
  input  [31:0] in_3,
  input  [31:0] in_4,
  input  [31:0] in_5,
  input  [31:0] in_6,
  input  [31:0] in_7,
  input  [31:0] in_8,
  input  [31:0] in_9,
  input  [31:0] in_10,
  input  [31:0] in_11,
  input  [31:0] in_12,
  input  [31:0] in_13,
  input  [31:0] in_14,
  input  [31:0] in_15,
  input  [31:0] in_16,
  input  [31:0] in_17,
  input  [31:0] in_18,
  input  [31:0] in_19,
  input  [31:0] in_20,
  input  [31:0] in_21,
  input  [31:0] in_22,
  input  [31:0] in_23,
  input  [31:0] in_24,
  input  in_25,
  output [31:0] out_26,
  output [31:0] out_27,
  output [31:0] out_28,
  output [31:0] out_29,
  output [31:0] out_30,
  output [31:0] out_31,
  output [31:0] out_32,
  output [31:0] out_33,
  output [31:0] out_34,
  output [31:0] out_35,
  output [31:0] out_36,
  output [31:0] out_37,
  output [31:0] out_38,
  output [31:0] out_39,
  output [31:0] out_40,
  output [31:0] out_41,
  output [31:0] out_42,
  output [31:0] out_43,
  output [31:0] out_44,
  output [31:0] out_45,
  output [31:0] out_46,
  output [31:0] out_47,
  output [31:0] out_48,
  output [31:0] out_49
);

  wire [4:4] pull_resistor_1_node;
  wire [31:0] pull_resistor_2_node, pull_resistor_3_node, pull_resistor_7_node, pull_resistor_9_node,
       pull_resistor_10_node, pull_resistor_12_node, pull_resistor_13_node, pull_resistor_14_node,
       pull_resistor_15_node, pull_resistor_17_node, pull_resistor_18_node, pull_resistor_20_node,
       pull_resistor_22_node, pull_resistor_23_node, pull_resistor_24_node, shifter_3_out, shifter_4_out,
       shifter_5_out, shifter_7_out, shifter_10_out, shifter_15_out, shifter_18_out, shifter_20_out,
       shifter_24_out;

  Pull_Resistor pull_resistor_1 (.node(pull_resistor_1_node[4]));
  Pull_Resistor pull_resistor_2 (.node(pull_resistor_2_node));
  Shifter #(.width(32)) shifter_1 (
    .in(\Вход_0 ), .\dist ({{4{pull_resistor_1_node[4]}}, in_25}), .out(pull_resistor_2_node));
  Pull_Resistor pull_resistor_3 (.node(pull_resistor_3_node));
  Shifter #(.width(32)) shifter_2 (
    .in(in_2), .\dist ({{4{pull_resistor_1_node[4]}}, in_25}), .out(pull_resistor_3_node));
  Shifter #(.width(32)) shifter_3 (.in(in_3), .\dist ({{4{pull_resistor_1_node[4]}}, in_25}), .out(shifter_3_out));
  Pull_Resistor pull_resistor_4 (.node(shifter_3_out));
  Shifter #(.width(32)) shifter_4 (.in(in_4), .\dist ({{4{pull_resistor_1_node[4]}}, in_25}), .out(shifter_4_out));
  Pull_Resistor pull_resistor_5 (.node(shifter_4_out));
  Shifter #(.width(32)) shifter_5 (.in(in_5), .\dist ({{4{pull_resistor_1_node[4]}}, in_25}), .out(shifter_5_out));
  Pull_Resistor pull_resistor_6 (.node(shifter_5_out));
  Pull_Resistor pull_resistor_7 (.node(pull_resistor_7_node));
  Shifter #(.width(32)) shifter_6 (
    .in(in_6), .\dist ({{4{pull_resistor_1_node[4]}}, in_25}), .out(pull_resistor_7_node));
  Shifter #(.width(32)) shifter_7 (.in(in_7), .\dist ({{4{pull_resistor_1_node[4]}}, in_25}), .out(shifter_7_out));
  Pull_Resistor pull_resistor_8 (.node(shifter_7_out));
  Pull_Resistor pull_resistor_9 (.node(pull_resistor_9_node));
  Shifter #(.width(32)) shifter_8 (
    .in(in_8), .\dist ({{4{pull_resistor_1_node[4]}}, in_25}), .out(pull_resistor_9_node));
  Pull_Resistor pull_resistor_10 (.node(pull_resistor_10_node));
  Shifter #(.width(32)) shifter_9 (
    .in(in_9), .\dist ({{4{pull_resistor_1_node[4]}}, in_25}), .out(pull_resistor_10_node));
  Shifter #(.width(32)) shifter_10 (.in(in_10), .\dist ({{4{pull_resistor_1_node[4]}}, in_25}), .out(shifter_10_out));
  Pull_Resistor pull_resistor_11 (.node(shifter_10_out));
  Pull_Resistor pull_resistor_12 (.node(pull_resistor_12_node));
  Shifter #(.width(32)) shifter_11 (
    .in(in_11), .\dist ({{4{pull_resistor_1_node[4]}}, in_25}), .out(pull_resistor_12_node));
  Pull_Resistor pull_resistor_13 (.node(pull_resistor_13_node));
  Shifter #(.width(32)) shifter_12 (
    .in(in_12), .\dist ({{4{pull_resistor_1_node[4]}}, in_25}), .out(pull_resistor_13_node));
  Pull_Resistor pull_resistor_14 (.node(pull_resistor_14_node));
  Shifter #(.width(32)) shifter_13 (
    .in(in_13), .\dist ({{4{pull_resistor_1_node[4]}}, in_25}), .out(pull_resistor_14_node));
  Pull_Resistor pull_resistor_15 (.node(pull_resistor_15_node));
  Shifter #(.width(32)) shifter_14 (
    .in(in_14), .\dist ({{4{pull_resistor_1_node[4]}}, in_25}), .out(pull_resistor_15_node));
  Shifter #(.width(32)) shifter_15 (.in(in_15), .\dist ({{4{pull_resistor_1_node[4]}}, in_25}), .out(shifter_15_out));
  Pull_Resistor pull_resistor_16 (.node(shifter_15_out));
  Pull_Resistor pull_resistor_17 (.node(pull_resistor_17_node));
  Shifter #(.width(32)) shifter_16 (
    .in(in_16), .\dist ({{4{pull_resistor_1_node[4]}}, in_25}), .out(pull_resistor_17_node));
  Pull_Resistor pull_resistor_18 (.node(pull_resistor_18_node));
  Shifter #(.width(32)) shifter_17 (
    .in(in_17), .\dist ({{4{pull_resistor_1_node[4]}}, in_25}), .out(pull_resistor_18_node));
  Shifter #(.width(32)) shifter_18 (.in(in_18), .\dist ({{4{pull_resistor_1_node[4]}}, in_25}), .out(shifter_18_out));
  Pull_Resistor pull_resistor_19 (.node(shifter_18_out));
  Pull_Resistor pull_resistor_20 (.node(pull_resistor_20_node));
  Shifter #(.width(32)) shifter_19 (
    .in(in_19), .\dist ({{4{pull_resistor_1_node[4]}}, in_25}), .out(pull_resistor_20_node));
  Shifter #(.width(32)) shifter_20 (.in(in_20), .\dist ({{4{pull_resistor_1_node[4]}}, in_25}), .out(shifter_20_out));
  Pull_Resistor pull_resistor_21 (.node(shifter_20_out));
  Pull_Resistor pull_resistor_22 (.node(pull_resistor_22_node));
  Shifter #(.width(32)) shifter_21 (
    .in(in_21), .\dist ({{4{pull_resistor_1_node[4]}}, in_25}), .out(pull_resistor_22_node));
  Pull_Resistor pull_resistor_23 (.node(pull_resistor_23_node));
  Shifter #(.width(32)) shifter_22 (
    .in(in_22), .\dist ({{4{pull_resistor_1_node[4]}}, in_25}), .out(pull_resistor_23_node));
  Pull_Resistor pull_resistor_24 (.node(pull_resistor_24_node));
  Shifter #(.width(32)) shifter_23 (
    .in(in_23), .\dist ({{4{pull_resistor_1_node[4]}}, in_25}), .out(pull_resistor_24_node));
  Shifter #(.width(32)) shifter_24 (.in(in_24), .\dist ({{4{pull_resistor_1_node[4]}}, in_25}), .out(shifter_24_out));
  Pull_Resistor pull_resistor_25 (.node(shifter_24_out));
  assign out_26 = in_25 ? pull_resistor_2_node : 32'bz;  // Controlled_Buffer controlled_buffer_1
  assign out_27 = in_25 ? pull_resistor_3_node : 32'bz;  // Controlled_Buffer controlled_buffer_2
  assign out_28 = in_25 ? shifter_3_out : 32'bz;  // Controlled_Buffer controlled_buffer_3
  assign out_29 = in_25 ? shifter_4_out : 32'bz;  // Controlled_Buffer controlled_buffer_4
  assign out_30 = in_25 ? shifter_5_out : 32'bz;  // Controlled_Buffer controlled_buffer_5
  assign out_31 = in_25 ? pull_resistor_7_node : 32'bz;  // Controlled_Buffer controlled_buffer_6
  assign out_32 = in_25 ? shifter_7_out : 32'bz;  // Controlled_Buffer controlled_buffer_7
  assign out_33 = in_25 ? pull_resistor_9_node : 32'bz;  // Controlled_Buffer controlled_buffer_8
  assign out_34 = in_25 ? pull_resistor_10_node : 32'bz;  // Controlled_Buffer controlled_buffer_9
  assign out_35 = in_25 ? shifter_10_out : 32'bz;  // Controlled_Buffer controlled_buffer_10
  assign out_36 = in_25 ? pull_resistor_12_node : 32'bz;  // Controlled_Buffer controlled_buffer_11
  assign out_37 = in_25 ? pull_resistor_13_node : 32'bz;  // Controlled_Buffer controlled_buffer_12
  assign out_38 = in_25 ? pull_resistor_14_node : 32'bz;  // Controlled_Buffer controlled_buffer_13
  assign out_39 = in_25 ? pull_resistor_15_node : 32'bz;  // Controlled_Buffer controlled_buffer_14
  assign out_40 = in_25 ? shifter_15_out : 32'bz;  // Controlled_Buffer controlled_buffer_15
  assign out_41 = in_25 ? pull_resistor_17_node : 32'bz;  // Controlled_Buffer controlled_buffer_16
  assign out_42 = in_25 ? pull_resistor_18_node : 32'bz;  // Controlled_Buffer controlled_buffer_17
  assign out_43 = in_25 ? shifter_18_out : 32'bz;  // Controlled_Buffer controlled_buffer_18
  assign out_44 = in_25 ? pull_resistor_20_node : 32'bz;  // Controlled_Buffer controlled_buffer_19
  assign out_45 = in_25 ? shifter_20_out : 32'bz;  // Controlled_Buffer controlled_buffer_20
  assign out_46 = in_25 ? pull_resistor_22_node : 32'bz;  // Controlled_Buffer controlled_buffer_21
  assign out_47 = in_25 ? pull_resistor_23_node : 32'bz;  // Controlled_Buffer controlled_buffer_22
  assign out_48 = in_25 ? pull_resistor_24_node : 32'bz;  // Controlled_Buffer controlled_buffer_23
  assign out_49 = in_25 ? shifter_24_out : 32'bz;  // Controlled_Buffer controlled_buffer_24

  // Other names for the same wires on the sheet: On = in_25
endmodule

module ShifterRight (
  input  [31:0] \Вход_0 ,
  input  [31:0] in_2,
  input  [31:0] in_3,
  input  [31:0] in_4,
  input  [31:0] in_5,
  input  [31:0] in_6,
  input  [31:0] in_7,
  input  [31:0] in_8,
  input  [31:0] in_9,
  input  [31:0] in_10,
  input  [31:0] in_11,
  input  [31:0] in_12,
  input  [31:0] in_13,
  input  [31:0] in_14,
  input  [31:0] in_15,
  input  [31:0] in_16,
  input  [31:0] in_17,
  input  [31:0] in_18,
  input  [31:0] in_19,
  input  [31:0] in_20,
  input  [31:0] in_21,
  input  [31:0] in_22,
  input  [31:0] in_23,
  input  [31:0] in_24,
  input  in_25,
  output [31:0] out_26,
  output [31:0] out_27,
  output [31:0] out_28,
  output [31:0] out_29,
  output [31:0] out_30,
  output [31:0] out_31,
  output [31:0] out_32,
  output [31:0] out_33,
  output [31:0] out_34,
  output [31:0] out_35,
  output [31:0] out_36,
  output [31:0] out_37,
  output [31:0] out_38,
  output [31:0] out_39,
  output [31:0] out_40,
  output [31:0] out_41,
  output [31:0] out_42,
  output [31:0] out_43,
  output [31:0] out_44,
  output [31:0] out_45,
  output [31:0] out_46,
  output [31:0] out_47,
  output [31:0] out_48,
  output [31:0] out_49
);

  wire [4:4] pull_resistor_1_node;
  wire [31:0] pull_resistor_5_node, pull_resistor_8_node, pull_resistor_10_node, pull_resistor_12_node,
       pull_resistor_13_node, pull_resistor_15_node, pull_resistor_16_node, pull_resistor_18_node,
       pull_resistor_22_node, pull_resistor_23_node, pull_resistor_24_node, shifter_1_out, shifter_2_out,
       shifter_3_out, shifter_5_out, shifter_6_out, shifter_8_out, shifter_10_out, shifter_13_out,
       shifter_16_out, shifter_18_out, shifter_19_out, shifter_20_out, shifter_24_out;

  Pull_Resistor pull_resistor_1 (.node(pull_resistor_1_node[4]));
  Shifter #(.width(32), .shift("lr")) shifter_1 (
    .in(\Вход_0 ), .\dist ({{4{pull_resistor_1_node[4]}}, in_25}), .out(shifter_1_out));
  Pull_Resistor pull_resistor_2 (.node(shifter_1_out));
  Shifter #(.width(32), .shift("lr")) shifter_2 (
    .in(in_2), .\dist ({{4{pull_resistor_1_node[4]}}, in_25}), .out(shifter_2_out));
  Pull_Resistor pull_resistor_3 (.node(shifter_2_out));
  Shifter #(.width(32), .shift("lr")) shifter_3 (
    .in(in_3), .\dist ({{4{pull_resistor_1_node[4]}}, in_25}), .out(shifter_3_out));
  Pull_Resistor pull_resistor_4 (.node(shifter_3_out));
  Pull_Resistor pull_resistor_5 (.node(pull_resistor_5_node));
  Shifter #(.width(32), .shift("lr")) shifter_4 (
    .in(in_4), .\dist ({{4{pull_resistor_1_node[4]}}, in_25}), .out(pull_resistor_5_node));
  Shifter #(.width(32), .shift("lr")) shifter_5 (
    .in(in_5), .\dist ({{4{pull_resistor_1_node[4]}}, in_25}), .out(shifter_5_out));
  Pull_Resistor pull_resistor_6 (.node(shifter_5_out));
  Shifter #(.width(32), .shift("lr")) shifter_6 (
    .in(in_6), .\dist ({{4{pull_resistor_1_node[4]}}, in_25}), .out(shifter_6_out));
  Pull_Resistor pull_resistor_7 (.node(shifter_6_out));
  Pull_Resistor pull_resistor_8 (.node(pull_resistor_8_node));
  Shifter #(.width(32), .shift("lr")) shifter_7 (
    .in(in_7), .\dist ({{4{pull_resistor_1_node[4]}}, in_25}), .out(pull_resistor_8_node));
  Shifter #(.width(32), .shift("lr")) shifter_8 (
    .in(in_8), .\dist ({{4{pull_resistor_1_node[4]}}, in_25}), .out(shifter_8_out));
  Pull_Resistor pull_resistor_9 (.node(shifter_8_out));
  Pull_Resistor pull_resistor_10 (.node(pull_resistor_10_node));
  Shifter #(.width(32), .shift("lr")) shifter_9 (
    .in(in_9), .\dist ({{4{pull_resistor_1_node[4]}}, in_25}), .out(pull_resistor_10_node));
  Shifter #(.width(32), .shift("lr")) shifter_10 (
    .in(in_10), .\dist ({{4{pull_resistor_1_node[4]}}, in_25}), .out(shifter_10_out));
  Pull_Resistor pull_resistor_11 (.node(shifter_10_out));
  Pull_Resistor pull_resistor_12 (.node(pull_resistor_12_node));
  Shifter #(.width(32), .shift("lr")) shifter_11 (
    .in(in_11), .\dist ({{4{pull_resistor_1_node[4]}}, in_25}), .out(pull_resistor_12_node));
  Pull_Resistor pull_resistor_13 (.node(pull_resistor_13_node));
  Shifter #(.width(32), .shift("lr")) shifter_12 (
    .in(in_12), .\dist ({{4{pull_resistor_1_node[4]}}, in_25}), .out(pull_resistor_13_node));
  Shifter #(.width(32), .shift("lr")) shifter_13 (
    .in(in_13), .\dist ({{4{pull_resistor_1_node[4]}}, in_25}), .out(shifter_13_out));
  Pull_Resistor pull_resistor_14 (.node(shifter_13_out));
  Pull_Resistor pull_resistor_15 (.node(pull_resistor_15_node));
  Shifter #(.width(32), .shift("lr")) shifter_14 (
    .in(in_14), .\dist ({{4{pull_resistor_1_node[4]}}, in_25}), .out(pull_resistor_15_node));
  Pull_Resistor pull_resistor_16 (.node(pull_resistor_16_node));
  Shifter #(.width(32), .shift("lr")) shifter_15 (
    .in(in_15), .\dist ({{4{pull_resistor_1_node[4]}}, in_25}), .out(pull_resistor_16_node));
  Shifter #(.width(32), .shift("lr")) shifter_16 (
    .in(in_16), .\dist ({{4{pull_resistor_1_node[4]}}, in_25}), .out(shifter_16_out));
  Pull_Resistor pull_resistor_17 (.node(shifter_16_out));
  Pull_Resistor pull_resistor_18 (.node(pull_resistor_18_node));
  Shifter #(.width(32), .shift("lr")) shifter_17 (
    .in(in_17), .\dist ({{4{pull_resistor_1_node[4]}}, in_25}), .out(pull_resistor_18_node));
  Shifter #(.width(32), .shift("lr")) shifter_18 (
    .in(in_18), .\dist ({{4{pull_resistor_1_node[4]}}, in_25}), .out(shifter_18_out));
  Pull_Resistor pull_resistor_19 (.node(shifter_18_out));
  Shifter #(.width(32), .shift("lr")) shifter_19 (
    .in(in_19), .\dist ({{4{pull_resistor_1_node[4]}}, in_25}), .out(shifter_19_out));
  Pull_Resistor pull_resistor_20 (.node(shifter_19_out));
  Shifter #(.width(32), .shift("lr")) shifter_20 (
    .in(in_20), .\dist ({{4{pull_resistor_1_node[4]}}, in_25}), .out(shifter_20_out));
  Pull_Resistor pull_resistor_21 (.node(shifter_20_out));
  Pull_Resistor pull_resistor_22 (.node(pull_resistor_22_node));
  Shifter #(.width(32), .shift("lr")) shifter_21 (
    .in(in_21), .\dist ({{4{pull_resistor_1_node[4]}}, in_25}), .out(pull_resistor_22_node));
  Pull_Resistor pull_resistor_23 (.node(pull_resistor_23_node));
  Shifter #(.width(32), .shift("lr")) shifter_22 (
    .in(in_22), .\dist ({{4{pull_resistor_1_node[4]}}, in_25}), .out(pull_resistor_23_node));
  Pull_Resistor pull_resistor_24 (.node(pull_resistor_24_node));
  Shifter #(.width(32), .shift("lr")) shifter_23 (
    .in(in_23), .\dist ({{4{pull_resistor_1_node[4]}}, in_25}), .out(pull_resistor_24_node));
  Shifter #(.width(32), .shift("lr")) shifter_24 (
    .in(in_24), .\dist ({{4{pull_resistor_1_node[4]}}, in_25}), .out(shifter_24_out));
  Pull_Resistor pull_resistor_25 (.node(shifter_24_out));
  assign out_26 = in_25 ? shifter_1_out : 32'bz;  // Controlled_Buffer controlled_buffer_1
  assign out_27 = in_25 ? shifter_2_out : 32'bz;  // Controlled_Buffer controlled_buffer_2
  assign out_28 = in_25 ? shifter_3_out : 32'bz;  // Controlled_Buffer controlled_buffer_3
  assign out_29 = in_25 ? pull_resistor_5_node : 32'bz;  // Controlled_Buffer controlled_buffer_4
  assign out_30 = in_25 ? shifter_5_out : 32'bz;  // Controlled_Buffer controlled_buffer_5
  assign out_31 = in_25 ? shifter_6_out : 32'bz;  // Controlled_Buffer controlled_buffer_6
  assign out_32 = in_25 ? pull_resistor_8_node : 32'bz;  // Controlled_Buffer controlled_buffer_7
  assign out_33 = in_25 ? shifter_8_out : 32'bz;  // Controlled_Buffer controlled_buffer_8
  assign out_34 = in_25 ? pull_resistor_10_node : 32'bz;  // Controlled_Buffer controlled_buffer_9
  assign out_35 = in_25 ? shifter_10_out : 32'bz;  // Controlled_Buffer controlled_buffer_10
  assign out_36 = in_25 ? pull_resistor_12_node : 32'bz;  // Controlled_Buffer controlled_buffer_11
  assign out_37 = in_25 ? pull_resistor_13_node : 32'bz;  // Controlled_Buffer controlled_buffer_12
  assign out_38 = in_25 ? shifter_13_out : 32'bz;  // Controlled_Buffer controlled_buffer_13
  assign out_39 = in_25 ? pull_resistor_15_node : 32'bz;  // Controlled_Buffer controlled_buffer_14
  assign out_40 = in_25 ? pull_resistor_16_node : 32'bz;  // Controlled_Buffer controlled_buffer_15
  assign out_41 = in_25 ? shifter_16_out : 32'bz;  // Controlled_Buffer controlled_buffer_16
  assign out_42 = in_25 ? pull_resistor_18_node : 32'bz;  // Controlled_Buffer controlled_buffer_17
  assign out_43 = in_25 ? shifter_18_out : 32'bz;  // Controlled_Buffer controlled_buffer_18
  assign out_44 = in_25 ? shifter_19_out : 32'bz;  // Controlled_Buffer controlled_buffer_19
  assign out_45 = in_25 ? shifter_20_out : 32'bz;  // Controlled_Buffer controlled_buffer_20
  assign out_46 = in_25 ? pull_resistor_22_node : 32'bz;  // Controlled_Buffer controlled_buffer_21
  assign out_47 = in_25 ? pull_resistor_23_node : 32'bz;  // Controlled_Buffer controlled_buffer_22
  assign out_48 = in_25 ? pull_resistor_24_node : 32'bz;  // Controlled_Buffer controlled_buffer_23
  assign out_49 = in_25 ? shifter_24_out : 32'bz;  // Controlled_Buffer controlled_buffer_24

  // Other names for the same wires on the sheet: On = in_25
endmodule
